// Digital circuit ALU.dig as structural Verilog
module ALU (
  input  A5,
  input  B6,
  input  A6,
  input  B7,
  input  A7,
  input  B8,
  input  A8,
  input  B9,
  input  Sel3,
  input  Sel2,
  input  Cin,
  input  [1:0] Sel,
  input  Cin_2,
  input  [15:0] A,
  input  [3:0] B,
  output V5,
  output Cout,
  output V6,
  output V7,
  output V8,
  output Cout_2,
  output Z,
  output N
);

  wire add_1_c_o, add_1_s, add_2_c_o, add_2_s, add_3_c_o, add_3_s, add_4_s, and_1_out, and_2_out, and_3_out,
       and_4_out, and_5_out, and_6_out, and_7_out, and_8_out, and_9_out, and_10_out, and_11_out, and_12_out,
       decoder_1_out_1, decoder_2_out_1, multiplexer_1_out, multiplexer_2_out, multiplexer_3_out,
       multiplexer_4_out, multiplexer_5_out, multiplexer_6_out, multiplexer_7_out, multiplexer_8_out,
       multiplexer_9_out, multiplexer_10_out, multiplexer_11_out, multiplexer_12_out, not_1_out, not_2_out,
       not_3_out, not_4_out, not_5_out, not_6_out, not_7_out, not_8_out, or_1_out, or_2_out, or_3_out,
       or_4_out, or_5_out, or_6_out, or_8_out, or_9_out, or_10_out, or_11_out, or_12_out, or_13_out,
       or_14_out, xor_1_out, xor_2_out, xor_3_out, xor_4_out, xor_5_out, xor_6_out, xor_7_out, xor_8_out;
  wire [1:0] decoder_1_out_2, decoder_2_out_2;

  Decoder #(.Selector_Bits(2)) decoder_1 (
    .sel(Sel), .out_1(decoder_1_out_1), .out_2(decoder_1_out_2[0]), .out_3(decoder_1_out_2[1]));  // open: out_0
  Multiplexer multiplexer_1 (.sel(decoder_1_out_1), .in_0(B[0]), .in_1(not_1_out), .out(multiplexer_1_out));
  not not_1 (not_1_out, B[0]);
  Multiplexer multiplexer_2 (.sel(decoder_1_out_1), .in_0(B[1]), .in_1(not_2_out), .out(multiplexer_2_out));
  not not_2 (not_2_out, B[1]);
  Multiplexer multiplexer_3 (.sel(decoder_1_out_1), .in_0(B[2]), .in_1(not_3_out), .out(multiplexer_3_out));
  not not_3 (not_3_out, B[2]);
  Multiplexer multiplexer_4 (.sel(decoder_1_out_1), .in_0(B[3]), .in_1(not_4_out), .out(multiplexer_4_out));
  not not_4 (not_4_out, B[3]);
  or or_1 (or_1_out, decoder_1_out_1, Cin_2);
  Add add_1 (.a(A[0]), .b(multiplexer_1_out), .c_i(or_1_out), .s(add_1_s), .c_o(add_1_c_o));
  and and_1 (and_1_out, A[0], multiplexer_1_out);
  or or_2 (or_2_out, A[0], multiplexer_1_out);
  Add add_2 (.a(A[1]), .b(multiplexer_2_out), .c_i(add_1_c_o), .s(add_2_s), .c_o(add_2_c_o));
  and and_2 (and_2_out, A[1], multiplexer_2_out);
  or or_3 (or_3_out, A[1], multiplexer_2_out);
  Add add_3 (.a(A[2]), .b(multiplexer_3_out), .c_i(add_2_c_o), .s(add_3_s), .c_o(add_3_c_o));
  and and_3 (and_3_out, A[2], multiplexer_3_out);
  or or_4 (or_4_out, A[2], multiplexer_3_out);
  Add add_4 (.a(A[3]), .b(multiplexer_4_out), .c_i(add_3_c_o), .s(add_4_s), .c_o(Cout_2));
  and and_4 (and_4_out, A[3], multiplexer_4_out);
  or or_5 (or_5_out, A[3], multiplexer_4_out);
  Multiplexer #(.Selector_Bits(2)) multiplexer_5 (
    .sel(decoder_1_out_2), .in_0(add_1_s), .in_1(and_1_out), .in_2(or_2_out), .in_3(or_2_out),
    .out(multiplexer_5_out));
  Multiplexer #(.Selector_Bits(2)) multiplexer_6 (
    .sel(decoder_1_out_2), .in_0(add_2_s), .in_1(and_2_out), .in_2(or_3_out), .in_3(or_3_out),
    .out(multiplexer_6_out));
  Multiplexer #(.Selector_Bits(2)) multiplexer_7 (
    .sel(decoder_1_out_2), .in_0(add_3_s), .in_1(and_3_out), .in_2(or_4_out), .in_3(or_4_out),
    .out(multiplexer_7_out));
  Multiplexer #(.Selector_Bits(2)) multiplexer_8 (
    .sel(decoder_1_out_2), .in_0(add_4_s), .in_1(and_4_out), .in_2(or_5_out), .in_3(or_5_out),
    .out(multiplexer_8_out));
  nor nor_1 (Z, multiplexer_5_out, multiplexer_6_out, multiplexer_7_out, multiplexer_8_out);
  not not_5 (not_5_out, B6);
  not not_6 (not_6_out, B7);
  not not_7 (not_7_out, B8);
  not not_8 (not_8_out, B9);
  Multiplexer multiplexer_9 (.sel(decoder_2_out_1), .in_0(B6), .in_1(not_5_out), .out(multiplexer_9_out));
  Multiplexer multiplexer_10 (.sel(decoder_2_out_1), .in_0(B7), .in_1(not_6_out), .out(multiplexer_10_out));
  Multiplexer multiplexer_11 (.sel(decoder_2_out_1), .in_0(B8), .in_1(not_7_out), .out(multiplexer_11_out));
  Multiplexer multiplexer_12 (.sel(decoder_2_out_1), .in_0(B9), .in_1(not_8_out), .out(multiplexer_12_out));
  Decoder #(.Selector_Bits(2)) decoder_2 (
    .sel({Sel3, Sel2}), .out_1(decoder_2_out_1), .out_2(decoder_2_out_2[0]), .out_3(decoder_2_out_2[1]));  // open: out_0
  xor xor_1 (xor_1_out, A5, multiplexer_9_out);
  xor xor_2 (xor_2_out, A6, multiplexer_10_out);
  xor xor_3 (xor_3_out, A7, multiplexer_11_out);
  xor xor_4 (xor_4_out, A8, multiplexer_12_out);
  or or_6 (or_6_out, Cin, decoder_2_out_1);
  and and_5 (and_5_out, or_9_out, xor_1_out);
  xor xor_5 (xor_5_out, or_9_out, xor_1_out);
  and and_6 (and_6_out, multiplexer_9_out, A5);
  and and_7 (and_7_out, or_11_out, xor_2_out);
  xor xor_6 (xor_6_out, or_11_out, xor_2_out);
  and and_8 (and_8_out, multiplexer_10_out, A6);
  and and_9 (and_9_out, or_13_out, xor_3_out);
  xor xor_7 (xor_7_out, or_13_out, xor_3_out);
  and and_10 (and_10_out, multiplexer_11_out, A7);
  and and_11 (and_11_out, or_6_out, xor_4_out);
  xor xor_8 (xor_8_out, or_6_out, xor_4_out);
  and and_12 (and_12_out, multiplexer_12_out, A8);
  or or_7 (Cout, and_5_out, and_6_out);
  or or_8 (or_8_out, xor_1_out, and_6_out);
  or or_9 (or_9_out, and_7_out, and_8_out);
  or or_10 (or_10_out, xor_2_out, and_8_out);
  or or_11 (or_11_out, and_9_out, and_10_out);
  or or_12 (or_12_out, xor_3_out, and_10_out);
  or or_13 (or_13_out, and_11_out, and_12_out);
  or or_14 (or_14_out, xor_4_out, and_12_out);
  Multiplexer #(.Selector_Bits(2)) multiplexer_13 (
    .sel(decoder_2_out_2), .in_0(xor_5_out), .in_1(and_6_out), .in_2(or_8_out), .in_3(or_8_out), .out(V5));
  Multiplexer #(.Selector_Bits(2)) multiplexer_14 (
    .sel(decoder_2_out_2), .in_0(xor_6_out), .in_1(and_8_out), .in_2(or_10_out), .in_3(or_10_out), .out(V6));
  Multiplexer #(.Selector_Bits(2)) multiplexer_15 (
    .sel(decoder_2_out_2), .in_0(xor_7_out), .in_1(and_10_out), .in_2(or_12_out), .in_3(or_12_out), .out(V7));
  Multiplexer #(.Selector_Bits(2)) multiplexer_16 (
    .sel(decoder_2_out_2), .in_0(xor_8_out), .in_1(and_12_out), .in_2(or_14_out), .in_3(or_14_out), .out(V8));
  // Pins of 4 and 16 bits meet at A

  assign N = Cout_2;
endmodule
