// Digital circuit ALU_Streamlined.dig as structural Verilog
module ALU_Streamlined (
  input  [15:0] A,
  input  [15:0] B,
  input  [2:0] Sel,
  input  C_in,
  output [15:0] Out,
  output C,
  output Z,
  output N,
  output V
);

  wire bitselector_1_out, bitselector_2_out, bitselector_3_out, C_out_Add, C_out_Sub;
  wire [15:0] add_1_s, and_1_out, div_1_q, mul_1_mul, mul_1_mul_2, or_1_out, sub_1_s, xor_1_out;

  Add #(.Bits(16)) add_1 (.a(A), .b(B), .c_i(C_in), .s(add_1_s), .c_o(C_out_Add));
  Sub #(.Bits(16)) sub_1 (.a(A), .b(B), .c_i(C_in), .s(sub_1_s), .c_o(C_out_Sub));
  Mul #(.Bits(16)) mul_1 (.a(A), .b(B), .mul({mul_1_mul_2, mul_1_mul}));
  Div #(.Bits(16)) div_1 (.a(A), .b(B), .q(div_1_q));  // open: r
  assign and_1_out = A & B;  // And and_1, 16 bits wide
  assign or_1_out = A | B;  // Or or_1, 16 bits wide
  assign xor_1_out = A ^ B;  // XOr xor_1, 16 bits wide
  Multiplexer #(.Selector_Bits(3), .Bits(16)) multiplexer_1 (
    .sel(Sel), .in_0(add_1_s), .in_1(sub_1_s), .in_2(mul_1_mul), .in_3(mul_1_mul_2), .in_4(div_1_q),
    .in_5(and_1_out), .in_6(or_1_out), .in_7(xor_1_out), .out(Out));
  BitSelector #(.Selector_Bits(8)) bitselector_1 (.in(A), .sel({8{1'b0}}), .out(bitselector_1_out));
  BitSelector #(.Selector_Bits(8)) bitselector_2 (.in(B), .sel({8{1'b0}}), .out(bitselector_2_out));
  BitSelector #(.Selector_Bits(8)) bitselector_3 (.in(Out), .sel({8{1'b0}}), .out(bitselector_3_out));
  Comparator #(.Bits(16), .Signed("true")) comparator_1 (.a(Out), .b({16{1'b0}}), .eq(Z), .lt(N));  // open: gt
  Multiplexer multiplexer_2 (.sel(Sel[0]), .in_0(C_out_Add), .in_1(C_out_Sub), .out(C));
  overflow_detector overflow_detector_1 (.A(bitselector_1_out), .B(bitselector_2_out), .O(bitselector_3_out), .V(V));
  // Pins of 8 and 16 bits meet at 16'h8000
endmodule
