// Digital circuit extended_adder.dig as structural Verilog
module extended_adder (
  input  Cin,
  input  A,
  input  B,
  input  [1:0] Opt,
  input  Sub,
  output Cout,
  output S
);

  wire add_1_s, and_1_out, multiplexer_1_out, not_1_out, or_1_out;

  not not_1 (not_1_out, B);
  Multiplexer multiplexer_1 (.sel(Sub), .in_0(B), .in_1(not_1_out), .out(multiplexer_1_out));
  Add add_1 (.a(A), .b(multiplexer_1_out), .c_i(Cin), .s(add_1_s), .c_o(Cout));
  and and_1 (and_1_out, A, multiplexer_1_out);
  or or_1 (or_1_out, A, multiplexer_1_out);
  Multiplexer #(.Selector_Bits(2)) multiplexer_2 (
    .sel(Opt), .in_0(add_1_s), .in_1(and_1_out), .in_2(or_1_out), .in_3(or_1_out), .out(S));
endmodule
