// Digital circuit overflow_detector.dig as structural Verilog
module overflow_detector (
  input  A,
  input  B,
  input  O,
  output V
);

  wire and_1_out, and_2_out, not_1_out, not_2_out, not_3_out;

  not not_1 (not_1_out, A);
  not not_2 (not_2_out, B);
  not not_3 (not_3_out, O);
  and and_1 (and_1_out, not_1_out, not_2_out, O);
  and and_2 (and_2_out, A, B, not_3_out);
  or or_1 (V, and_1_out, and_2_out);
endmodule
