// Digital circuit cpu.dig as structural Verilog
module cpu (
  input  CLK
);

  wire FL_EN, LDR, STR, WE;
  wire [1:0] ALUOP, DMUX;
  wire [2:0] RS1, RS2, WS;
  wire [3:0] alu_1_flag;
  wire [15:0] multiplexer_1_out, PC_q, plus_1_s, RAM_d1, RAM_d2, reg_file_1_out1, reg_file_1_out2, undriven;

  Register #(.Bits(16), .isProgramCounter("true")) PC (.D(plus_1_s), .C(CLK), .en(1'b1), .Q(PC_q));
  Add #(.Bits(16)) plus_1 (.a(16'h1), .b(PC_q), .c_i(1'b0), .s(plus_1_s));  // open: c_o
  RAMDualAccess #(.AddrBits(16), .Bits(16)) RAM (
    .str(STR), .C(CLK), .ld(LDR), .A1(reg_file_1_out1), .Din1(reg_file_1_out2), .A2(PC_q), .D1(RAM_d1),
    .D2(RAM_d2));
  Multiplexer #(.Selector_Bits(2), .Bits(16)) multiplexer_1 (
    .sel(DMUX), .in_0(undriven), .in_1(RAM_d1), .in_2({{8{1'b0}}, RAM_d2[7:0]}), .in_3({16{1'b0}}),
    .out(multiplexer_1_out));
  control_unit control_unit_1 (
    .INST(RAM_d2), .FL_Z(alu_1_flag[0]), .ALUOP(ALUOP), .RS1(RS1), .RS2(RS2), .WS(WS), .STR(STR), .WE(WE),
    .DMUX(DMUX), .LDR(LDR), .FL_EN(FL_EN));  // open: HE
  reg_file reg_file_1 (
    .RS1(RS1), .RS2(RS2), .WS(WS), .WE(WE), .IN(multiplexer_1_out), .clk(CLK),
    .FL_IN({{12{1'b0}}, alu_1_flag}), .FL_EN(FL_EN), .OUT1(reg_file_1_out1), .OUT2(reg_file_1_out2));
  alu alu_1 (.A(reg_file_1_out1), .B(reg_file_1_out2), .ALUOP(ALUOP), .FLAG(alu_1_flag));  // open: RESULT
endmodule
