// Digital circuit reg_file.dig as structural Verilog
module reg_file (
  input  [2:0] RS1,
  input  [2:0] RS2,
  input  [2:0] WS,
  input  WE,
  input  [15:0] IN,
  input  clk,
  input  [15:0] FL_IN,
  input  FL_EN,
  input  [15:0] PC_IN,
  input  HE,
  output [15:0] OUT1,
  output [15:0] OUT2,
  output [15:0] PC_S,
  output PC_WE,
  output [15:0] FL_OUT
);

  wire demultiplexer_1_out_0, demultiplexer_1_out_1, demultiplexer_1_out_2, demultiplexer_1_out_3,
       demultiplexer_1_out_4, demultiplexer_1_out_5, or_1_out;
  wire [15:0] high_mask_in_1_q, high_mask_in_2_q, high_mask_in_3_q, high_mask_in_4_q, high_mask_in_5_q,
       high_mask_in_6_q, multiplexer_1_out, R1_q, R2_q, R3_q, R4_q, RZ_q;

  Demultiplexer #(.Selector_Bits(3)) demultiplexer_1 (
    .sel(WS), .in(WE), .out_0(demultiplexer_1_out_0), .out_1(demultiplexer_1_out_1),
    .out_2(demultiplexer_1_out_2), .out_3(demultiplexer_1_out_3), .out_4(demultiplexer_1_out_4),
    .out_5(demultiplexer_1_out_5), .out_7(PC_WE));  // open: out_6
  or or_1 (or_1_out, demultiplexer_1_out_5, FL_EN);
  Multiplexer #(.Bits(16)) multiplexer_1 (.sel(PC_WE), .in_0(PC_IN), .in_1(IN), .out(multiplexer_1_out));
  high_mask_in high_mask_in_1 (.D_HIGH(IN), .D(R1_q), .EN(HE), .Q(high_mask_in_1_q));
  high_mask_in high_mask_in_2 (.D_HIGH(IN), .D(R2_q), .EN(HE), .Q(high_mask_in_2_q));
  high_mask_in high_mask_in_3 (.D_HIGH(IN), .D(R3_q), .EN(HE), .Q(high_mask_in_3_q));
  high_mask_in high_mask_in_4 (.D_HIGH(IN), .D(R4_q), .EN(HE), .Q(high_mask_in_4_q));
  high_mask_in high_mask_in_5 (.D_HIGH(FL_IN), .D(FL_OUT), .EN(HE), .Q(high_mask_in_5_q));
  high_mask_in high_mask_in_6 (.D_HIGH(multiplexer_1_out), .D(PC_IN), .EN(HE), .Q(high_mask_in_6_q));
  Register #(.Bits(16)) RZ (.D({16{1'b0}}), .C(clk), .en(demultiplexer_1_out_0), .Q(RZ_q));
  Register #(.Bits(16)) R1 (.D(high_mask_in_1_q), .C(clk), .en(demultiplexer_1_out_1), .Q(R1_q));
  Register #(.Bits(16)) R2 (.D(high_mask_in_2_q), .C(clk), .en(demultiplexer_1_out_2), .Q(R2_q));
  Register #(.Bits(16)) R3 (.D(high_mask_in_3_q), .C(clk), .en(demultiplexer_1_out_3), .Q(R3_q));
  Register #(.Bits(16)) R4 (.D(high_mask_in_4_q), .C(clk), .en(demultiplexer_1_out_4), .Q(R4_q));
  Register #(.Bits(16)) FL (.D(high_mask_in_5_q), .C(clk), .en(or_1_out), .Q(FL_OUT));
  Multiplexer #(.Bits(16)) multiplexer_2 (.sel(PC_WE), .in_0({16{1'b0}}), .in_1(high_mask_in_6_q), .out(PC_S));
  Multiplexer #(.Selector_Bits(3), .Bits(16)) multiplexer_3 (
    .sel(RS1), .in_0(RZ_q), .in_1(R1_q), .in_2(R2_q), .in_3(R3_q), .in_4(R4_q), .in_5(FL_OUT),
    .in_6({16{1'b0}}), .in_7(PC_IN), .out(OUT1));
  Multiplexer #(.Selector_Bits(3), .Bits(16)) multiplexer_4 (
    .sel(RS2), .in_0(RZ_q), .in_1(R1_q), .in_2(R2_q), .in_3(R3_q), .in_4(R4_q), .in_5(FL_OUT),
    .in_6({16{1'b0}}), .in_7(PC_IN), .out(OUT2));

  // Notes on the sheet:
  //   RS1: The index of the register which should output its value to OUT1.
  //   RS2: The index of the register which should output its value to OUT2.
  //   WS: The index of the register which should save the value on IN on the next clock cycle (if WE is high).
  //   WE: Whether the register selected by WS should save the value from IN on the next cycle.
  //   IN: The value to be saved into the register specified by WS if WE is high,
  //   OUT1: The value in the register specified by RS1.
  //   OUT2: The value in the register specified by RS2.
  //   FL_IN: The value to be saved into the register specified by WS if WE is high,
  //   FL_EN: Whether the register selected by WS should save the value from IN on the next cycle.
endmodule

/* Test case:
clk RS1 RS2 WS WE IN OUT1 OUT2 PC_IN PC_S
c 0 0 0 1 0x1234 0x0000 0x0000 0x0000 0x0000
c 1 1 1 1 0x1234 0x1234 0x1234 0x0000 0x0000
c 2 1 2 1 0xBEEF 0xBEEF 0x1234 0x0000 0x0000
c 3 2 3 1 0xDEAD 0xDEAD 0xBEEF 0x0000 0x0000
c 4 3 4 1 0xFFFF 0xFFFF 0xDEAD 0x0000 0x0000
c 4 3 4 0 0xABCD 0xFFFF 0xDEAD 0x0000 0x0000
c 4 3 3 0 0xABCD 0xFFFF 0xDEAD 0x0000 0x0000
c 2 1 2 0 0xABCD 0xBEEF 0x1234 0x0000 0x0000
c 2 1 1 0 0xABCD 0xBEEF 0x1234 0x0000 0x0000
c 2 1 3 1 0xBADE 0xBEEF 0x1234 0x0000 0x0000
c 1 3 3 1 0xBADE 0x1234 0xBADE 0x0000 0x0000
c 1 1 3 0 0x1234 0x1234 0x1234 0x0000 0x0000
c 3 4 1 1 0x0000 0xBADE 0xFFFF 0x0000 0x0000
c 1 1 3 0 0x1234 0x0000 0x0000 0x0000 0x0000
c 3 4 0 1 0xBADE 0xBADE 0xFFFF 0x0000 0x0000
c 0 0 3 1 0xBADE 0x0000 0x0000 0x0000 0x0000
c 0 0 4 1 0x0001 0x0000 0x0000 0x0000 0x0000
c 0 4 2 1 0x0001 0x0000 0x0001 0x0005 0x0000
*/
