// Digital circuit hazard_unit.dig as structural Verilog
module hazard_unit (
  input  RegWriteM,
  input  RegWriteW,
  input  [15:0] RA1E,
  input  [15:0] RA2E,
  input  [15:0] WA3M,
  input  [15:0] WA3W,
  input  [15:0] RA1D,
  input  [15:0] RA2D,
  input  [15:0] WA3E,
  input  MemToRegE,
  input  PCSrcD,
  input  PCSrcE,
  input  PCSrcM,
  input  PCSrcW,
  input  BranchTakenE,
  input  MemToRegM,
  input  ALUSrcE,
  output [1:0] ForwardBE,
  output [1:0] ForwardAE,
  output StallF,
  output StallD,
  output FlushD,
  output FlushE,
  output PCorLDRF
);

  wire and_1_out, comparator_1_lt, comparator_2_lt, Match1_EM_eq, Match1_EW_eq, Match1D_E_eq, Match2_EM_eq,
       Match2_EW_eq, Match2DE_eq, or_5_out, or_6_out, or_7_out, or_8_out;
  wire [1:0] data_hazard_forwarding_1_forwarde, data_hazard_forwarding_2_forwarde;

  or or_1 (StallD, MemToRegM, and_1_out);
  or or_2 (StallF, or_8_out, MemToRegM, and_1_out);
  or or_3 (FlushE, BranchTakenE, and_1_out);
  or or_4 (FlushD, PCSrcW, or_8_out, BranchTakenE);
  Multiplexer #(.Bits(2)) multiplexer_1 (
    .sel(or_6_out), .in_0(data_hazard_forwarding_1_forwarde), .in_1(2'b00), .out(ForwardAE));
  Multiplexer #(.Bits(2)) multiplexer_2 (
    .sel(or_5_out), .in_0(data_hazard_forwarding_2_forwarde), .in_1(2'b00), .out(ForwardBE));
  or or_5 (or_5_out, comparator_2_lt, ALUSrcE);
  and and_1 (and_1_out, or_7_out, MemToRegE);
  or or_6 (or_6_out, comparator_1_lt, ALUSrcE);
  data_hazard_forwarding data_hazard_forwarding_1 (
    .I_3(Match1_EW_eq), .I_2(Match1_EM_eq), .I_1(RegWriteM), .I_0(RegWriteW),
    .ForwardE(data_hazard_forwarding_1_forwarde));
  data_hazard_forwarding data_hazard_forwarding_2 (
    .I_3(Match2_EW_eq), .I_2(Match2_EM_eq), .I_1(RegWriteM), .I_0(RegWriteW),
    .ForwardE(data_hazard_forwarding_2_forwarde));
  or or_7 (or_7_out, Match1D_E_eq, Match2DE_eq);
  Comparator #(.Bits(16)) comparator_1 (.a(RA1E), .b({16{1'b0}}), .lt(comparator_1_lt));  // open: gt, eq
  Comparator #(.Bits(16)) comparator_2 (.a(RA2E), .b({16{1'b0}}), .lt(comparator_2_lt));  // open: gt, eq
  Comparator #(.Bits(16)) Match1_EM (.a(WA3M), .b(RA1E), .eq(Match1_EM_eq));  // open: gt, lt
  Comparator #(.Bits(16)) Match1_EW (.a(WA3W), .b(RA1E), .eq(Match1_EW_eq));  // open: gt, lt
  Comparator #(.Bits(16)) Match2_EM (.a(WA3M), .b(RA2E), .eq(Match2_EM_eq));  // open: gt, lt
  Comparator #(.Bits(16)) Match2_EW (.a(WA3W), .b(RA2E), .eq(Match2_EW_eq));  // open: gt, lt
  Comparator #(.Bits(16)) Match2DE (.a(RA2D), .b(WA3E), .eq(Match2DE_eq));  // open: gt, lt
  Comparator #(.Bits(16)) Match1D_E (.a(RA1D), .b(WA3E), .eq(Match1D_E_eq));  // open: gt, lt
  or or_8 (or_8_out, PCSrcM, PCSrcE, PCSrcD);

  assign PCorLDRF = MemToRegM;

  // Notes on the sheet:
  //   LDRStall
  //   PCWritePendingF
endmodule
