// Digital circuit high_mask_in.dig as structural Verilog
module high_mask_in (
  input  [15:0] D_HIGH,
  input  [15:0] D,
  input  EN,
  output [15:0] Q
);

  Multiplexer #(.Bits(16)) multiplexer_1 (.sel(EN), .in_0(D_HIGH), .in_1({D_HIGH[7:0], D[7:0]}), .out(Q));
endmodule
