// Digital circuit mem_wb_ppr.dig as structural Verilog
module mem_wb_ppr (
  input  CLK,
  input  PCSrcM,
  input  RegWriteM,
  input  MemToRegM,
  input  [15:0] ReadDataM,
  input  [15:0] ALUResultM,
  input  [2:0] WA3M,
  input  SethM,
  output PCSrcW,
  output RegWriteW,
  output MemToRegW,
  output [15:0] ReadDataW,
  output [15:0] ALUResultW,
  output [2:0] WA3W,
  output SethW
);

  Register PCSrc (.D(PCSrcM), .C(CLK), .en(1'b1), .Q(PCSrcW));
  Register RegWrite (.D(RegWriteM), .C(CLK), .en(1'b1), .Q(RegWriteW));
  Register MemToReg (.D(MemToRegM), .C(CLK), .en(1'b1), .Q(MemToRegW));
  Register #(.Bits(16)) ReadData (.D(ReadDataM), .C(CLK), .en(1'b1), .Q(ReadDataW));
  Register Seth (.D(SethM), .C(CLK), .en(1'b1), .Q(SethW));
  Register #(.Bits(16)) ALUResult (.D(ALUResultM), .C(CLK), .en(1'b1), .Q(ALUResultW));
  Register #(.Bits(3)) WA3 (.D(WA3M), .C(CLK), .en(1'b1), .Q(WA3W));

  // Notes on the sheet:
  //   MEM/WB
endmodule
