// Digital circuit ram_parallel_rw_single_port.dig as structural Verilog
module ram_parallel_rw_single_port (
  input  CLK,
  input  WE,
  input  [15:0] A_ST,
  input  [15:0] A_LD,
  input  [15:0] D_ST,
  output [15:0] D
);

  RAMDualAccess #(.AddrBits(16), .isProgramMemory("true"), .Bits(16)) ramdualaccess_1 (
    .str(WE), .C(CLK), .ld(1'b0), .A1(A_ST), .Din1(D_ST), .A2(A_LD), .D2(D));  // open: D1
endmodule
