// Digital circuit circular_buffer.dig as structural Verilog
module circular_buffer (
  input  TailWE,
  input  [37:0] TailData,
  input  HeadRE,
  input  UpdateWE,
  input  [37:0] UpdateData,
  input  [4:0] UpdateA,
  input  CLK,
  output [37:0] HeadData,
  output [4:0] TailIdx,
  output [4:0] HeadIdx
);

  wire demultiplexer_1_out_0, demultiplexer_1_out_1, demultiplexer_1_out_2, demultiplexer_1_out_3,
       demultiplexer_1_out_4, demultiplexer_1_out_5, demultiplexer_1_out_6, demultiplexer_1_out_7,
       demultiplexer_1_out_8, demultiplexer_1_out_9, demultiplexer_1_out_10, demultiplexer_1_out_11,
       demultiplexer_1_out_12, demultiplexer_1_out_13, demultiplexer_1_out_14, demultiplexer_1_out_15,
       demultiplexer_1_out_16, demultiplexer_1_out_17, demultiplexer_1_out_18, demultiplexer_1_out_19,
       demultiplexer_1_out_20, demultiplexer_1_out_21, demultiplexer_1_out_22, demultiplexer_1_out_23,
       demultiplexer_1_out_24, demultiplexer_1_out_25, demultiplexer_1_out_26, demultiplexer_1_out_27,
       demultiplexer_1_out_28, demultiplexer_1_out_29, demultiplexer_1_out_30, demultiplexer_1_out_31,
       demultiplexer_2_out_0, demultiplexer_2_out_1, demultiplexer_2_out_2, demultiplexer_2_out_3,
       demultiplexer_2_out_4, demultiplexer_2_out_5, demultiplexer_2_out_6, demultiplexer_2_out_7,
       demultiplexer_2_out_8, demultiplexer_2_out_9, demultiplexer_2_out_10, demultiplexer_2_out_11,
       demultiplexer_2_out_12, demultiplexer_2_out_13, demultiplexer_2_out_14, demultiplexer_2_out_15,
       demultiplexer_2_out_16, demultiplexer_2_out_17, demultiplexer_2_out_18, demultiplexer_2_out_19,
       demultiplexer_2_out_20, demultiplexer_2_out_21, demultiplexer_2_out_22, demultiplexer_2_out_23,
       demultiplexer_2_out_24, demultiplexer_2_out_25, demultiplexer_2_out_26, demultiplexer_2_out_27,
       demultiplexer_2_out_28, demultiplexer_2_out_29, demultiplexer_2_out_30, demultiplexer_2_out_31,
       or_3_out, or_5_out, or_7_out, or_9_out, or_11_out, or_13_out, or_15_out, or_17_out, or_19_out,
       or_21_out, or_23_out, or_25_out, or_27_out, or_29_out, or_31_out, or_33_out, or_35_out, or_37_out,
       or_39_out, or_41_out, or_43_out, or_45_out, or_47_out, or_49_out, or_51_out, or_53_out, or_55_out,
       or_57_out, or_59_out, or_61_out, or_63_out, or_65_out;
  wire [37:0] demultiplexer_3_out_0, demultiplexer_3_out_1, demultiplexer_3_out_2, demultiplexer_3_out_3,
       demultiplexer_3_out_4, demultiplexer_3_out_5, demultiplexer_3_out_6, demultiplexer_3_out_7,
       demultiplexer_3_out_8, demultiplexer_3_out_9, demultiplexer_3_out_10, demultiplexer_3_out_11,
       demultiplexer_3_out_12, demultiplexer_3_out_13, demultiplexer_3_out_14, demultiplexer_3_out_15,
       demultiplexer_3_out_16, demultiplexer_3_out_17, demultiplexer_3_out_18, demultiplexer_3_out_19,
       demultiplexer_3_out_20, demultiplexer_3_out_21, demultiplexer_3_out_22, demultiplexer_3_out_23,
       demultiplexer_3_out_24, demultiplexer_3_out_25, demultiplexer_3_out_26, demultiplexer_3_out_27,
       demultiplexer_3_out_28, demultiplexer_3_out_29, demultiplexer_3_out_30, demultiplexer_3_out_31,
       demultiplexer_4_out_0, demultiplexer_4_out_1, demultiplexer_4_out_2, demultiplexer_4_out_3,
       demultiplexer_4_out_4, demultiplexer_4_out_5, demultiplexer_4_out_6, demultiplexer_4_out_7,
       demultiplexer_4_out_8, demultiplexer_4_out_9, demultiplexer_4_out_10, demultiplexer_4_out_11,
       demultiplexer_4_out_12, demultiplexer_4_out_13, demultiplexer_4_out_14, demultiplexer_4_out_15,
       demultiplexer_4_out_16, demultiplexer_4_out_17, demultiplexer_4_out_18, demultiplexer_4_out_19,
       demultiplexer_4_out_20, demultiplexer_4_out_21, demultiplexer_4_out_22, demultiplexer_4_out_23,
       demultiplexer_4_out_24, demultiplexer_4_out_25, demultiplexer_4_out_26, demultiplexer_4_out_27,
       demultiplexer_4_out_28, demultiplexer_4_out_29, demultiplexer_4_out_30, demultiplexer_4_out_31,
       multiplexer_1_out, or_1_out, or_2_out, or_4_out, or_6_out, or_8_out, or_10_out, or_12_out, or_14_out,
       or_16_out, or_18_out, or_20_out, or_22_out, or_24_out, or_26_out, or_28_out, or_30_out, or_32_out,
       or_34_out, or_36_out, or_38_out, or_40_out, or_42_out, or_44_out, or_46_out, or_48_out, or_50_out,
       or_52_out, or_54_out, or_56_out, or_58_out, or_60_out, or_62_out, or_64_out, ROB_0_q, ROB_1_q,
       ROB_2_q, ROB_3_q, ROB_4_q, ROB_5_q, ROB_6_q, ROB_7_q, ROB_8_q, ROB_9_q, ROB_10_q, ROB_11_q, ROB_12_q,
       ROB_13_q, ROB_14_q, ROB_15_q, ROB_16_q, ROB_17_q, ROB_18_q, ROB_19_q, ROB_20_q, ROB_21_q, ROB_22_q,
       ROB_23_q, ROB_24_q, ROB_25_q, ROB_26_q, ROB_27_q, ROB_28_q, ROB_29_q, ROB_30_q, ROB_31_q;

  Counter #(.Bits(5)) Write_Index__TailA (.en(TailWE), .C(CLK), .clr(1'b0), .out(TailIdx));  // open: ovf
  Counter #(.Bits(5)) Read_Index__HeadA (.en(HeadRE), .C(CLK), .clr(HeadRE), .out(HeadIdx));  // open: ovf
  Demultiplexer #(.Selector_Bits(5)) demultiplexer_1 (
    .sel(UpdateA), .in(UpdateWE), .out_0(demultiplexer_1_out_0), .out_1(demultiplexer_1_out_1),
    .out_2(demultiplexer_1_out_2), .out_3(demultiplexer_1_out_3), .out_4(demultiplexer_1_out_4),
    .out_5(demultiplexer_1_out_5), .out_6(demultiplexer_1_out_6), .out_7(demultiplexer_1_out_7),
    .out_8(demultiplexer_1_out_8), .out_9(demultiplexer_1_out_9), .out_10(demultiplexer_1_out_10),
    .out_11(demultiplexer_1_out_11), .out_12(demultiplexer_1_out_12), .out_13(demultiplexer_1_out_13),
    .out_14(demultiplexer_1_out_14), .out_15(demultiplexer_1_out_15), .out_16(demultiplexer_1_out_16),
    .out_17(demultiplexer_1_out_17), .out_18(demultiplexer_1_out_18), .out_19(demultiplexer_1_out_19),
    .out_20(demultiplexer_1_out_20), .out_21(demultiplexer_1_out_21), .out_22(demultiplexer_1_out_22),
    .out_23(demultiplexer_1_out_23), .out_24(demultiplexer_1_out_24), .out_25(demultiplexer_1_out_25),
    .out_26(demultiplexer_1_out_26), .out_27(demultiplexer_1_out_27), .out_28(demultiplexer_1_out_28),
    .out_29(demultiplexer_1_out_29), .out_30(demultiplexer_1_out_30), .out_31(demultiplexer_1_out_31));
  Demultiplexer #(.Selector_Bits(5)) demultiplexer_2 (
    .sel(TailIdx), .in(TailWE), .out_0(demultiplexer_2_out_0), .out_1(demultiplexer_2_out_1),
    .out_2(demultiplexer_2_out_2), .out_3(demultiplexer_2_out_3), .out_4(demultiplexer_2_out_4),
    .out_5(demultiplexer_2_out_5), .out_6(demultiplexer_2_out_6), .out_7(demultiplexer_2_out_7),
    .out_8(demultiplexer_2_out_8), .out_9(demultiplexer_2_out_9), .out_10(demultiplexer_2_out_10),
    .out_11(demultiplexer_2_out_11), .out_12(demultiplexer_2_out_12), .out_13(demultiplexer_2_out_13),
    .out_14(demultiplexer_2_out_14), .out_15(demultiplexer_2_out_15), .out_16(demultiplexer_2_out_16),
    .out_17(demultiplexer_2_out_17), .out_18(demultiplexer_2_out_18), .out_19(demultiplexer_2_out_19),
    .out_20(demultiplexer_2_out_20), .out_21(demultiplexer_2_out_21), .out_22(demultiplexer_2_out_22),
    .out_23(demultiplexer_2_out_23), .out_24(demultiplexer_2_out_24), .out_25(demultiplexer_2_out_25),
    .out_26(demultiplexer_2_out_26), .out_27(demultiplexer_2_out_27), .out_28(demultiplexer_2_out_28),
    .out_29(demultiplexer_2_out_29), .out_30(demultiplexer_2_out_30), .out_31(demultiplexer_2_out_31));
  assign or_1_out = multiplexer_1_out | UpdateData;  // Or or_1, 38 bits wide
  Demultiplexer #(.Selector_Bits(5), .Bits(38)) demultiplexer_3 (
    .sel(UpdateA), .in(or_1_out), .out_0(demultiplexer_3_out_0), .out_1(demultiplexer_3_out_1),
    .out_2(demultiplexer_3_out_2), .out_3(demultiplexer_3_out_3), .out_4(demultiplexer_3_out_4),
    .out_5(demultiplexer_3_out_5), .out_6(demultiplexer_3_out_6), .out_7(demultiplexer_3_out_7),
    .out_8(demultiplexer_3_out_8), .out_9(demultiplexer_3_out_9), .out_10(demultiplexer_3_out_10),
    .out_11(demultiplexer_3_out_11), .out_12(demultiplexer_3_out_12), .out_13(demultiplexer_3_out_13),
    .out_14(demultiplexer_3_out_14), .out_15(demultiplexer_3_out_15), .out_16(demultiplexer_3_out_16),
    .out_17(demultiplexer_3_out_17), .out_18(demultiplexer_3_out_18), .out_19(demultiplexer_3_out_19),
    .out_20(demultiplexer_3_out_20), .out_21(demultiplexer_3_out_21), .out_22(demultiplexer_3_out_22),
    .out_23(demultiplexer_3_out_23), .out_24(demultiplexer_3_out_24), .out_25(demultiplexer_3_out_25),
    .out_26(demultiplexer_3_out_26), .out_27(demultiplexer_3_out_27), .out_28(demultiplexer_3_out_28),
    .out_29(demultiplexer_3_out_29), .out_30(demultiplexer_3_out_30), .out_31(demultiplexer_3_out_31));
  Demultiplexer #(.Selector_Bits(5), .Bits(38)) demultiplexer_4 (
    .sel(TailIdx), .in(TailData), .out_0(demultiplexer_4_out_0), .out_1(demultiplexer_4_out_1),
    .out_2(demultiplexer_4_out_2), .out_3(demultiplexer_4_out_3), .out_4(demultiplexer_4_out_4),
    .out_5(demultiplexer_4_out_5), .out_6(demultiplexer_4_out_6), .out_7(demultiplexer_4_out_7),
    .out_8(demultiplexer_4_out_8), .out_9(demultiplexer_4_out_9), .out_10(demultiplexer_4_out_10),
    .out_11(demultiplexer_4_out_11), .out_12(demultiplexer_4_out_12), .out_13(demultiplexer_4_out_13),
    .out_14(demultiplexer_4_out_14), .out_15(demultiplexer_4_out_15), .out_16(demultiplexer_4_out_16),
    .out_17(demultiplexer_4_out_17), .out_18(demultiplexer_4_out_18), .out_19(demultiplexer_4_out_19),
    .out_20(demultiplexer_4_out_20), .out_21(demultiplexer_4_out_21), .out_22(demultiplexer_4_out_22),
    .out_23(demultiplexer_4_out_23), .out_24(demultiplexer_4_out_24), .out_25(demultiplexer_4_out_25),
    .out_26(demultiplexer_4_out_26), .out_27(demultiplexer_4_out_27), .out_28(demultiplexer_4_out_28),
    .out_29(demultiplexer_4_out_29), .out_30(demultiplexer_4_out_30), .out_31(demultiplexer_4_out_31));
  assign or_2_out = demultiplexer_4_out_0 | demultiplexer_3_out_0;  // Or or_2, 38 bits wide
  or or_3 (or_3_out, demultiplexer_2_out_0, demultiplexer_1_out_0);
  assign or_4_out = demultiplexer_4_out_1 | demultiplexer_3_out_1;  // Or or_4, 38 bits wide
  or or_5 (or_5_out, demultiplexer_2_out_1, demultiplexer_1_out_1);
  assign or_6_out = demultiplexer_4_out_2 | demultiplexer_3_out_2;  // Or or_6, 38 bits wide
  or or_7 (or_7_out, demultiplexer_2_out_2, demultiplexer_1_out_2);
  assign or_8_out = demultiplexer_4_out_3 | demultiplexer_3_out_3;  // Or or_8, 38 bits wide
  or or_9 (or_9_out, demultiplexer_2_out_3, demultiplexer_1_out_3);
  assign or_10_out = demultiplexer_4_out_4 | demultiplexer_3_out_4;  // Or or_10, 38 bits wide
  or or_11 (or_11_out, demultiplexer_2_out_4, demultiplexer_1_out_4);
  assign or_12_out = demultiplexer_4_out_5 | demultiplexer_3_out_5;  // Or or_12, 38 bits wide
  or or_13 (or_13_out, demultiplexer_2_out_5, demultiplexer_1_out_5);
  assign or_14_out = demultiplexer_4_out_6 | demultiplexer_3_out_6;  // Or or_14, 38 bits wide
  or or_15 (or_15_out, demultiplexer_2_out_6, demultiplexer_1_out_6);
  assign or_16_out = demultiplexer_4_out_7 | demultiplexer_3_out_7;  // Or or_16, 38 bits wide
  or or_17 (or_17_out, demultiplexer_2_out_7, demultiplexer_1_out_7);
  assign or_18_out = demultiplexer_4_out_8 | demultiplexer_3_out_8;  // Or or_18, 38 bits wide
  or or_19 (or_19_out, demultiplexer_2_out_8, demultiplexer_1_out_8);
  assign or_20_out = demultiplexer_4_out_9 | demultiplexer_3_out_9;  // Or or_20, 38 bits wide
  or or_21 (or_21_out, demultiplexer_2_out_9, demultiplexer_1_out_9);
  assign or_22_out = demultiplexer_4_out_10 | demultiplexer_3_out_10;  // Or or_22, 38 bits wide
  or or_23 (or_23_out, demultiplexer_2_out_10, demultiplexer_1_out_10);
  assign or_24_out = demultiplexer_4_out_11 | demultiplexer_3_out_11;  // Or or_24, 38 bits wide
  or or_25 (or_25_out, demultiplexer_2_out_11, demultiplexer_1_out_11);
  assign or_26_out = demultiplexer_4_out_12 | demultiplexer_3_out_12;  // Or or_26, 38 bits wide
  or or_27 (or_27_out, demultiplexer_2_out_12, demultiplexer_1_out_12);
  assign or_28_out = demultiplexer_4_out_13 | demultiplexer_3_out_13;  // Or or_28, 38 bits wide
  or or_29 (or_29_out, demultiplexer_2_out_13, demultiplexer_1_out_13);
  assign or_30_out = demultiplexer_4_out_14 | demultiplexer_3_out_14;  // Or or_30, 38 bits wide
  or or_31 (or_31_out, demultiplexer_2_out_14, demultiplexer_1_out_14);
  assign or_32_out = demultiplexer_4_out_15 | demultiplexer_3_out_15;  // Or or_32, 38 bits wide
  or or_33 (or_33_out, demultiplexer_2_out_15, demultiplexer_1_out_15);
  assign or_34_out = demultiplexer_4_out_16 | demultiplexer_3_out_16;  // Or or_34, 38 bits wide
  or or_35 (or_35_out, demultiplexer_2_out_16, demultiplexer_1_out_16);
  assign or_36_out = demultiplexer_4_out_17 | demultiplexer_3_out_17;  // Or or_36, 38 bits wide
  or or_37 (or_37_out, demultiplexer_2_out_17, demultiplexer_1_out_17);
  assign or_38_out = demultiplexer_4_out_18 | demultiplexer_3_out_18;  // Or or_38, 38 bits wide
  or or_39 (or_39_out, demultiplexer_2_out_18, demultiplexer_1_out_18);
  assign or_40_out = demultiplexer_4_out_19 | demultiplexer_3_out_19;  // Or or_40, 38 bits wide
  or or_41 (or_41_out, demultiplexer_2_out_19, demultiplexer_1_out_19);
  assign or_42_out = demultiplexer_4_out_20 | demultiplexer_3_out_20;  // Or or_42, 38 bits wide
  or or_43 (or_43_out, demultiplexer_2_out_20, demultiplexer_1_out_20);
  assign or_44_out = demultiplexer_4_out_21 | demultiplexer_3_out_21;  // Or or_44, 38 bits wide
  or or_45 (or_45_out, demultiplexer_2_out_21, demultiplexer_1_out_21);
  assign or_46_out = demultiplexer_4_out_22 | demultiplexer_3_out_22;  // Or or_46, 38 bits wide
  or or_47 (or_47_out, demultiplexer_2_out_22, demultiplexer_1_out_22);
  assign or_48_out = demultiplexer_4_out_23 | demultiplexer_3_out_23;  // Or or_48, 38 bits wide
  or or_49 (or_49_out, demultiplexer_2_out_23, demultiplexer_1_out_23);
  assign or_50_out = demultiplexer_4_out_24 | demultiplexer_3_out_24;  // Or or_50, 38 bits wide
  or or_51 (or_51_out, demultiplexer_2_out_24, demultiplexer_1_out_24);
  assign or_52_out = demultiplexer_4_out_25 | demultiplexer_3_out_25;  // Or or_52, 38 bits wide
  or or_53 (or_53_out, demultiplexer_2_out_25, demultiplexer_1_out_25);
  assign or_54_out = demultiplexer_4_out_26 | demultiplexer_3_out_26;  // Or or_54, 38 bits wide
  or or_55 (or_55_out, demultiplexer_2_out_26, demultiplexer_1_out_26);
  assign or_56_out = demultiplexer_4_out_27 | demultiplexer_3_out_27;  // Or or_56, 38 bits wide
  or or_57 (or_57_out, demultiplexer_2_out_27, demultiplexer_1_out_27);
  assign or_58_out = demultiplexer_4_out_28 | demultiplexer_3_out_28;  // Or or_58, 38 bits wide
  or or_59 (or_59_out, demultiplexer_2_out_28, demultiplexer_1_out_28);
  assign or_60_out = demultiplexer_4_out_29 | demultiplexer_3_out_29;  // Or or_60, 38 bits wide
  or or_61 (or_61_out, demultiplexer_2_out_29, demultiplexer_1_out_29);
  assign or_62_out = demultiplexer_4_out_30 | demultiplexer_3_out_30;  // Or or_62, 38 bits wide
  or or_63 (or_63_out, demultiplexer_2_out_30, demultiplexer_1_out_30);
  assign or_64_out = demultiplexer_4_out_31 | demultiplexer_3_out_31;  // Or or_64, 38 bits wide
  or or_65 (or_65_out, demultiplexer_2_out_31, demultiplexer_1_out_31);
  Register #(.Bits(38)) ROB_0 (.D(or_2_out), .C(CLK), .en(or_3_out), .Q(ROB_0_q));
  Register #(.Bits(38)) ROB_1 (.D(or_4_out), .C(CLK), .en(or_5_out), .Q(ROB_1_q));
  Register #(.Bits(38)) ROB_2 (.D(or_6_out), .C(CLK), .en(or_7_out), .Q(ROB_2_q));
  Register #(.Bits(38)) ROB_3 (.D(or_8_out), .C(CLK), .en(or_9_out), .Q(ROB_3_q));
  Register #(.Bits(38)) ROB_4 (.D(or_10_out), .C(CLK), .en(or_11_out), .Q(ROB_4_q));
  Register #(.Bits(38)) ROB_5 (.D(or_12_out), .C(CLK), .en(or_13_out), .Q(ROB_5_q));
  Register #(.Bits(38)) ROB_6 (.D(or_14_out), .C(CLK), .en(or_15_out), .Q(ROB_6_q));
  Register #(.Bits(38)) ROB_7 (.D(or_16_out), .C(CLK), .en(or_17_out), .Q(ROB_7_q));
  Register #(.Bits(38)) ROB_8 (.D(or_18_out), .C(CLK), .en(or_19_out), .Q(ROB_8_q));
  Register #(.Bits(38)) ROB_9 (.D(or_20_out), .C(CLK), .en(or_21_out), .Q(ROB_9_q));
  Register #(.Bits(38)) ROB_10 (.D(or_22_out), .C(CLK), .en(or_23_out), .Q(ROB_10_q));
  Register #(.Bits(38)) ROB_11 (.D(or_24_out), .C(CLK), .en(or_25_out), .Q(ROB_11_q));
  Register #(.Bits(38)) ROB_12 (.D(or_26_out), .C(CLK), .en(or_27_out), .Q(ROB_12_q));
  Register #(.Bits(38)) ROB_13 (.D(or_28_out), .C(CLK), .en(or_29_out), .Q(ROB_13_q));
  Register #(.Bits(38)) ROB_14 (.D(or_30_out), .C(CLK), .en(or_31_out), .Q(ROB_14_q));
  Register #(.Bits(38)) ROB_15 (.D(or_32_out), .C(CLK), .en(or_33_out), .Q(ROB_15_q));
  Register #(.Bits(38)) ROB_16 (.D(or_34_out), .C(CLK), .en(or_35_out), .Q(ROB_16_q));
  Register #(.Bits(38)) ROB_17 (.D(or_36_out), .C(CLK), .en(or_37_out), .Q(ROB_17_q));
  Register #(.Bits(38)) ROB_18 (.D(or_38_out), .C(CLK), .en(or_39_out), .Q(ROB_18_q));
  Register #(.Bits(38)) ROB_19 (.D(or_40_out), .C(CLK), .en(or_41_out), .Q(ROB_19_q));
  Register #(.Bits(38)) ROB_20 (.D(or_42_out), .C(CLK), .en(or_43_out), .Q(ROB_20_q));
  Register #(.Bits(38)) ROB_21 (.D(or_44_out), .C(CLK), .en(or_45_out), .Q(ROB_21_q));
  Register #(.Bits(38)) ROB_22 (.D(or_46_out), .C(CLK), .en(or_47_out), .Q(ROB_22_q));
  Register #(.Bits(38)) ROB_23 (.D(or_48_out), .C(CLK), .en(or_49_out), .Q(ROB_23_q));
  Register #(.Bits(38)) ROB_24 (.D(or_50_out), .C(CLK), .en(or_51_out), .Q(ROB_24_q));
  Register #(.Bits(38)) ROB_25 (.D(or_52_out), .C(CLK), .en(or_53_out), .Q(ROB_25_q));
  Register #(.Bits(38)) ROB_26 (.D(or_54_out), .C(CLK), .en(or_55_out), .Q(ROB_26_q));
  Register #(.Bits(38)) ROB_27 (.D(or_56_out), .C(CLK), .en(or_57_out), .Q(ROB_27_q));
  Register #(.Bits(38)) ROB_28 (.D(or_58_out), .C(CLK), .en(or_59_out), .Q(ROB_28_q));
  Register #(.Bits(38)) ROB_29 (.D(or_60_out), .C(CLK), .en(or_61_out), .Q(ROB_29_q));
  Register #(.Bits(38)) ROB_30 (.D(or_62_out), .C(CLK), .en(or_63_out), .Q(ROB_30_q));
  Register #(.Bits(38)) ROB_31 (.D(or_64_out), .C(CLK), .en(or_65_out), .Q(ROB_31_q));
  Multiplexer #(.Selector_Bits(5), .Bits(38)) multiplexer_1 (
    .sel(UpdateA), .in_0(ROB_0_q), .in_1(ROB_1_q), .in_2(ROB_2_q), .in_3(ROB_3_q), .in_4(ROB_4_q),
    .in_5(ROB_5_q), .in_6(ROB_6_q), .in_7(ROB_7_q), .in_8(ROB_8_q), .in_9(ROB_9_q), .in_10(ROB_10_q),
    .in_11(ROB_11_q), .in_12(ROB_12_q), .in_13(ROB_13_q), .in_14(ROB_14_q), .in_15(ROB_15_q),
    .in_16(ROB_16_q), .in_17(ROB_17_q), .in_18(ROB_18_q), .in_19(ROB_19_q), .in_20(ROB_20_q),
    .in_21(ROB_21_q), .in_22(ROB_22_q), .in_23(ROB_23_q), .in_24(ROB_24_q), .in_25(ROB_25_q),
    .in_26(ROB_26_q), .in_27(ROB_27_q), .in_28(ROB_28_q), .in_29(ROB_29_q), .in_30(ROB_30_q),
    .in_31(ROB_31_q), .out(multiplexer_1_out));
  Multiplexer #(.Selector_Bits(5), .Bits(38)) multiplexer_2 (
    .sel(HeadIdx), .in_0(ROB_0_q), .in_1(ROB_1_q), .in_2(ROB_2_q), .in_3(ROB_3_q), .in_4(ROB_4_q),
    .in_5(ROB_5_q), .in_6(ROB_6_q), .in_7(ROB_7_q), .in_8(ROB_8_q), .in_9(ROB_9_q), .in_10(ROB_10_q),
    .in_11(ROB_11_q), .in_12(ROB_12_q), .in_13(ROB_13_q), .in_14(ROB_14_q), .in_15(ROB_15_q),
    .in_16(ROB_16_q), .in_17(ROB_17_q), .in_18(ROB_18_q), .in_19(ROB_19_q), .in_20(ROB_20_q),
    .in_21(ROB_21_q), .in_22(ROB_22_q), .in_23(ROB_23_q), .in_24(ROB_24_q), .in_25(ROB_25_q),
    .in_26(ROB_26_q), .in_27(ROB_27_q), .in_28(ROB_28_q), .in_29(ROB_29_q), .in_30(ROB_30_q),
    .in_31(ROB_31_q), .out(HeadData));

  // Notes on the sheet:
  //   ROB Circular Buffer
  //   Update Enable
  //   Tail Enable
  //   Update Data
  //   Tail Data
  //   Current Data
endmodule
