// Digital circuit cpu.dig as structural Verilog
module cpu (
  input  CLK,
  input  CLK_2,
  input  CU_FL_EN
);

  wire and_1_out, and_2_out, and_3_out, and_4_out, and_5_out, and_6_out, comparator_1_eq,
       condition_unit_1_condexe, condition_unit_2_condexe, control_unit_1_alusrcd, control_unit_1_branchd,
       control_unit_1_flagen, control_unit_1_flagwrited, control_unit_1_memtoregd, control_unit_1_memwrited,
       control_unit_1_nop, control_unit_1_pcsrcd, control_unit_1_regwrited, control_unit_1_sethd,
       dp_i_ppr_1_branchi, dp_i_ppr_1_condi, dp_i_ppr_1_flagwritei, dp_i_ppr_1_hei, dp_i_ppr_1_pcsrci,
       ex_mem_ppr_1_memtoregm, ex_mem_ppr_1_memwritem, ex_mem_ppr_1_pcsrcm, ex_mem_ppr_1_regwritem,
       ex_mem_ppr_1_sethm, hazard_unit_1_flushd, hazard_unit_1_flushe, hazard_unit_1_stalld,
       hazard_unit_1_stallf, i_wb_ppr_1_p5, i_wb_ppr_1_p6, id_ex_ppr_1_alusrce, id_ex_ppr_1_branche,
       id_ex_ppr_1_conde, id_ex_ppr_1_flagwritee, id_ex_ppr_1_memtorege, id_ex_ppr_1_memwritee,
       id_ex_ppr_1_pcsrce, id_ex_ppr_1_regwritee, id_ex_ppr_1_sethe, Is_I_Format_eq, Issue_Queue_empty,
       Issue_Queue_full, mem_wb_ppr_1_memtoregw, mem_wb_ppr_1_pcsrcw, mem_wb_ppr_1_regwritew,
       mem_wb_ppr_1_sethw, multiplexer_6_out, multiplexer_7_out, not_1_out, not_2_out, not_3_out, not_4_out,
       not_5_out, not_6_out, RMT_p8, RMT_p9, RMT_p10, RMT_p11, RMT_p12, RMT_p13, rrd_dp_ppr_1_p8, undriven,
       undriven_4, undriven_5, wb_r_ppr_1_p3, wb_r_ppr_1_p4;
  wire [1:0] control_unit_1_aluctrld, dp_i_ppr_1_aluopi, hazard_unit_1_forwardae, hazard_unit_1_forwardbe,
       id_ex_ppr_1_aluctrle;
  wire [2:0] ex_mem_ppr_1_wa3m, id_ex_ppr_1_wae, mem_wb_ppr_1_wa3w;
  wire [3:0] alu_1_flag, alu_2_flag, condition_unit_1_flagsm, dp_i_ppr_1_flagsi, id_ex_ppr_1_flagse, PC_2_q,
       PC_q, PC_q_2, PC_q_3, PC_q_4;
  wire [4:0] dp_i_ppr_1_dsttagi, RMT_p5, RMT_p7, rrd_dp_ppr_1_p13, wb_r_ppr_1_p1;
  wire [15:0] alu_1_result, alu_2_result, bitextender_1_out, bitextender_2_out, bitextender_3_out,
       bitextender_4_out, dp_i_ppr_1_rai, dp_i_ppr_1_rbi, ex_mem_ppr_1_aluresultm, ex_mem_ppr_1_writedatam,
       i_wb_ppr_1_p7, i_wb_ppr_1_p8, id_ex_ppr_1_ra1e, id_ex_ppr_1_ra2e, id_ex_ppr_1_rd1e, id_ex_ppr_1_rd2e,
       id_ex_ppr_1_sei16e, if_id_ppr_1_insn_out, IF_ID_RR_RD_PPR_insn_out, IF_ID_RR_RD_PPR_pc_out,
       mem_wb_ppr_1_aluresultw, mem_wb_ppr_1_readdataw, multiplexer_1_out, multiplexer_2_out,
       multiplexer_3_out, multiplexer_4_out, multiplexer_5_out, multiplexer_8_out, multiplexer_9_out,
       multiplexer_10_out, multiplexer_12_out, plus_1_2_s, plus_1_s, RAM_2_d1, RAM_2_d2, RAM_d2,
       reg_address_extender_1_out, reg_address_extender_2_out, reg_address_extender_3_out,
       reg_address_extender_4_out, reg_address_extender_5_out, reg_file_1_out1, reg_file_1_out2,
       rrd_dp_ppr_1_p11, rrd_dp_ppr_1_p12, rrd_dp_ppr_1_p14, undriven_3, wb_r_ppr_1_p2;
  wire [15:4] PC_2_q_2;
  wire [37:0] ROB_headdata;
  wire [46:0] Issue_Queue_nextdata, multiplexer_11_out;
  wire [46:6] rrd_dp_ppr_1_p10;
  wire [46:40] undriven_2;

  Seven_Seg_Hex seven_seg_hex_1 (.d(PC_q_3), .dp(1'b0));
  Seven_Seg_Hex seven_seg_hex_2 (.d(PC_q_4), .dp(1'b0));
  Seven_Seg_Hex seven_seg_hex_3 (.d(PC_q), .dp(1'b0));
  Seven_Seg_Hex seven_seg_hex_4 (.d(PC_q_2), .dp(1'b0));
  Seven_Seg_Hex seven_seg_hex_5 (.d(PC_2_q_2[11:8]), .dp(1'b0));
  Seven_Seg_Hex seven_seg_hex_6 (.d(PC_2_q_2[15:12]), .dp(1'b0));
  Seven_Seg_Hex seven_seg_hex_7 (.d(PC_2_q), .dp(1'b0));
  Seven_Seg_Hex seven_seg_hex_8 (.d(PC_2_q_2[7:4]), .dp(1'b0));
  Multiplexer #(.Bits(16)) multiplexer_1 (
    .sel(undriven_4), .in_0(plus_1_s), .in_1(undriven_3), .out(multiplexer_1_out));
  not not_1 (not_1_out, hazard_unit_1_stallf);
  Multiplexer #(.Bits(16)) multiplexer_2 (
    .sel(and_6_out), .in_0(multiplexer_1_out), .in_1(alu_2_result), .out(multiplexer_2_out));
  Multiplexer #(.Bits(16)) multiplexer_3 (
    .sel(and_4_out), .in_0(multiplexer_4_out), .in_1(alu_1_result), .out(multiplexer_3_out));
  Multiplexer #(.Bits(16)) multiplexer_4 (
    .sel(mem_wb_ppr_1_pcsrcw), .in_0(plus_1_2_s), .in_1(multiplexer_12_out), .out(multiplexer_4_out));
  Register #(.Bits(16), .isProgramCounter("true")) PC (
    .D(multiplexer_2_out), .C(CLK_2), .en(undriven_5), .Q({PC_q_4, PC_q_3, PC_q_2, PC_q}));
  Add #(.Bits(16)) plus_1 (.a(16'h1), .b({PC_q_4, PC_q_3, PC_q_2, PC_q}), .c_i(1'b0), .s(plus_1_s));  // open: c_o
  Register #(.Bits(16), .isProgramCounter("true")) PC_2 (
    .D(multiplexer_3_out), .C(CLK), .en(not_1_out), .Q({PC_2_q_2, PC_2_q}));
  Add #(.Bits(16)) plus_1_2 (.a(16'h1), .b({PC_2_q_2, PC_2_q}), .c_i(1'b0), .s(plus_1_2_s));  // open: c_o
  RAMDualAccess #(.AddrBits(16), .isProgramMemory("true"), .Bits(16)) RAM (
    .str(i_wb_ppr_1_p6), .C(CLK_2), .ld(i_wb_ppr_1_p5), .A1(i_wb_ppr_1_p8), .Din1(i_wb_ppr_1_p7),
    .A2({PC_q_4, PC_q_3, PC_q_2, PC_q}), .D2(RAM_d2));  // open: D1
  RAMDualAccess #(.AddrBits(16), .isProgramMemory("true"), .Bits(16)) RAM_2 (
    .str(ex_mem_ppr_1_memwritem), .C(CLK), .ld(ex_mem_ppr_1_memtoregm), .A1(ex_mem_ppr_1_aluresultm),
    .Din1(ex_mem_ppr_1_writedatam), .A2({PC_2_q_2, PC_2_q}), .D1(RAM_2_d1), .D2(RAM_2_d2));
  ifd_rrd_ppr IF_ID_RR_RD_PPR (
    .CLK(CLK_2), .INSN_IN(RAM_d2), .PC_IN({PC_q_4, PC_q_3, PC_q_2, PC_q}),
    .INSN_OUT(IF_ID_RR_RD_PPR_insn_out), .PC_OUT(IF_ID_RR_RD_PPR_pc_out), .EN(not_2_out));
  if_id_ppr if_id_ppr_1 (
    .CLK(CLK), .INSN_IN(RAM_2_d2), .INSN_OUT(if_id_ppr_1_insn_out), .CLR(hazard_unit_1_flushd), .EN(not_3_out));
  not not_2 (not_2_out, undriven);
  not not_3 (not_3_out, hazard_unit_1_stalld);
  control_unit control_unit_1 (
    .INST(if_id_ppr_1_insn_out), .PCSrcD(control_unit_1_pcsrcd), .RegWriteD(control_unit_1_regwrited),
    .MemToRegD(control_unit_1_memtoregd), .MemWriteD(control_unit_1_memwrited),
    .ALUCtrlD(control_unit_1_aluctrld), .BranchD(control_unit_1_branchd), .ALUSrcD(control_unit_1_alusrcd),
    .FlagWriteD(control_unit_1_flagwrited), .SethD(control_unit_1_sethd), .FlagEN(control_unit_1_flagen),
    .NOP(control_unit_1_nop));
  Multiplexer #(.Bits(16)) multiplexer_5 (
    .sel(control_unit_1_nop), .in_0(if_id_ppr_1_insn_out), .in_1({16{1'b0}}), .out(multiplexer_5_out));
  not not_4 (not_4_out, CLK);
  BitExtender #(.inputBits(4)) bitextender_1 (.in(alu_2_flag), .out(bitextender_1_out));
  // rename_map_table RMT: pin names not known; wires that end beside it: CLK_2, IF_ID_RR_RD_PPR_insn_out[6:4], IF_ID_RR_RD_PPR_insn_out[2:0], IF_ID_RR_RD_PPR_insn_out[10:8], RMT_p5, ROB_headdata[18:16], RMT_p7, RMT_p8, RMT_p9, RMT_p10, RMT_p11, RMT_p12, RMT_p13
  reg_file ARF (
    .RS1(IF_ID_RR_RD_PPR_insn_out[6:4]), .RS2(IF_ID_RR_RD_PPR_insn_out[2:0]), .WS(ROB_headdata[18:16]),
    .WE(comparator_1_eq), .IN(ROB_headdata[15:0]), .clk(CLK_2), .FL_IN(bitextender_1_out), .FL_EN(CU_FL_EN),
    .PC_IN(IF_ID_RR_RD_PPR_pc_out), .HE(wb_r_ppr_1_p4));  // open: OUT1, OUT2, PC_S, PC_WE
  circular_buffer ROB (
    .TailData({IF_ID_RR_RD_PPR_pc_out, 3'b000, IF_ID_RR_RD_PPR_insn_out[10:8], {16{1'b0}}}),
    .HeadRE(comparator_1_eq), .UpdateWE(1'b1), .UpdateData({{22{1'b0}}, wb_r_ppr_1_p2}),
    .UpdateA(wb_r_ppr_1_p1), .CLK(CLK_2), .HeadData(ROB_headdata), .TailIdx(RMT_p5), .HeadIdx(RMT_p7));  // open: TailWE
  Comparator comparator_1 (.a(ROB_headdata[19]), .b(1'b1), .eq(comparator_1_eq));  // open: gt, lt
  reg_address_extender reg_address_extender_1 (.IN(multiplexer_5_out[2:0]), .OUT(reg_address_extender_1_out));
  BitExtender #(.inputBits(4)) bitextender_2 (.in(condition_unit_1_flagsm), .out(bitextender_2_out));
  reg_address_extender reg_address_extender_2 (.IN(multiplexer_5_out[6:4]), .OUT(reg_address_extender_2_out));
  Multiplexer multiplexer_6 (.sel(RMT_p10), .in_0(RMT_p8), .in_1(RMT_p11), .out(multiplexer_6_out));
  Multiplexer multiplexer_7 (.sel(RMT_p12), .in_0(RMT_p9), .in_1(RMT_p13), .out(multiplexer_7_out));
  BitExtender bitextender_3 (.in(multiplexer_5_out[7:0]), .out(bitextender_3_out));
  reg_file reg_file_1 (
    .RS1(multiplexer_5_out[6:4]), .RS2(multiplexer_5_out[2:0]), .WS(mem_wb_ppr_1_wa3w),
    .WE(mem_wb_ppr_1_regwritew), .IN(multiplexer_12_out), .CLK(not_4_out), .FL_IN(bitextender_2_out),
    .FL_EN(control_unit_1_flagen), .PC_IN(multiplexer_3_out), .HE(mem_wb_ppr_1_sethw),
    .OUT1(reg_file_1_out1), .OUT2(reg_file_1_out2));
  id_ex_ppr id_ex_ppr_1 (
    .CLK(CLK), .PCSrcD(control_unit_1_pcsrcd), .RegWriteD(control_unit_1_regwrited),
    .MemToRegD(control_unit_1_memtoregd), .MemWriteD(control_unit_1_memwrited),
    .ALUCtrlD(control_unit_1_aluctrld), .BranchD(control_unit_1_branchd), .ALUSrcD(control_unit_1_alusrcd),
    .FlagWriteD(control_unit_1_flagwrited), .SethD(control_unit_1_sethd), .CondD(multiplexer_5_out[11]),
    .FlagsD(condition_unit_1_flagsm), .WAD(multiplexer_5_out[10:8]), .SEI16D(bitextender_3_out),
    .Ra1D(reg_address_extender_2_out), .Ra2D(reg_address_extender_1_out), .Rd1D(reg_file_1_out1),
    .Rd2D(reg_file_1_out2), .PCSrcE(id_ex_ppr_1_pcsrce), .RegWriteE(id_ex_ppr_1_regwritee),
    .MemToRegE(id_ex_ppr_1_memtorege), .MemWriteE(id_ex_ppr_1_memwritee), .ALUCtrlE(id_ex_ppr_1_aluctrle),
    .BranchE(id_ex_ppr_1_branche), .ALUSrcE(id_ex_ppr_1_alusrce), .FlagWriteE(id_ex_ppr_1_flagwritee),
    .SethE(id_ex_ppr_1_sethe), .CondE(id_ex_ppr_1_conde), .FlagsE(id_ex_ppr_1_flagse), .WAE(id_ex_ppr_1_wae),
    .SEI16E(id_ex_ppr_1_sei16e), .Ra1E(id_ex_ppr_1_ra1e), .Ra2E(id_ex_ppr_1_ra2e), .Rd1E(id_ex_ppr_1_rd1e),
    .Rd2E(id_ex_ppr_1_rd2e), .CLR(hazard_unit_1_flushe));
  // rrd_dp_ppr rrd_dp_ppr_1: pin names not known; wires that end beside it: CLK_2, RMT_p10, RMT_p12, multiplexer_6_out, multiplexer_7_out, RMT_p5, IF_ID_RR_RD_PPR_insn_out, rrd_dp_ppr_1_p8, rrd_dp_ppr_1_p10[6], rrd_dp_ppr_1_p10[23], rrd_dp_ppr_1_p11, rrd_dp_ppr_1_p12, rrd_dp_ppr_1_p13, rrd_dp_ppr_1_p14
  Multiplexer #(.Selector_Bits(2), .Bits(16)) multiplexer_8 (
    .sel(hazard_unit_1_forwardae), .in_0(id_ex_ppr_1_rd1e), .in_1(multiplexer_12_out),
    .in_2(ex_mem_ppr_1_aluresultm), .in_3({16{1'b0}}), .out(multiplexer_8_out));
  Multiplexer #(.Selector_Bits(2), .Bits(16)) multiplexer_9 (
    .sel(hazard_unit_1_forwardbe), .in_0(id_ex_ppr_1_rd2e), .in_1(multiplexer_12_out),
    .in_2(ex_mem_ppr_1_aluresultm), .in_3({16{1'b0}}), .out(multiplexer_9_out));
  hazard_unit hazard_unit_1 (
    .ALUSrcE(id_ex_ppr_1_alusrce), .RegWriteW(mem_wb_ppr_1_regwritew), .RegWriteM(ex_mem_ppr_1_regwritem),
    .RA1E(id_ex_ppr_1_ra1e), .WA3M(reg_address_extender_3_out), .RA2E(id_ex_ppr_1_ra2e),
    .WA3W(reg_address_extender_4_out), .MemtoRegE(id_ex_ppr_1_memtorege), .WA3E(reg_address_extender_5_out),
    .RA2D(reg_address_extender_1_out), .RA1D(reg_address_extender_2_out), .PCSrcD(control_unit_1_pcsrcd),
    .PCSrcE(id_ex_ppr_1_pcsrce), .PCSrcM(ex_mem_ppr_1_pcsrcm), .PCSrcW(mem_wb_ppr_1_pcsrcw),
    .BranchTakenE(and_4_out), .ForwardAE(hazard_unit_1_forwardae), .ForwardBE(hazard_unit_1_forwardbe),
    .StallD(hazard_unit_1_stalld), .StallF(hazard_unit_1_stallf), .FlushE(hazard_unit_1_flushe),
    .FlushD(hazard_unit_1_flushd));
  Comparator Is_I_Format (.a(rrd_dp_ppr_1_p14[12]), .b(1'b0), .eq(Is_I_Format_eq));  // open: gt, lt
  Multiplexer #(.Bits(16)) multiplexer_10 (
    .sel(id_ex_ppr_1_alusrce), .in_0(multiplexer_9_out), .in_1(id_ex_ppr_1_sei16e), .out(multiplexer_10_out));
  not not_5 (not_5_out, Is_I_Format_eq);
  BitExtender bitextender_4 (.in(rrd_dp_ppr_1_p14[7:0]), .out(bitextender_4_out));
  alu alu_1 (
    .A(multiplexer_8_out), .B(multiplexer_10_out), .ALUOP(id_ex_ppr_1_aluctrle), .RESULT(alu_1_result),
    .FLAG(alu_1_flag));
  Multiplexer #(.Bits(47)) multiplexer_11 (
    .sel(not_5_out), .in_0({undriven_2, bitextender_4_out, 18'h20001, rrd_dp_ppr_1_p13, 1'b1}),
    .in_1({rrd_dp_ppr_1_p10[46:40], rrd_dp_ppr_1_p12, rrd_dp_ppr_1_p10[23], rrd_dp_ppr_1_p11, rrd_dp_ppr_1_p10[6], rrd_dp_ppr_1_p13, 1'b1}),
    .out(multiplexer_11_out));
  condition_unit condition_unit_1 (
    .FlagWriteE(id_ex_ppr_1_flagwritee), .CondE(id_ex_ppr_1_conde), .FlagsE(id_ex_ppr_1_flagse),
    .ALUFlags(alu_1_flag), .FlagsM(condition_unit_1_flagsm), .CondExE(condition_unit_1_condexe));
  reg_address_extender reg_address_extender_3 (.IN(ex_mem_ppr_1_wa3m), .OUT(reg_address_extender_3_out));
  reg_address_extender reg_address_extender_4 (.IN(mem_wb_ppr_1_wa3w), .OUT(reg_address_extender_4_out));
  reg_address_extender reg_address_extender_5 (.IN(id_ex_ppr_1_wae), .OUT(reg_address_extender_5_out));
  issue_queue Issue_Queue (
    .CLK(CLK_2), .CLRNext(CLK_2), .BC_Tag(wb_r_ppr_1_p1), .BC_Result(wb_r_ppr_1_p2), .BC_WE(wb_r_ppr_1_p3),
    .TailData(multiplexer_11_out), .Tail_WE(not_6_out), .NextData(Issue_Queue_nextdata),
    .Full(Issue_Queue_full), .Empty(Issue_Queue_empty));
  not not_6 (not_6_out, Issue_Queue_full);
  and and_1 (and_1_out, id_ex_ppr_1_pcsrce, condition_unit_1_condexe);
  and and_2 (and_2_out, id_ex_ppr_1_regwritee, condition_unit_1_condexe);
  and and_3 (and_3_out, id_ex_ppr_1_memwritee, condition_unit_1_condexe);
  and and_4 (and_4_out, id_ex_ppr_1_branche, condition_unit_1_condexe);
  ex_mem_ppr ex_mem_ppr_1 (
    .CLK(CLK), .PCSrcE(and_1_out), .RegWriteE(and_2_out), .MemToRegE(id_ex_ppr_1_memtorege),
    .MemWriteE(and_3_out), .sethE(id_ex_ppr_1_sethe), .ALUResultE(alu_1_result),
    .WriteDataE(multiplexer_9_out), .WAE(id_ex_ppr_1_wae), .PCSrcM(ex_mem_ppr_1_pcsrcm),
    .RegWriteM(ex_mem_ppr_1_regwritem), .MemToRegM(ex_mem_ppr_1_memtoregm),
    .MemWriteM(ex_mem_ppr_1_memwritem), .sethM(ex_mem_ppr_1_sethm), .ALUResultM(ex_mem_ppr_1_aluresultm),
    .WriteDataM(ex_mem_ppr_1_writedatam), .WA3M(ex_mem_ppr_1_wa3m));
  dp_i_ppr dp_i_ppr_1 (
    .CLK(CLK_2), .DstTagDP(Issue_Queue_nextdata[5:1]), .RaDP(Issue_Queue_nextdata[22:7]),
    .RbDP(Issue_Queue_nextdata[39:24]), .PCSrcDP(Issue_Queue_nextdata[40]),
    .ALUOPDP(Issue_Queue_nextdata[42:41]), .BranchDP(Issue_Queue_nextdata[43]),
    .FlagWriteDP(Issue_Queue_nextdata[44]), .HEDP(Issue_Queue_nextdata[45]),
    .CondDP(Issue_Queue_nextdata[46]), .DstTagI(dp_i_ppr_1_dsttagi), .RaI(dp_i_ppr_1_rai),
    .RbI(dp_i_ppr_1_rbi), .PCSrcI(dp_i_ppr_1_pcsrci), .ALUOPI(dp_i_ppr_1_aluopi),
    .BranchI(dp_i_ppr_1_branchi), .FlagWriteI(dp_i_ppr_1_flagwritei), .HEI(dp_i_ppr_1_hei),
    .CondI(dp_i_ppr_1_condi), .FlagsI(dp_i_ppr_1_flagsi));  // open: FlagsDP
  mem_wb_ppr mem_wb_ppr_1 (
    .CLK(CLK), .PCSrcM(ex_mem_ppr_1_pcsrcm), .RegWriteM(ex_mem_ppr_1_regwritem),
    .MemToRegM(ex_mem_ppr_1_memtoregm), .ReadDataM(RAM_2_d1), .SethM(ex_mem_ppr_1_sethm),
    .ALUResultM(ex_mem_ppr_1_aluresultm), .WA3M(ex_mem_ppr_1_wa3m), .PCSrcW(mem_wb_ppr_1_pcsrcw),
    .RegWriteW(mem_wb_ppr_1_regwritew), .MemToRegW(mem_wb_ppr_1_memtoregw),
    .ReadDataW(mem_wb_ppr_1_readdataw), .SethW(mem_wb_ppr_1_sethw), .ALUResultW(mem_wb_ppr_1_aluresultw),
    .WA3W(mem_wb_ppr_1_wa3w));
  alu alu_2 (
    .A(dp_i_ppr_1_rai), .B(dp_i_ppr_1_rbi), .ALUOP(dp_i_ppr_1_aluopi), .RESULT(alu_2_result),
    .FLAG(alu_2_flag));
  condition_unit condition_unit_2 (
    .FlagWriteE(dp_i_ppr_1_flagwritei), .CondE(dp_i_ppr_1_condi), .FlagsE(dp_i_ppr_1_flagsi),
    .ALUFlags(alu_2_flag), .CondExE(condition_unit_2_condexe));  // open: FlagsM
  Multiplexer #(.Bits(16)) multiplexer_12 (
    .sel(mem_wb_ppr_1_memtoregw), .in_0(mem_wb_ppr_1_aluresultw), .in_1(mem_wb_ppr_1_readdataw),
    .out(multiplexer_12_out));
  and and_5 (and_5_out, dp_i_ppr_1_pcsrci, condition_unit_2_condexe);
  and and_6 (and_6_out, dp_i_ppr_1_branchi, condition_unit_2_condexe);
  // i_wb_ppr i_wb_ppr_1: pin names not known; wires that end beside it: dp_i_ppr_1_dsttagi, dp_i_ppr_1_hei, and_5_out, alu_2_result, i_wb_ppr_1_p5, i_wb_ppr_1_p6, i_wb_ppr_1_p7, i_wb_ppr_1_p8
  // wb_r_ppr wb_r_ppr_1: pin names not known; wires that end beside it: wb_r_ppr_1_p1, wb_r_ppr_1_p2, wb_r_ppr_1_p3, wb_r_ppr_1_p4
  // Pins of 1 and 4 bits meet at rrd_dp_ppr_1_p14[15:12]
  // Pins of 1 and 4 bits meet at 4'b0000

  // Notes on the sheet:
  //   Update is masked into ROB with
  //   an OR with the existing value
  //   0-15: Value
  //   16-18: Dst
  //   19: Rdy
  //   20: Exc
  //   21: Misp
  //   22-37: PC
  //   Stall lines
  //   Hazard Unit
  //   For I-Format insns, we can just 
  //   put the Imm8 as R2 and mark it,
  //   also using 0 for R1 with it marked
  //   0: Valid
  //   1-5: Dst tag
  //   6: Rs1 rdy
  //   7-22: Rs1 tag/value
  //   23: Rs2 rdy
  //   24-39: Rs2 tag/value
  //   40: PC src
  //   41-42: ALUOP
  //   43: Branch
  //   44: Flag write
  //   45: HE
  //   46: Cond
  //   Common Data Bus (CDB)
  //   CDB
endmodule
