// Digital circuit dp_i_ppr.dig as structural Verilog
module dp_i_ppr (
  input  BranchDP,
  input  CLK,
  input  CondDP,
  input  [3:0] FlagsDP,
  input  FlagWriteDP,
  input  [4:0] DstTagDP,
  input  [15:0] RaDP,
  input  [15:0] RbDP,
  input  PCSrcDP,
  input  [1:0] ALUOPDP,
  input  HEDP,
  output BranchI,
  output CondI,
  output [3:0] FlagsI,
  output FlagWriteI,
  output [4:0] DstTagI,
  output [15:0] RaI,
  output [15:0] RbI,
  output PCSrcI,
  output [1:0] ALUOPI,
  output HEI
);

  Register #(.Bits(5)) DstTag (.D(DstTagDP), .C(CLK), .en(1'b1), .Q(DstTagI));
  Register #(.Bits(16)) Ra (.D(RaDP), .C(CLK), .en(1'b1), .Q(RaI));
  Register #(.Bits(16)) Rb (.D(RbDP), .C(CLK), .en(1'b1), .Q(RbI));
  Register PCSrc (.D(PCSrcDP), .C(CLK), .en(1'b1), .Q(PCSrcI));
  Register #(.Bits(2)) ALUOP (.D(ALUOPDP), .C(CLK), .en(1'b1), .Q(ALUOPI));
  Register Branch (.D(BranchDP), .C(CLK), .en(1'b1), .Q(BranchI));
  Register FlagWrite (.D(FlagWriteDP), .C(CLK), .en(1'b1), .Q(FlagWriteI));
  Register HE (.D(HEDP), .C(CLK), .en(1'b1), .Q(HEI));
  Register Cond (.D(CondDP), .C(CLK), .en(1'b1), .Q(CondI));
  Register #(.Bits(4)) Flags (.D(FlagsDP), .C(CLK), .en(1'b1), .Q(FlagsI));

  // Notes on the sheet:
  //   DP/I PPR
endmodule
