// Digital circuit i_wb_ppr.dig as structural Verilog
module i_wb_ppr (
  input  CLK,
  input  PCSrcI,
  input  MemToRegI,
  input  MemWriteI,
  input  [15:0] WriteDataI,
  input  [15:0] ALUResultI,
  input  [4:0] DstTagI,
  input  HEI,
  input  BCWriteI,
  output PCSrcW,
  output MemToRegW,
  output MemWriteW,
  output [15:0] WriteDataW,
  output [15:0] ALUResultW,
  output [4:0] DstTagW,
  output HEW,
  output BCWriteW
);

  Register #(.Bits(5)) DstTag (.D(DstTagI), .C(CLK), .en(1'b1), .Q(DstTagW));
  Register HE (.D(HEI), .C(CLK), .en(1'b1), .Q(HEW));
  Register BCWrite (.D(BCWriteI), .C(CLK), .en(1'b1), .Q(BCWriteW));
  Register PCSrc (.D(PCSrcI), .C(CLK), .en(1'b1), .Q(PCSrcW));
  Register MemToReg (.D(MemToRegI), .C(CLK), .en(1'b1), .Q(MemToRegW));
  Register MemWrite (.D(MemWriteI), .C(CLK), .en(1'b1), .Q(MemWriteW));
  Register #(.Bits(16)) WriteData (.D(WriteDataI), .C(CLK), .en(1'b1), .Q(WriteDataW));
  Register #(.Bits(16)) ALUResult (.D(ALUResultI), .C(CLK), .en(1'b1), .Q(ALUResultW));

  // Notes on the sheet:
  //   I/WB PPR
endmodule
