// Digital circuit ifd_rrd_ppr.dig as structural Verilog
module ifd_rrd_ppr (
  input  [15:0] INSN_IN,
  input  CLK,
  input  [15:0] PC_IN,
  input  EN,
  output [15:0] INSN_OUT,
  output [15:0] PC_OUT
);

  wire [15:0] multiplexer_1_out, multiplexer_2_out;

  Multiplexer #(.Bits(16)) multiplexer_1 (.sel(EN), .in_0(INSN_IN), .in_1({16{1'b0}}), .out(multiplexer_1_out));
  Multiplexer #(.Bits(16)) multiplexer_2 (.sel(EN), .in_0(PC_IN), .in_1({16{1'b0}}), .out(multiplexer_2_out));
  Register #(.Bits(16)) INSN (.D(multiplexer_1_out), .C(CLK), .en(1'b1), .Q(INSN_OUT));
  Register #(.Bits(16)) PC (.D(multiplexer_2_out), .C(CLK), .en(1'b1), .Q(PC_OUT));

  // Notes on the sheet:
  //   IFD/RRD PRR
endmodule
