// Digital circuit issue_queue.dig as structural Verilog
module issue_queue (
  input  CLK,
  input  CLRNext,
  input  Tail_WE,
  input  [46:0] TailData,
  input  [4:0] BC_Tag,
  input  [15:0] BC_Result,
  input  BC_WE,
  output [46:0] NextData,
  output Full,
  output Empty
);

  wire and_1_out, and_2_out, and_3_out, comparator_1_eq, demultiplexer_1_out_0, demultiplexer_1_out_1,
       demultiplexer_1_out_2, demultiplexer_3_out_0, demultiplexer_3_out_1, demultiplexer_3_out_2,
       priorityencoder_1_any;
  wire [1:0] multiplexer_4_out, priorityencoder_1_num, Tail_out;
  wire [46:0] demultiplexer_2_out_0, demultiplexer_2_out_1, demultiplexer_2_out_2,
       iq_update_checker_1_entryvalue_out, iq_update_checker_2_entryvalue_out,
       iq_update_checker_3_entryvalue_out, IQEntry0_tagdst_out, IQEntry1_tagdst_out, IQEntry2_tagdst_out,
       multiplexer_1_out, multiplexer_2_out, multiplexer_3_out;

  Comparator #(.Bits(2)) comparator_1 (.a(Tail_out), .b(2'b10), .eq(comparator_1_eq));  // open: gt, lt
  Counter #(.Bits(2)) Tail (.en(Tail_WE), .C(CLK), .clr(comparator_1_eq), .out(Tail_out));  // open: ovf
  Demultiplexer #(.Selector_Bits(2)) demultiplexer_1 (
    .sel(Tail_out), .in(Tail_WE), .out_0(demultiplexer_1_out_0), .out_1(demultiplexer_1_out_1),
    .out_2(demultiplexer_1_out_2));  // open: out_3
  Demultiplexer #(.Selector_Bits(2), .Bits(47)) demultiplexer_2 (
    .sel(Tail_out), .in(TailData), .out_0(demultiplexer_2_out_0), .out_1(demultiplexer_2_out_1),
    .out_2(demultiplexer_2_out_2));  // open: out_3
  Demultiplexer #(.Selector_Bits(2)) demultiplexer_3 (
    .sel(multiplexer_4_out), .in(CLRNext), .out_0(demultiplexer_3_out_0), .out_1(demultiplexer_3_out_1),
    .out_2(demultiplexer_3_out_2));  // open: out_3
  iq_update_checker iq_update_checker_1 (
    .BC_Result(BC_Result), .BC_Tag(BC_Tag), .BC_EN(BC_WE), .EntryValue_IN(IQEntry0_tagdst_out),
    .EntryValue_OUT(iq_update_checker_1_entryvalue_out));
  iq_update_checker iq_update_checker_2 (
    .BC_Result(BC_Result), .BC_Tag(BC_Tag), .BC_EN(BC_WE), .EntryValue_IN(IQEntry1_tagdst_out),
    .EntryValue_OUT(iq_update_checker_2_entryvalue_out));
  iq_update_checker iq_update_checker_3 (
    .BC_Result(BC_Result), .BC_Tag(BC_Tag), .BC_EN(BC_WE), .EntryValue_IN(IQEntry2_tagdst_out),
    .EntryValue_OUT(iq_update_checker_3_entryvalue_out));
  Multiplexer #(.Bits(47)) multiplexer_1 (
    .sel(demultiplexer_1_out_0), .in_0(iq_update_checker_1_entryvalue_out), .in_1(demultiplexer_2_out_0),
    .out(multiplexer_1_out));
  Multiplexer #(.Bits(47)) multiplexer_2 (
    .sel(demultiplexer_1_out_1), .in_0(iq_update_checker_2_entryvalue_out), .in_1(demultiplexer_2_out_1),
    .out(multiplexer_2_out));
  Multiplexer #(.Bits(47)) multiplexer_3 (
    .sel(demultiplexer_1_out_2), .in_0(iq_update_checker_3_entryvalue_out), .in_1(demultiplexer_2_out_2),
    .out(multiplexer_3_out));
  issue_queue_entry IQEntry0 (
    .V_OUT(IQEntry0_tagdst_out[0]), .TagDst_OUT(IQEntry0_tagdst_out[5:1]),
    .R1Rdy_OUT(IQEntry0_tagdst_out[6]), .R1TagVal_OUT(IQEntry0_tagdst_out[22:7]),
    .R2Rdy_OUT(IQEntry0_tagdst_out[23]), .R2TagVal_OUT(IQEntry0_tagdst_out[39:24]),
    .PCSrc_OUT(IQEntry0_tagdst_out[40]), .ALUOP_OUT(IQEntry0_tagdst_out[42:41]),
    .Branch_OUT(IQEntry0_tagdst_out[43]), .FlagWrite_OUT(IQEntry0_tagdst_out[44]),
    .HE_OUT(IQEntry0_tagdst_out[45]), .Cond_OUT(IQEntry0_tagdst_out[46]), .CLK(CLK),
    .CLR(demultiplexer_3_out_2), .V_IN(multiplexer_1_out[0]), .TagDst_IN(multiplexer_1_out[5:1]),
    .R1Rdy_IN(multiplexer_1_out[6]), .R1TagVal_IN(multiplexer_1_out[22:7]), .R2Rdy_IN(multiplexer_1_out[23]),
    .R2TagVal_IN(multiplexer_1_out[39:24]), .PCSrc_IN(multiplexer_1_out[40]),
    .ALUOP_IN(multiplexer_1_out[42:41]), .Branch_IN(multiplexer_1_out[43]),
    .FlagWrite_IN(multiplexer_1_out[44]), .HE_IN(multiplexer_1_out[45]), .Cond_IN(multiplexer_1_out[46]));
  issue_queue_entry IQEntry1 (
    .V_OUT(IQEntry1_tagdst_out[0]), .TagDst_OUT(IQEntry1_tagdst_out[5:1]),
    .R1Rdy_OUT(IQEntry1_tagdst_out[6]), .R1TagVal_OUT(IQEntry1_tagdst_out[22:7]),
    .R2Rdy_OUT(IQEntry1_tagdst_out[23]), .R2TagVal_OUT(IQEntry1_tagdst_out[39:24]),
    .PCSrc_OUT(IQEntry1_tagdst_out[40]), .ALUOP_OUT(IQEntry1_tagdst_out[42:41]),
    .Branch_OUT(IQEntry1_tagdst_out[43]), .FlagWrite_OUT(IQEntry1_tagdst_out[44]),
    .HE_OUT(IQEntry1_tagdst_out[45]), .Cond_OUT(IQEntry1_tagdst_out[46]), .CLK(CLK),
    .CLR(demultiplexer_3_out_1), .V_IN(multiplexer_2_out[0]), .TagDst_IN(multiplexer_2_out[5:1]),
    .R1Rdy_IN(multiplexer_2_out[6]), .R1TagVal_IN(multiplexer_2_out[22:7]), .R2Rdy_IN(multiplexer_2_out[23]),
    .R2TagVal_IN(multiplexer_2_out[39:24]), .PCSrc_IN(multiplexer_2_out[40]),
    .ALUOP_IN(multiplexer_2_out[42:41]), .Branch_IN(multiplexer_2_out[43]),
    .FlagWrite_IN(multiplexer_2_out[44]), .HE_IN(multiplexer_2_out[45]), .Cond_IN(multiplexer_2_out[46]));
  issue_queue_entry IQEntry2 (
    .V_OUT(IQEntry2_tagdst_out[0]), .TagDst_OUT(IQEntry2_tagdst_out[5:1]),
    .R1Rdy_OUT(IQEntry2_tagdst_out[6]), .R1TagVal_OUT(IQEntry2_tagdst_out[22:7]),
    .R2Rdy_OUT(IQEntry2_tagdst_out[23]), .R2TagVal_OUT(IQEntry2_tagdst_out[39:24]),
    .PCSrc_OUT(IQEntry2_tagdst_out[40]), .ALUOP_OUT(IQEntry2_tagdst_out[42:41]),
    .Branch_OUT(IQEntry2_tagdst_out[43]), .FlagWrite_OUT(IQEntry2_tagdst_out[44]),
    .HE_OUT(IQEntry2_tagdst_out[45]), .Cond_OUT(IQEntry2_tagdst_out[46]), .CLK(CLK),
    .CLR(demultiplexer_3_out_0), .V_IN(multiplexer_3_out[0]), .TagDst_IN(multiplexer_3_out[5:1]),
    .R1Rdy_IN(multiplexer_3_out[6]), .R1TagVal_IN(multiplexer_3_out[22:7]), .R2Rdy_IN(multiplexer_3_out[23]),
    .R2TagVal_IN(multiplexer_3_out[39:24]), .PCSrc_IN(multiplexer_3_out[40]),
    .ALUOP_IN(multiplexer_3_out[42:41]), .Branch_IN(multiplexer_3_out[43]),
    .FlagWrite_IN(multiplexer_3_out[44]), .HE_IN(multiplexer_3_out[45]), .Cond_IN(multiplexer_3_out[46]));
  and and_1 (and_1_out, IQEntry0_tagdst_out[0], IQEntry0_tagdst_out[6], IQEntry0_tagdst_out[23]);
  and and_2 (and_2_out, IQEntry1_tagdst_out[0], IQEntry1_tagdst_out[6], IQEntry1_tagdst_out[23]);
  and and_3 (and_3_out, IQEntry2_tagdst_out[0], IQEntry2_tagdst_out[6], IQEntry2_tagdst_out[23]);
  PriorityEncoder #(.Selector_Bits(2)) priorityencoder_1 (
    .in0(and_3_out), .in1(and_2_out), .in2(and_1_out), .in3(1'b0), .num(priorityencoder_1_num),
    .any(priorityencoder_1_any));
  Multiplexer #(.Bits(2)) multiplexer_4 (
    .sel(priorityencoder_1_any), .in_0(2'b11), .in_1(priorityencoder_1_num), .out(multiplexer_4_out));
  Multiplexer #(.Selector_Bits(2), .Bits(47)) multiplexer_5 (
    .sel(multiplexer_4_out), .in_0(IQEntry2_tagdst_out), .in_1(IQEntry1_tagdst_out),
    .in_2(IQEntry0_tagdst_out), .in_3({47{1'b0}}), .out(NextData));
  and and_4 (Full, IQEntry0_tagdst_out[0], IQEntry1_tagdst_out[0], IQEntry2_tagdst_out[0]);
  nor nor_1 (Empty, IQEntry0_tagdst_out[0], IQEntry1_tagdst_out[0], IQEntry2_tagdst_out[0]);

  // Notes on the sheet:
  //   Issue Queue (IQ)
endmodule
