// Digital circuit issue_queue_entry.dig as structural Verilog
module issue_queue_entry (
  input  CLK,
  input  V_IN,
  input  [4:0] TagDst_IN,
  input  R1Rdy_IN,
  input  [15:0] R1TagVal_IN,
  input  R2Rdy_IN,
  input  [15:0] R2TagVal_IN,
  input  CLR,
  input  PCSrc_IN,
  input  [1:0] ALUOP_IN,
  input  Branch_IN,
  input  FlagWrite_IN,
  input  HE_IN,
  input  Cond_IN,
  output V_OUT,
  output [4:0] TagDst_OUT,
  output R1Rdy_OUT,
  output [15:0] R1TagVal_OUT,
  output R2Rdy_OUT,
  output [15:0] R2TagVal_OUT,
  output PCSrc_OUT,
  output [1:0] ALUOP_OUT,
  output Branch_OUT,
  output FlagWrite_OUT,
  output HE_OUT,
  output Cond_OUT
);

  wire multiplexer_1_out, multiplexer_3_out, multiplexer_5_out, multiplexer_7_out, multiplexer_9_out,
       multiplexer_10_out, multiplexer_11_out, multiplexer_12_out;
  wire [1:0] multiplexer_8_out;
  wire [4:0] multiplexer_2_out;
  wire [15:0] multiplexer_4_out, multiplexer_6_out;

  Multiplexer multiplexer_1 (.sel(CLR), .in_0(V_IN), .in_1(1'b0), .out(multiplexer_1_out));
  Multiplexer #(.Bits(5)) multiplexer_2 (.sel(CLR), .in_0(TagDst_IN), .in_1({5{1'b0}}), .out(multiplexer_2_out));
  Multiplexer multiplexer_3 (.sel(CLR), .in_0(R1Rdy_IN), .in_1(1'b0), .out(multiplexer_3_out));
  Multiplexer #(.Bits(16)) multiplexer_4 (.sel(CLR), .in_0(R1TagVal_IN), .in_1({16{1'b0}}), .out(multiplexer_4_out));
  Multiplexer multiplexer_5 (.sel(CLR), .in_0(R2Rdy_IN), .in_1(1'b0), .out(multiplexer_5_out));
  Multiplexer #(.Bits(16)) multiplexer_6 (.sel(CLR), .in_0(R2TagVal_IN), .in_1({16{1'b0}}), .out(multiplexer_6_out));
  Multiplexer multiplexer_7 (.sel(CLR), .in_0(PCSrc_IN), .in_1(1'b0), .out(multiplexer_7_out));
  Multiplexer #(.Bits(2)) multiplexer_8 (.sel(CLR), .in_0(ALUOP_IN), .in_1(2'b00), .out(multiplexer_8_out));
  Multiplexer multiplexer_9 (.sel(CLR), .in_0(Branch_IN), .in_1(1'b0), .out(multiplexer_9_out));
  Multiplexer multiplexer_10 (.sel(CLR), .in_0(FlagWrite_IN), .in_1(1'b0), .out(multiplexer_10_out));
  Multiplexer multiplexer_11 (.sel(CLR), .in_0(HE_IN), .in_1(1'b0), .out(multiplexer_11_out));
  Multiplexer multiplexer_12 (.sel(CLR), .in_0(Cond_IN), .in_1(1'b0), .out(multiplexer_12_out));
  Register V (.D(multiplexer_1_out), .C(CLK), .en(1'b1), .Q(V_OUT));
  Register #(.Bits(5)) TagDst (.D(multiplexer_2_out), .C(CLK), .en(1'b1), .Q(TagDst_OUT));
  Register R1Rdy (.D(multiplexer_3_out), .C(CLK), .en(1'b1), .Q(R1Rdy_OUT));
  Register #(.Bits(16)) R1TagVal (.D(multiplexer_4_out), .C(CLK), .en(1'b1), .Q(R1TagVal_OUT));
  Register R2Rdy (.D(multiplexer_5_out), .C(CLK), .en(1'b1), .Q(R2Rdy_OUT));
  Register #(.Bits(16)) R2TagVal (.D(multiplexer_6_out), .C(CLK), .en(1'b1), .Q(R2TagVal_OUT));
  Register PCSrc (.D(multiplexer_7_out), .C(CLK), .en(1'b1), .Q(PCSrc_OUT));
  Register #(.Bits(2)) ALUOP (.D(multiplexer_8_out), .C(CLK), .en(1'b1), .Q(ALUOP_OUT));
  Register Branch (.D(multiplexer_9_out), .C(CLK), .en(1'b1), .Q(Branch_OUT));
  Register FlagWrite (.D(multiplexer_10_out), .C(CLK), .en(1'b1), .Q(FlagWrite_OUT));
  Register HE (.D(multiplexer_11_out), .C(CLK), .en(1'b1), .Q(HE_OUT));
  Register Cond (.D(multiplexer_12_out), .C(CLK), .en(1'b1), .Q(Cond_OUT));
endmodule
