// Digital circuit rename_map_table.dig as structural Verilog
module rename_map_table (
  input  [2:0] WS,
  input  CLK,
  input  V_IN,
  input  [4:0] ROBTag_IN,
  input  [2:0] RS1,
  input  [2:0] RS2,
  input  [2:0] UpdateDst,
  input  [4:0] UpdateTag,
  output R1V_OUT,
  output [4:0] R1ROBTag_OUT,
  output R2V_OUT,
  output [4:0] R2ROBTag_OUT
);

  wire decoder_1_out_0, decoder_1_out_1, decoder_1_out_2, decoder_1_out_3, decoder_1_out_4, decoder_1_out_5,
       decoder_1_out_7, demultiplexer_1_out_0, demultiplexer_1_out_1, demultiplexer_1_out_2,
       demultiplexer_1_out_3, demultiplexer_1_out_4, demultiplexer_1_out_5, demultiplexer_1_out_7,
       demultiplexer_5_out_0, demultiplexer_5_out_1, demultiplexer_5_out_2, demultiplexer_5_out_3,
       demultiplexer_5_out_4, demultiplexer_5_out_5, demultiplexer_5_out_7, demultiplexer_6_out_0,
       demultiplexer_6_out_1, demultiplexer_6_out_2, demultiplexer_6_out_3, demultiplexer_6_out_4,
       demultiplexer_6_out_5, demultiplexer_6_out_7, demultiplexer_7_out_0, demultiplexer_7_out_1,
       demultiplexer_7_out_2, demultiplexer_7_out_3, demultiplexer_7_out_4, demultiplexer_7_out_5,
       demultiplexer_7_out_7, multiplexer_1_out, R0_V_q, R1_V_q, R2_V_q, R3_V_q, R4_V_q, R5_V_q, R7_V_q,
       rmt_condition_write_1_v_out, rmt_condition_write_2_v_out, rmt_condition_write_3_v_out,
       rmt_condition_write_4_v_out, rmt_condition_write_5_v_out, rmt_condition_write_6_v_out,
       rmt_condition_write_7_v_out;
  wire [4:0] demultiplexer_2_out_0, demultiplexer_2_out_1, demultiplexer_2_out_2, demultiplexer_2_out_3,
       demultiplexer_2_out_4, demultiplexer_2_out_5, demultiplexer_2_out_7, demultiplexer_3_out_0,
       demultiplexer_3_out_1, demultiplexer_3_out_2, demultiplexer_3_out_3, demultiplexer_3_out_4,
       demultiplexer_3_out_5, demultiplexer_3_out_7, demultiplexer_4_out_0, demultiplexer_4_out_1,
       demultiplexer_4_out_2, demultiplexer_4_out_3, demultiplexer_4_out_4, demultiplexer_4_out_5,
       demultiplexer_4_out_7, multiplexer_2_out, R0_Tag_q, R1_Tag_q, R2_Tag_q, R3_Tag_q, R4_Tag_q, R5_Tag_q,
       R7_Tag_q, rmt_condition_write_1_data, rmt_condition_write_2_data, rmt_condition_write_3_data,
       rmt_condition_write_4_data, rmt_condition_write_5_data, rmt_condition_write_6_data,
       rmt_condition_write_7_data;

  Demultiplexer #(.Selector_Bits(3)) demultiplexer_1 (
    .sel(UpdateDst), .in(multiplexer_1_out), .out_0(demultiplexer_1_out_0), .out_1(demultiplexer_1_out_1),
    .out_2(demultiplexer_1_out_2), .out_3(demultiplexer_1_out_3), .out_4(demultiplexer_1_out_4),
    .out_5(demultiplexer_1_out_5), .out_7(demultiplexer_1_out_7));  // open: out_6
  Demultiplexer #(.Selector_Bits(3), .Bits(5)) demultiplexer_2 (
    .sel(UpdateDst), .in(multiplexer_2_out), .out_0(demultiplexer_2_out_0), .out_1(demultiplexer_2_out_1),
    .out_2(demultiplexer_2_out_2), .out_3(demultiplexer_2_out_3), .out_4(demultiplexer_2_out_4),
    .out_5(demultiplexer_2_out_5), .out_7(demultiplexer_2_out_7));  // open: out_6
  Demultiplexer #(.Selector_Bits(3), .Bits(5)) demultiplexer_3 (
    .sel(UpdateDst), .in(UpdateTag), .out_0(demultiplexer_3_out_0), .out_1(demultiplexer_3_out_1),
    .out_2(demultiplexer_3_out_2), .out_3(demultiplexer_3_out_3), .out_4(demultiplexer_3_out_4),
    .out_5(demultiplexer_3_out_5), .out_7(demultiplexer_3_out_7));  // open: out_6
  Demultiplexer #(.Selector_Bits(3), .Bits(5)) demultiplexer_4 (
    .sel(WS), .in(ROBTag_IN), .out_0(demultiplexer_4_out_0), .out_1(demultiplexer_4_out_1),
    .out_2(demultiplexer_4_out_2), .out_3(demultiplexer_4_out_3), .out_4(demultiplexer_4_out_4),
    .out_5(demultiplexer_4_out_5), .out_7(demultiplexer_4_out_7));  // open: out_6
  Demultiplexer #(.Selector_Bits(3)) demultiplexer_5 (
    .sel(WS), .in(V_IN), .out_0(demultiplexer_5_out_0), .out_1(demultiplexer_5_out_1),
    .out_2(demultiplexer_5_out_2), .out_3(demultiplexer_5_out_3), .out_4(demultiplexer_5_out_4),
    .out_5(demultiplexer_5_out_5), .out_7(demultiplexer_5_out_7));  // open: out_6
  Decoder #(.Selector_Bits(3)) decoder_1 (
    .sel(WS), .out_0(decoder_1_out_0), .out_1(decoder_1_out_1), .out_2(decoder_1_out_2),
    .out_3(decoder_1_out_3), .out_4(decoder_1_out_4), .out_5(decoder_1_out_5), .out_7(decoder_1_out_7));  // open: out_6
  rmt_condition_write rmt_condition_write_1 (
    .WS(decoder_1_out_0), .ROBTag_IN(demultiplexer_4_out_0), .V_IN(demultiplexer_5_out_0),
    .UpdateTag(demultiplexer_3_out_0), .CurrentTag(demultiplexer_2_out_0), .Update(demultiplexer_1_out_0),
    .V_OUT(rmt_condition_write_1_v_out), .Data(rmt_condition_write_1_data));
  rmt_condition_write rmt_condition_write_2 (
    .WS(decoder_1_out_1), .ROBTag_IN(demultiplexer_4_out_1), .V_IN(demultiplexer_5_out_1),
    .UpdateTag(demultiplexer_3_out_1), .CurrentTag(demultiplexer_2_out_1), .Update(demultiplexer_1_out_1),
    .V_OUT(rmt_condition_write_2_v_out), .Data(rmt_condition_write_2_data));
  rmt_condition_write rmt_condition_write_3 (
    .WS(decoder_1_out_2), .ROBTag_IN(demultiplexer_4_out_2), .V_IN(demultiplexer_5_out_2),
    .UpdateTag(demultiplexer_3_out_2), .CurrentTag(demultiplexer_2_out_2), .Update(demultiplexer_1_out_2),
    .V_OUT(rmt_condition_write_3_v_out), .Data(rmt_condition_write_3_data));
  rmt_condition_write rmt_condition_write_4 (
    .WS(decoder_1_out_3), .ROBTag_IN(demultiplexer_4_out_3), .V_IN(demultiplexer_5_out_3),
    .UpdateTag(demultiplexer_3_out_3), .CurrentTag(demultiplexer_2_out_3), .Update(demultiplexer_1_out_3),
    .V_OUT(rmt_condition_write_4_v_out), .Data(rmt_condition_write_4_data));
  rmt_condition_write rmt_condition_write_5 (
    .WS(decoder_1_out_4), .ROBTag_IN(demultiplexer_4_out_4), .V_IN(demultiplexer_5_out_4),
    .UpdateTag(demultiplexer_3_out_4), .CurrentTag(demultiplexer_2_out_4), .Update(demultiplexer_1_out_4),
    .V_OUT(rmt_condition_write_5_v_out), .Data(rmt_condition_write_5_data));
  rmt_condition_write rmt_condition_write_6 (
    .WS(decoder_1_out_5), .ROBTag_IN(demultiplexer_4_out_5), .V_IN(demultiplexer_5_out_5),
    .UpdateTag(demultiplexer_3_out_5), .CurrentTag(demultiplexer_2_out_5), .Update(demultiplexer_1_out_5),
    .V_OUT(rmt_condition_write_6_v_out), .Data(rmt_condition_write_6_data));
  rmt_condition_write rmt_condition_write_7 (
    .WS(decoder_1_out_7), .ROBTag_IN(demultiplexer_4_out_7), .V_IN(demultiplexer_5_out_7),
    .UpdateTag(demultiplexer_3_out_7), .CurrentTag(demultiplexer_2_out_7), .Update(demultiplexer_1_out_7),
    .V_OUT(rmt_condition_write_7_v_out), .Data(rmt_condition_write_7_data));
  Demultiplexer #(.Selector_Bits(3)) demultiplexer_6 (
    .sel(WS), .in(CLK), .out_0(demultiplexer_6_out_0), .out_1(demultiplexer_6_out_1),
    .out_2(demultiplexer_6_out_2), .out_3(demultiplexer_6_out_3), .out_4(demultiplexer_6_out_4),
    .out_5(demultiplexer_6_out_5), .out_7(demultiplexer_6_out_7));  // open: out_6
  Demultiplexer #(.Selector_Bits(3)) demultiplexer_7 (
    .sel(WS), .in(CLK), .out_0(demultiplexer_7_out_0), .out_1(demultiplexer_7_out_1),
    .out_2(demultiplexer_7_out_2), .out_3(demultiplexer_7_out_3), .out_4(demultiplexer_7_out_4),
    .out_5(demultiplexer_7_out_5), .out_7(demultiplexer_7_out_7));  // open: out_6
  Register R0_V (.D(rmt_condition_write_1_v_out), .C(demultiplexer_7_out_0), .en(1'b1), .Q(R0_V_q));
  Register #(.Bits(5)) R0_Tag (.D(rmt_condition_write_1_data), .C(demultiplexer_6_out_0), .en(1'b1), .Q(R0_Tag_q));
  Register R1_V (.D(rmt_condition_write_2_v_out), .C(demultiplexer_7_out_1), .en(1'b1), .Q(R1_V_q));
  Register #(.Bits(5)) R1_Tag (.D(rmt_condition_write_2_data), .C(demultiplexer_6_out_1), .en(1'b1), .Q(R1_Tag_q));
  Register R2_V (.D(rmt_condition_write_3_v_out), .C(demultiplexer_7_out_2), .en(1'b1), .Q(R2_V_q));
  Register #(.Bits(5)) R2_Tag (.D(rmt_condition_write_3_data), .C(demultiplexer_6_out_2), .en(1'b1), .Q(R2_Tag_q));
  Register R3_V (.D(rmt_condition_write_4_v_out), .C(demultiplexer_7_out_3), .en(1'b1), .Q(R3_V_q));
  Register #(.Bits(5)) R3_Tag (.D(rmt_condition_write_4_data), .C(demultiplexer_6_out_3), .en(1'b1), .Q(R3_Tag_q));
  Register R4_V (.D(rmt_condition_write_5_v_out), .C(demultiplexer_7_out_4), .en(1'b1), .Q(R4_V_q));
  Register #(.Bits(5)) R4_Tag (.D(rmt_condition_write_5_data), .C(demultiplexer_6_out_4), .en(1'b1), .Q(R4_Tag_q));
  Register R5_V (.D(rmt_condition_write_6_v_out), .C(demultiplexer_7_out_5), .en(1'b1), .Q(R5_V_q));
  Register #(.Bits(5)) R5_Tag (.D(rmt_condition_write_6_data), .C(demultiplexer_6_out_5), .en(1'b1), .Q(R5_Tag_q));
  Register R7_V (.D(rmt_condition_write_7_v_out), .C(demultiplexer_7_out_7), .en(1'b1), .Q(R7_V_q));
  Register #(.Bits(5)) R7_Tag (.D(rmt_condition_write_7_data), .C(demultiplexer_6_out_7), .en(1'b1), .Q(R7_Tag_q));
  Multiplexer #(.Selector_Bits(3)) multiplexer_1 (
    .sel(UpdateDst), .in_0(R0_V_q), .in_1(R1_V_q), .in_2(R2_V_q), .in_3(R3_V_q), .in_4(R4_V_q),
    .in_5(R5_V_q), .in_6(1'b0), .in_7(R7_V_q), .out(multiplexer_1_out));
  Multiplexer #(.Selector_Bits(3), .Bits(5)) multiplexer_2 (
    .sel(UpdateDst), .in_0(R0_Tag_q), .in_1(R1_Tag_q), .in_2(R2_Tag_q), .in_3(R3_Tag_q), .in_4(R4_Tag_q),
    .in_5(R5_Tag_q), .in_6({5{1'b0}}), .in_7(R7_Tag_q), .out(multiplexer_2_out));
  Multiplexer #(.Selector_Bits(3)) multiplexer_3 (
    .sel(RS1), .in_0(R0_V_q), .in_1(R1_V_q), .in_2(R2_V_q), .in_3(R3_V_q), .in_4(R4_V_q), .in_5(R5_V_q),
    .in_6(1'b0), .in_7(R7_V_q), .out(R1V_OUT));
  Multiplexer #(.Selector_Bits(3), .Bits(5)) multiplexer_4 (
    .sel(RS1), .in_0(R0_Tag_q), .in_1(R1_Tag_q), .in_2(R2_Tag_q), .in_3(R3_Tag_q), .in_4(R4_Tag_q),
    .in_5(R5_Tag_q), .in_6({5{1'b0}}), .in_7(R7_Tag_q), .out(R1ROBTag_OUT));
  Multiplexer #(.Selector_Bits(3)) multiplexer_5 (
    .sel(RS2), .in_0(R0_V_q), .in_1(R1_V_q), .in_2(R2_V_q), .in_3(R3_V_q), .in_4(R4_V_q), .in_5(R5_V_q),
    .in_6(1'b0), .in_7(R7_V_q), .out(R2V_OUT));
  Multiplexer #(.Selector_Bits(3), .Bits(5)) multiplexer_6 (
    .sel(RS2), .in_0(R0_Tag_q), .in_1(R1_Tag_q), .in_2(R2_Tag_q), .in_3(R3_Tag_q), .in_4(R4_Tag_q),
    .in_5(R5_Tag_q), .in_6({5{1'b0}}), .in_7(R7_Tag_q), .out(R2ROBTag_OUT));

  // Notes on the sheet:
  //   Rename Map Table (RMT)
  //   Rework this to multiplex the CLK
  //   line on each register based on OR
  //   between WS and all indexes of
  //   registers that have matching tag 
  //   values to RESET_TAG input
endmodule
