// Digital circuit rrd_dp_ppr.dig as structural Verilog
module rrd_dp_ppr (
  input  CLK,
  input  R1V_IN,
  input  R2V_IN,
  input  [15:0] Ra_Tag1_IN,
  input  [15:0] Rb_Tag2_IN,
  input  [2:0] TagDst_IN,
  input  [15:0] INSN_IN,
  input  EN,
  output R1V_OUT,
  output R2V_OUT,
  output [15:0] Ra_Tag1_OUT,
  output [15:0] Rb_Tag2_OUT,
  output [2:0] TagDst_OUT,
  output [15:0] INSN_OUT
);

  Register R1V (.D(R1V_IN), .C(CLK), .en(EN), .Q(R1V_OUT));
  Register R2V (.D(R2V_IN), .C(CLK), .en(EN), .Q(R2V_OUT));
  Register #(.Bits(16)) Ra_Tag1 (.D(Ra_Tag1_IN), .C(CLK), .en(EN), .Q(Ra_Tag1_OUT));
  Register #(.Bits(16)) Rb_Tag2 (.D(Rb_Tag2_IN), .C(CLK), .en(EN), .Q(Rb_Tag2_OUT));
  Register #(.Bits(3)) TagDst (.D(TagDst_IN), .C(CLK), .en(EN), .Q(TagDst_OUT));
  Register #(.Bits(16)) INSN (.D(INSN_IN), .C(CLK), .en(EN), .Q(INSN_OUT));

  // Notes on the sheet:
  //   RRD/DP PPR
endmodule
