// Digital circuit wb_r_ppr.dig as structural Verilog
module wb_r_ppr (
  input  DstTagW,
  input  CLK,
  input  [15:0] ALUResultW,
  input  BCWriteW,
  input  HEW,
  output DstTagR,
  output [15:0] ALUResultR,
  output BCWriteR,
  output HER
);

  Register DstTag (.D(DstTagW), .C(CLK), .en(1'b1), .Q(DstTagR));
  Register #(.Bits(16)) ALUResult (.D(ALUResultW), .C(CLK), .en(1'b1), .Q(ALUResultR));
  Register BCWrite (.D(BCWriteW), .C(CLK), .en(1'b1), .Q(BCWriteR));
  Register HE (.D(HEW), .C(CLK), .en(1'b1), .Q(HER));

  // Notes on the sheet:
  //   WB/R PPR
endmodule
