// Digital circuit circular_buffer.dig as structural Verilog
module circular_buffer (
  input  TailWE,
  input  [42:0] TailData,
  input  HeadRE,
  input  UpdateWE_IRALU,
  input  [42:0] UpdateData_IRALU,
  input  [4:0] UpdateA_IRALU,
  input  CLK,
  input  CLR,
  input  [42:0] UpdateData_RMEM,
  input  UpdateWE_RMEM,
  input  [4:0] UpdateA_RMEM,
  output [42:0] HeadData,
  output [4:0] TailIdx,
  output [4:0] HeadIdx
);

  wire demultiplexer_1_out_0, demultiplexer_1_out_1, demultiplexer_1_out_2, demultiplexer_1_out_3,
       demultiplexer_1_out_4, demultiplexer_1_out_5, demultiplexer_1_out_6, demultiplexer_1_out_7,
       demultiplexer_1_out_8, demultiplexer_1_out_9, demultiplexer_1_out_10, demultiplexer_1_out_11,
       demultiplexer_1_out_12, demultiplexer_1_out_13, demultiplexer_1_out_14, demultiplexer_1_out_15,
       demultiplexer_1_out_16, demultiplexer_1_out_17, demultiplexer_1_out_18, demultiplexer_1_out_19,
       demultiplexer_1_out_20, demultiplexer_1_out_21, demultiplexer_1_out_22, demultiplexer_1_out_23,
       demultiplexer_1_out_24, demultiplexer_1_out_25, demultiplexer_1_out_26, demultiplexer_1_out_27,
       demultiplexer_1_out_28, demultiplexer_1_out_29, demultiplexer_1_out_30, demultiplexer_1_out_31,
       demultiplexer_3_out_0, demultiplexer_3_out_1, demultiplexer_3_out_2, demultiplexer_3_out_3,
       demultiplexer_3_out_4, demultiplexer_3_out_5, demultiplexer_3_out_6, demultiplexer_3_out_7,
       demultiplexer_3_out_8, demultiplexer_3_out_9, demultiplexer_3_out_10, demultiplexer_3_out_11,
       demultiplexer_3_out_12, demultiplexer_3_out_13, demultiplexer_3_out_14, demultiplexer_3_out_15,
       demultiplexer_3_out_16, demultiplexer_3_out_17, demultiplexer_3_out_18, demultiplexer_3_out_19,
       demultiplexer_3_out_20, demultiplexer_3_out_21, demultiplexer_3_out_22, demultiplexer_3_out_23,
       demultiplexer_3_out_24, demultiplexer_3_out_25, demultiplexer_3_out_26, demultiplexer_3_out_27,
       demultiplexer_3_out_28, demultiplexer_3_out_29, demultiplexer_3_out_30, demultiplexer_3_out_31,
       demultiplexer_4_out_0, demultiplexer_4_out_1, demultiplexer_4_out_2, demultiplexer_4_out_3,
       demultiplexer_4_out_4, demultiplexer_4_out_5, demultiplexer_4_out_6, demultiplexer_4_out_7,
       demultiplexer_4_out_8, demultiplexer_4_out_9, demultiplexer_4_out_10, demultiplexer_4_out_11,
       demultiplexer_4_out_12, demultiplexer_4_out_13, demultiplexer_4_out_14, demultiplexer_4_out_15,
       demultiplexer_4_out_16, demultiplexer_4_out_17, demultiplexer_4_out_18, demultiplexer_4_out_19,
       demultiplexer_4_out_20, demultiplexer_4_out_21, demultiplexer_4_out_22, demultiplexer_4_out_23,
       demultiplexer_4_out_24, demultiplexer_4_out_25, demultiplexer_4_out_26, demultiplexer_4_out_27,
       demultiplexer_4_out_28, demultiplexer_4_out_29, demultiplexer_4_out_30, demultiplexer_4_out_31,
       or_1_out, or_2_out, or_4_out, or_6_out, or_8_out, or_10_out, or_12_out, or_14_out, or_16_out,
       or_18_out, or_20_out, or_22_out, or_24_out, or_26_out, or_28_out, or_30_out, or_32_out, or_34_out,
       or_36_out, or_38_out, or_40_out, or_42_out, or_44_out, or_46_out, or_48_out, or_50_out, or_52_out,
       or_54_out, or_56_out, or_58_out, or_60_out, or_62_out, or_64_out, or_66_out;
  wire [42:0] demultiplexer_2_out_0, demultiplexer_2_out_1, demultiplexer_2_out_2, demultiplexer_2_out_3,
       demultiplexer_2_out_4, demultiplexer_2_out_5, demultiplexer_2_out_6, demultiplexer_2_out_7,
       demultiplexer_2_out_8, demultiplexer_2_out_9, demultiplexer_2_out_10, demultiplexer_2_out_11,
       demultiplexer_2_out_12, demultiplexer_2_out_13, demultiplexer_2_out_14, demultiplexer_2_out_15,
       demultiplexer_2_out_16, demultiplexer_2_out_17, demultiplexer_2_out_18, demultiplexer_2_out_19,
       demultiplexer_2_out_20, demultiplexer_2_out_21, demultiplexer_2_out_22, demultiplexer_2_out_23,
       demultiplexer_2_out_24, demultiplexer_2_out_25, demultiplexer_2_out_26, demultiplexer_2_out_27,
       demultiplexer_2_out_28, demultiplexer_2_out_29, demultiplexer_2_out_30, demultiplexer_2_out_31,
       demultiplexer_5_out_0, demultiplexer_5_out_1, demultiplexer_5_out_2, demultiplexer_5_out_3,
       demultiplexer_5_out_4, demultiplexer_5_out_5, demultiplexer_5_out_6, demultiplexer_5_out_7,
       demultiplexer_5_out_8, demultiplexer_5_out_9, demultiplexer_5_out_10, demultiplexer_5_out_11,
       demultiplexer_5_out_12, demultiplexer_5_out_13, demultiplexer_5_out_14, demultiplexer_5_out_15,
       demultiplexer_5_out_16, demultiplexer_5_out_17, demultiplexer_5_out_18, demultiplexer_5_out_19,
       demultiplexer_5_out_20, demultiplexer_5_out_21, demultiplexer_5_out_22, demultiplexer_5_out_23,
       demultiplexer_5_out_24, demultiplexer_5_out_25, demultiplexer_5_out_26, demultiplexer_5_out_27,
       demultiplexer_5_out_28, demultiplexer_5_out_29, demultiplexer_5_out_30, demultiplexer_5_out_31,
       demultiplexer_6_out_0, demultiplexer_6_out_1, demultiplexer_6_out_2, demultiplexer_6_out_3,
       demultiplexer_6_out_4, demultiplexer_6_out_5, demultiplexer_6_out_6, demultiplexer_6_out_7,
       demultiplexer_6_out_8, demultiplexer_6_out_9, demultiplexer_6_out_10, demultiplexer_6_out_11,
       demultiplexer_6_out_12, demultiplexer_6_out_13, demultiplexer_6_out_14, demultiplexer_6_out_15,
       demultiplexer_6_out_16, demultiplexer_6_out_17, demultiplexer_6_out_18, demultiplexer_6_out_19,
       demultiplexer_6_out_20, demultiplexer_6_out_21, demultiplexer_6_out_22, demultiplexer_6_out_23,
       demultiplexer_6_out_24, demultiplexer_6_out_25, demultiplexer_6_out_26, demultiplexer_6_out_27,
       demultiplexer_6_out_28, demultiplexer_6_out_29, demultiplexer_6_out_30, demultiplexer_6_out_31,
       driver_1_out, driver_2_out, multiplexer_1_out, multiplexer_2_out, multiplexer_3_out,
       multiplexer_4_out, multiplexer_5_out, multiplexer_6_out, multiplexer_7_out, multiplexer_8_out,
       multiplexer_9_out, multiplexer_10_out, multiplexer_11_out, multiplexer_12_out, multiplexer_13_out,
       multiplexer_14_out, multiplexer_15_out, multiplexer_16_out, multiplexer_17_out, multiplexer_18_out,
       multiplexer_19_out, multiplexer_20_out, multiplexer_21_out, multiplexer_22_out, multiplexer_23_out,
       multiplexer_24_out, multiplexer_25_out, multiplexer_26_out, multiplexer_27_out, multiplexer_28_out,
       multiplexer_29_out, multiplexer_30_out, multiplexer_31_out, multiplexer_32_out, multiplexer_33_out,
       multiplexer_34_out, or_3_out, or_5_out, or_7_out, or_9_out, or_11_out, or_13_out, or_15_out,
       or_17_out, or_19_out, or_21_out, or_23_out, or_25_out, or_27_out, or_29_out, or_31_out, or_33_out,
       or_35_out, or_37_out, or_39_out, or_41_out, or_43_out, or_45_out, or_47_out, or_49_out, or_51_out,
       or_53_out, or_55_out, or_57_out, or_59_out, or_61_out, or_63_out, or_65_out, ROB_0_q, ROB_1_q,
       ROB_2_q, ROB_3_q, ROB_4_q, ROB_5_q, ROB_6_q, ROB_7_q, ROB_8_q, ROB_9_q, ROB_10_q, ROB_11_q, ROB_12_q,
       ROB_13_q, ROB_14_q, ROB_15_q, ROB_16_q, ROB_17_q, ROB_18_q, ROB_19_q, ROB_20_q, ROB_21_q, ROB_22_q,
       ROB_23_q, ROB_24_q, ROB_25_q, ROB_26_q, ROB_27_q, ROB_28_q, ROB_29_q, ROB_30_q, ROB_31_q,
       rob_update_mask_1_entry, rob_update_mask_2_entry;

  or or_1 (or_1_out, TailWE, CLR);
  or or_2 (or_2_out, CLR, HeadRE);
  Counter #(.Bits(5)) Write_Index__TailA (.en(or_1_out), .C(CLK), .clr(CLR), .out(TailIdx));  // open: ovf
  Counter #(.Bits(5)) Read_Index__HeadA (.en(or_2_out), .C(CLK), .clr(CLR), .out(HeadIdx));  // open: ovf
  Demultiplexer #(.Selector_Bits(5)) demultiplexer_1 (
    .sel(UpdateA_RMEM), .in(UpdateWE_RMEM), .out_0(demultiplexer_1_out_0), .out_1(demultiplexer_1_out_1),
    .out_2(demultiplexer_1_out_2), .out_3(demultiplexer_1_out_3), .out_4(demultiplexer_1_out_4),
    .out_5(demultiplexer_1_out_5), .out_6(demultiplexer_1_out_6), .out_7(demultiplexer_1_out_7),
    .out_8(demultiplexer_1_out_8), .out_9(demultiplexer_1_out_9), .out_10(demultiplexer_1_out_10),
    .out_11(demultiplexer_1_out_11), .out_12(demultiplexer_1_out_12), .out_13(demultiplexer_1_out_13),
    .out_14(demultiplexer_1_out_14), .out_15(demultiplexer_1_out_15), .out_16(demultiplexer_1_out_16),
    .out_17(demultiplexer_1_out_17), .out_18(demultiplexer_1_out_18), .out_19(demultiplexer_1_out_19),
    .out_20(demultiplexer_1_out_20), .out_21(demultiplexer_1_out_21), .out_22(demultiplexer_1_out_22),
    .out_23(demultiplexer_1_out_23), .out_24(demultiplexer_1_out_24), .out_25(demultiplexer_1_out_25),
    .out_26(demultiplexer_1_out_26), .out_27(demultiplexer_1_out_27), .out_28(demultiplexer_1_out_28),
    .out_29(demultiplexer_1_out_29), .out_30(demultiplexer_1_out_30), .out_31(demultiplexer_1_out_31));
  rob_update_mask rob_update_mask_1 (
    .Current(multiplexer_34_out), .Update(UpdateData_RMEM), .Entry(rob_update_mask_1_entry));
  assign driver_1_out = UpdateWE_RMEM ? rob_update_mask_1_entry : 43'bz;  // Driver driver_1
  PullDown #(.Bits(43)) pulldown_1 (.out(driver_1_out));
  Demultiplexer #(.Selector_Bits(5), .Bits(43)) demultiplexer_2 (
    .sel(UpdateA_RMEM), .in(driver_1_out), .out_0(demultiplexer_2_out_0), .out_1(demultiplexer_2_out_1),
    .out_2(demultiplexer_2_out_2), .out_3(demultiplexer_2_out_3), .out_4(demultiplexer_2_out_4),
    .out_5(demultiplexer_2_out_5), .out_6(demultiplexer_2_out_6), .out_7(demultiplexer_2_out_7),
    .out_8(demultiplexer_2_out_8), .out_9(demultiplexer_2_out_9), .out_10(demultiplexer_2_out_10),
    .out_11(demultiplexer_2_out_11), .out_12(demultiplexer_2_out_12), .out_13(demultiplexer_2_out_13),
    .out_14(demultiplexer_2_out_14), .out_15(demultiplexer_2_out_15), .out_16(demultiplexer_2_out_16),
    .out_17(demultiplexer_2_out_17), .out_18(demultiplexer_2_out_18), .out_19(demultiplexer_2_out_19),
    .out_20(demultiplexer_2_out_20), .out_21(demultiplexer_2_out_21), .out_22(demultiplexer_2_out_22),
    .out_23(demultiplexer_2_out_23), .out_24(demultiplexer_2_out_24), .out_25(demultiplexer_2_out_25),
    .out_26(demultiplexer_2_out_26), .out_27(demultiplexer_2_out_27), .out_28(demultiplexer_2_out_28),
    .out_29(demultiplexer_2_out_29), .out_30(demultiplexer_2_out_30), .out_31(demultiplexer_2_out_31));
  Demultiplexer #(.Selector_Bits(5)) demultiplexer_3 (
    .sel(UpdateA_IRALU), .in(UpdateWE_IRALU), .out_0(demultiplexer_3_out_0), .out_1(demultiplexer_3_out_1),
    .out_2(demultiplexer_3_out_2), .out_3(demultiplexer_3_out_3), .out_4(demultiplexer_3_out_4),
    .out_5(demultiplexer_3_out_5), .out_6(demultiplexer_3_out_6), .out_7(demultiplexer_3_out_7),
    .out_8(demultiplexer_3_out_8), .out_9(demultiplexer_3_out_9), .out_10(demultiplexer_3_out_10),
    .out_11(demultiplexer_3_out_11), .out_12(demultiplexer_3_out_12), .out_13(demultiplexer_3_out_13),
    .out_14(demultiplexer_3_out_14), .out_15(demultiplexer_3_out_15), .out_16(demultiplexer_3_out_16),
    .out_17(demultiplexer_3_out_17), .out_18(demultiplexer_3_out_18), .out_19(demultiplexer_3_out_19),
    .out_20(demultiplexer_3_out_20), .out_21(demultiplexer_3_out_21), .out_22(demultiplexer_3_out_22),
    .out_23(demultiplexer_3_out_23), .out_24(demultiplexer_3_out_24), .out_25(demultiplexer_3_out_25),
    .out_26(demultiplexer_3_out_26), .out_27(demultiplexer_3_out_27), .out_28(demultiplexer_3_out_28),
    .out_29(demultiplexer_3_out_29), .out_30(demultiplexer_3_out_30), .out_31(demultiplexer_3_out_31));
  Demultiplexer #(.Selector_Bits(5)) demultiplexer_4 (
    .sel(TailIdx), .in(TailWE), .out_0(demultiplexer_4_out_0), .out_1(demultiplexer_4_out_1),
    .out_2(demultiplexer_4_out_2), .out_3(demultiplexer_4_out_3), .out_4(demultiplexer_4_out_4),
    .out_5(demultiplexer_4_out_5), .out_6(demultiplexer_4_out_6), .out_7(demultiplexer_4_out_7),
    .out_8(demultiplexer_4_out_8), .out_9(demultiplexer_4_out_9), .out_10(demultiplexer_4_out_10),
    .out_11(demultiplexer_4_out_11), .out_12(demultiplexer_4_out_12), .out_13(demultiplexer_4_out_13),
    .out_14(demultiplexer_4_out_14), .out_15(demultiplexer_4_out_15), .out_16(demultiplexer_4_out_16),
    .out_17(demultiplexer_4_out_17), .out_18(demultiplexer_4_out_18), .out_19(demultiplexer_4_out_19),
    .out_20(demultiplexer_4_out_20), .out_21(demultiplexer_4_out_21), .out_22(demultiplexer_4_out_22),
    .out_23(demultiplexer_4_out_23), .out_24(demultiplexer_4_out_24), .out_25(demultiplexer_4_out_25),
    .out_26(demultiplexer_4_out_26), .out_27(demultiplexer_4_out_27), .out_28(demultiplexer_4_out_28),
    .out_29(demultiplexer_4_out_29), .out_30(demultiplexer_4_out_30), .out_31(demultiplexer_4_out_31));
  rob_update_mask rob_update_mask_2 (
    .Current(multiplexer_33_out), .Update(UpdateData_IRALU), .Entry(rob_update_mask_2_entry));
  assign driver_2_out = UpdateWE_IRALU ? rob_update_mask_2_entry : 43'bz;  // Driver driver_2
  PullDown #(.Bits(43)) pulldown_2 (.out(driver_2_out));
  Demultiplexer #(.Selector_Bits(5), .Bits(43)) demultiplexer_5 (
    .sel(UpdateA_IRALU), .in(driver_2_out), .out_0(demultiplexer_5_out_0), .out_1(demultiplexer_5_out_1),
    .out_2(demultiplexer_5_out_2), .out_3(demultiplexer_5_out_3), .out_4(demultiplexer_5_out_4),
    .out_5(demultiplexer_5_out_5), .out_6(demultiplexer_5_out_6), .out_7(demultiplexer_5_out_7),
    .out_8(demultiplexer_5_out_8), .out_9(demultiplexer_5_out_9), .out_10(demultiplexer_5_out_10),
    .out_11(demultiplexer_5_out_11), .out_12(demultiplexer_5_out_12), .out_13(demultiplexer_5_out_13),
    .out_14(demultiplexer_5_out_14), .out_15(demultiplexer_5_out_15), .out_16(demultiplexer_5_out_16),
    .out_17(demultiplexer_5_out_17), .out_18(demultiplexer_5_out_18), .out_19(demultiplexer_5_out_19),
    .out_20(demultiplexer_5_out_20), .out_21(demultiplexer_5_out_21), .out_22(demultiplexer_5_out_22),
    .out_23(demultiplexer_5_out_23), .out_24(demultiplexer_5_out_24), .out_25(demultiplexer_5_out_25),
    .out_26(demultiplexer_5_out_26), .out_27(demultiplexer_5_out_27), .out_28(demultiplexer_5_out_28),
    .out_29(demultiplexer_5_out_29), .out_30(demultiplexer_5_out_30), .out_31(demultiplexer_5_out_31));
  Demultiplexer #(.Selector_Bits(5), .Bits(43)) demultiplexer_6 (
    .sel(TailIdx), .in(TailData), .out_0(demultiplexer_6_out_0), .out_1(demultiplexer_6_out_1),
    .out_2(demultiplexer_6_out_2), .out_3(demultiplexer_6_out_3), .out_4(demultiplexer_6_out_4),
    .out_5(demultiplexer_6_out_5), .out_6(demultiplexer_6_out_6), .out_7(demultiplexer_6_out_7),
    .out_8(demultiplexer_6_out_8), .out_9(demultiplexer_6_out_9), .out_10(demultiplexer_6_out_10),
    .out_11(demultiplexer_6_out_11), .out_12(demultiplexer_6_out_12), .out_13(demultiplexer_6_out_13),
    .out_14(demultiplexer_6_out_14), .out_15(demultiplexer_6_out_15), .out_16(demultiplexer_6_out_16),
    .out_17(demultiplexer_6_out_17), .out_18(demultiplexer_6_out_18), .out_19(demultiplexer_6_out_19),
    .out_20(demultiplexer_6_out_20), .out_21(demultiplexer_6_out_21), .out_22(demultiplexer_6_out_22),
    .out_23(demultiplexer_6_out_23), .out_24(demultiplexer_6_out_24), .out_25(demultiplexer_6_out_25),
    .out_26(demultiplexer_6_out_26), .out_27(demultiplexer_6_out_27), .out_28(demultiplexer_6_out_28),
    .out_29(demultiplexer_6_out_29), .out_30(demultiplexer_6_out_30), .out_31(demultiplexer_6_out_31));
  assign or_3_out = demultiplexer_6_out_0 | demultiplexer_2_out_0 | demultiplexer_5_out_0;  // Or or_3, 43 bits wide
  or or_4 (or_4_out, demultiplexer_4_out_0, CLR, demultiplexer_1_out_0, demultiplexer_3_out_0);
  assign or_5_out = demultiplexer_6_out_1 | demultiplexer_2_out_1 | demultiplexer_5_out_1;  // Or or_5, 43 bits wide
  or or_6 (or_6_out, demultiplexer_4_out_1, CLR, demultiplexer_1_out_1, demultiplexer_3_out_1);
  assign or_7_out = demultiplexer_6_out_2 | demultiplexer_2_out_2 | demultiplexer_5_out_2;  // Or or_7, 43 bits wide
  or or_8 (or_8_out, demultiplexer_4_out_2, CLR, demultiplexer_1_out_2, demultiplexer_3_out_2);
  assign or_9_out = demultiplexer_6_out_3 | demultiplexer_2_out_3 | demultiplexer_5_out_3;  // Or or_9, 43 bits wide
  or or_10 (or_10_out, demultiplexer_4_out_3, CLR, demultiplexer_1_out_3, demultiplexer_3_out_3);
  assign or_11_out = demultiplexer_6_out_4 | demultiplexer_2_out_4 | demultiplexer_5_out_4;  // Or or_11, 43 bits wide
  or or_12 (or_12_out, demultiplexer_4_out_4, CLR, demultiplexer_1_out_4, demultiplexer_3_out_4);
  assign or_13_out = demultiplexer_6_out_5 | demultiplexer_2_out_5 | demultiplexer_5_out_5;  // Or or_13, 43 bits wide
  or or_14 (or_14_out, demultiplexer_4_out_5, CLR, demultiplexer_1_out_5, demultiplexer_3_out_5);
  assign or_15_out = demultiplexer_6_out_6 | demultiplexer_2_out_6 | demultiplexer_5_out_6;  // Or or_15, 43 bits wide
  or or_16 (or_16_out, demultiplexer_4_out_6, CLR, demultiplexer_1_out_6, demultiplexer_3_out_6);
  assign or_17_out = demultiplexer_6_out_7 | demultiplexer_2_out_7 | demultiplexer_5_out_7;  // Or or_17, 43 bits wide
  or or_18 (or_18_out, demultiplexer_4_out_7, CLR, demultiplexer_1_out_7, demultiplexer_3_out_7);
  assign or_19_out = demultiplexer_6_out_8 | demultiplexer_2_out_8 | demultiplexer_5_out_8;  // Or or_19, 43 bits wide
  or or_20 (or_20_out, demultiplexer_4_out_8, CLR, demultiplexer_1_out_8, demultiplexer_3_out_8);
  assign or_21_out = demultiplexer_6_out_9 | demultiplexer_2_out_9 | demultiplexer_5_out_9;  // Or or_21, 43 bits wide
  or or_22 (or_22_out, demultiplexer_4_out_9, CLR, demultiplexer_1_out_9, demultiplexer_3_out_9);
  assign or_23_out = demultiplexer_6_out_10 | demultiplexer_2_out_10 | demultiplexer_5_out_10;  // Or or_23, 43 bits wide
  or or_24 (or_24_out, demultiplexer_4_out_10, CLR, demultiplexer_1_out_10, demultiplexer_3_out_10);
  assign or_25_out = demultiplexer_6_out_11 | demultiplexer_2_out_11 | demultiplexer_5_out_11;  // Or or_25, 43 bits wide
  or or_26 (or_26_out, demultiplexer_4_out_11, CLR, demultiplexer_1_out_11, demultiplexer_3_out_11);
  assign or_27_out = demultiplexer_6_out_12 | demultiplexer_2_out_12 | demultiplexer_5_out_12;  // Or or_27, 43 bits wide
  or or_28 (or_28_out, demultiplexer_4_out_12, CLR, demultiplexer_1_out_12, demultiplexer_3_out_12);
  assign or_29_out = demultiplexer_6_out_13 | demultiplexer_2_out_13 | demultiplexer_5_out_13;  // Or or_29, 43 bits wide
  or or_30 (or_30_out, demultiplexer_4_out_13, CLR, demultiplexer_1_out_13, demultiplexer_3_out_13);
  assign or_31_out = demultiplexer_6_out_14 | demultiplexer_2_out_14 | demultiplexer_5_out_14;  // Or or_31, 43 bits wide
  or or_32 (or_32_out, demultiplexer_4_out_14, CLR, demultiplexer_1_out_14, demultiplexer_3_out_14);
  assign or_33_out = demultiplexer_6_out_15 | demultiplexer_2_out_15 | demultiplexer_5_out_15;  // Or or_33, 43 bits wide
  or or_34 (or_34_out, demultiplexer_4_out_15, CLR, demultiplexer_1_out_15, demultiplexer_3_out_15);
  assign or_35_out = demultiplexer_6_out_16 | demultiplexer_2_out_16 | demultiplexer_5_out_16;  // Or or_35, 43 bits wide
  or or_36 (or_36_out, demultiplexer_4_out_16, CLR, demultiplexer_1_out_16, demultiplexer_3_out_16);
  assign or_37_out = demultiplexer_6_out_17 | demultiplexer_2_out_17 | demultiplexer_5_out_17;  // Or or_37, 43 bits wide
  or or_38 (or_38_out, demultiplexer_4_out_17, CLR, demultiplexer_1_out_17, demultiplexer_3_out_17);
  assign or_39_out = demultiplexer_6_out_18 | demultiplexer_2_out_18 | demultiplexer_5_out_18;  // Or or_39, 43 bits wide
  or or_40 (or_40_out, demultiplexer_4_out_18, CLR, demultiplexer_1_out_18, demultiplexer_3_out_18);
  assign or_41_out = demultiplexer_6_out_19 | demultiplexer_2_out_19 | demultiplexer_5_out_19;  // Or or_41, 43 bits wide
  or or_42 (or_42_out, demultiplexer_4_out_19, CLR, demultiplexer_1_out_19, demultiplexer_3_out_19);
  assign or_43_out = demultiplexer_6_out_20 | demultiplexer_2_out_20 | demultiplexer_5_out_20;  // Or or_43, 43 bits wide
  or or_44 (or_44_out, demultiplexer_4_out_20, CLR, demultiplexer_1_out_20, demultiplexer_3_out_20);
  assign or_45_out = demultiplexer_6_out_21 | demultiplexer_2_out_21 | demultiplexer_5_out_21;  // Or or_45, 43 bits wide
  or or_46 (or_46_out, demultiplexer_4_out_21, CLR, demultiplexer_1_out_21, demultiplexer_3_out_21);
  assign or_47_out = demultiplexer_6_out_22 | demultiplexer_2_out_22 | demultiplexer_5_out_22;  // Or or_47, 43 bits wide
  or or_48 (or_48_out, demultiplexer_4_out_22, CLR, demultiplexer_1_out_22, demultiplexer_3_out_22);
  assign or_49_out = demultiplexer_6_out_23 | demultiplexer_2_out_23 | demultiplexer_5_out_23;  // Or or_49, 43 bits wide
  or or_50 (or_50_out, demultiplexer_4_out_23, CLR, demultiplexer_1_out_23, demultiplexer_3_out_23);
  assign or_51_out = demultiplexer_6_out_24 | demultiplexer_2_out_24 | demultiplexer_5_out_24;  // Or or_51, 43 bits wide
  or or_52 (or_52_out, demultiplexer_4_out_24, CLR, demultiplexer_1_out_24, demultiplexer_3_out_24);
  assign or_53_out = demultiplexer_6_out_25 | demultiplexer_2_out_25 | demultiplexer_5_out_25;  // Or or_53, 43 bits wide
  or or_54 (or_54_out, demultiplexer_4_out_25, CLR, demultiplexer_1_out_25, demultiplexer_3_out_25);
  assign or_55_out = demultiplexer_6_out_26 | demultiplexer_2_out_26 | demultiplexer_5_out_26;  // Or or_55, 43 bits wide
  or or_56 (or_56_out, demultiplexer_4_out_26, CLR, demultiplexer_1_out_26, demultiplexer_3_out_26);
  assign or_57_out = demultiplexer_6_out_27 | demultiplexer_2_out_27 | demultiplexer_5_out_27;  // Or or_57, 43 bits wide
  or or_58 (or_58_out, demultiplexer_4_out_27, CLR, demultiplexer_1_out_27, demultiplexer_3_out_27);
  assign or_59_out = demultiplexer_6_out_28 | demultiplexer_2_out_28 | demultiplexer_5_out_28;  // Or or_59, 43 bits wide
  or or_60 (or_60_out, demultiplexer_4_out_28, CLR, demultiplexer_1_out_28, demultiplexer_3_out_28);
  assign or_61_out = demultiplexer_6_out_29 | demultiplexer_2_out_29 | demultiplexer_5_out_29;  // Or or_61, 43 bits wide
  or or_62 (or_62_out, demultiplexer_4_out_29, CLR, demultiplexer_1_out_29, demultiplexer_3_out_29);
  assign or_63_out = demultiplexer_6_out_30 | demultiplexer_2_out_30 | demultiplexer_5_out_30;  // Or or_63, 43 bits wide
  or or_64 (or_64_out, demultiplexer_4_out_30, CLR, demultiplexer_1_out_30, demultiplexer_3_out_30);
  assign or_65_out = demultiplexer_6_out_31 | demultiplexer_2_out_31 | demultiplexer_5_out_31;  // Or or_65, 43 bits wide
  or or_66 (or_66_out, demultiplexer_4_out_31, CLR, demultiplexer_1_out_31, demultiplexer_3_out_31);
  Multiplexer #(.Bits(43)) multiplexer_1 (.sel(CLR), .in_0(or_3_out), .in_1({43{1'b0}}), .out(multiplexer_1_out));
  Multiplexer #(.Bits(43)) multiplexer_2 (.sel(CLR), .in_0(or_5_out), .in_1({43{1'b0}}), .out(multiplexer_2_out));
  Multiplexer #(.Bits(43)) multiplexer_3 (.sel(CLR), .in_0(or_7_out), .in_1({43{1'b0}}), .out(multiplexer_3_out));
  Multiplexer #(.Bits(43)) multiplexer_4 (.sel(CLR), .in_0(or_9_out), .in_1({43{1'b0}}), .out(multiplexer_4_out));
  Multiplexer #(.Bits(43)) multiplexer_5 (.sel(CLR), .in_0(or_11_out), .in_1({43{1'b0}}), .out(multiplexer_5_out));
  Multiplexer #(.Bits(43)) multiplexer_6 (.sel(CLR), .in_0(or_13_out), .in_1({43{1'b0}}), .out(multiplexer_6_out));
  Multiplexer #(.Bits(43)) multiplexer_7 (.sel(CLR), .in_0(or_15_out), .in_1({43{1'b0}}), .out(multiplexer_7_out));
  Multiplexer #(.Bits(43)) multiplexer_8 (.sel(CLR), .in_0(or_17_out), .in_1({43{1'b0}}), .out(multiplexer_8_out));
  Multiplexer #(.Bits(43)) multiplexer_9 (.sel(CLR), .in_0(or_19_out), .in_1({43{1'b0}}), .out(multiplexer_9_out));
  Multiplexer #(.Bits(43)) multiplexer_10 (.sel(CLR), .in_0(or_21_out), .in_1({43{1'b0}}), .out(multiplexer_10_out));
  Multiplexer #(.Bits(43)) multiplexer_11 (.sel(CLR), .in_0(or_23_out), .in_1({43{1'b0}}), .out(multiplexer_11_out));
  Multiplexer #(.Bits(43)) multiplexer_12 (.sel(CLR), .in_0(or_25_out), .in_1({43{1'b0}}), .out(multiplexer_12_out));
  Multiplexer #(.Bits(43)) multiplexer_13 (.sel(CLR), .in_0(or_27_out), .in_1({43{1'b0}}), .out(multiplexer_13_out));
  Multiplexer #(.Bits(43)) multiplexer_14 (.sel(CLR), .in_0(or_29_out), .in_1({43{1'b0}}), .out(multiplexer_14_out));
  Multiplexer #(.Bits(43)) multiplexer_15 (.sel(CLR), .in_0(or_31_out), .in_1({43{1'b0}}), .out(multiplexer_15_out));
  Multiplexer #(.Bits(43)) multiplexer_16 (.sel(CLR), .in_0(or_33_out), .in_1({43{1'b0}}), .out(multiplexer_16_out));
  Multiplexer #(.Bits(43)) multiplexer_17 (.sel(CLR), .in_0(or_35_out), .in_1({43{1'b0}}), .out(multiplexer_17_out));
  Multiplexer #(.Bits(43)) multiplexer_18 (.sel(CLR), .in_0(or_37_out), .in_1({43{1'b0}}), .out(multiplexer_18_out));
  Multiplexer #(.Bits(43)) multiplexer_19 (.sel(CLR), .in_0(or_39_out), .in_1({43{1'b0}}), .out(multiplexer_19_out));
  Multiplexer #(.Bits(43)) multiplexer_20 (.sel(CLR), .in_0(or_41_out), .in_1({43{1'b0}}), .out(multiplexer_20_out));
  Multiplexer #(.Bits(43)) multiplexer_21 (.sel(CLR), .in_0(or_43_out), .in_1({43{1'b0}}), .out(multiplexer_21_out));
  Multiplexer #(.Bits(43)) multiplexer_22 (.sel(CLR), .in_0(or_45_out), .in_1({43{1'b0}}), .out(multiplexer_22_out));
  Multiplexer #(.Bits(43)) multiplexer_23 (.sel(CLR), .in_0(or_47_out), .in_1({43{1'b0}}), .out(multiplexer_23_out));
  Multiplexer #(.Bits(43)) multiplexer_24 (.sel(CLR), .in_0(or_49_out), .in_1({43{1'b0}}), .out(multiplexer_24_out));
  Multiplexer #(.Bits(43)) multiplexer_25 (.sel(CLR), .in_0(or_51_out), .in_1({43{1'b0}}), .out(multiplexer_25_out));
  Multiplexer #(.Bits(43)) multiplexer_26 (.sel(CLR), .in_0(or_53_out), .in_1({43{1'b0}}), .out(multiplexer_26_out));
  Multiplexer #(.Bits(43)) multiplexer_27 (.sel(CLR), .in_0(or_55_out), .in_1({43{1'b0}}), .out(multiplexer_27_out));
  Multiplexer #(.Bits(43)) multiplexer_28 (.sel(CLR), .in_0(or_57_out), .in_1({43{1'b0}}), .out(multiplexer_28_out));
  Multiplexer #(.Bits(43)) multiplexer_29 (.sel(CLR), .in_0(or_59_out), .in_1({43{1'b0}}), .out(multiplexer_29_out));
  Multiplexer #(.Bits(43)) multiplexer_30 (.sel(CLR), .in_0(or_61_out), .in_1({43{1'b0}}), .out(multiplexer_30_out));
  Multiplexer #(.Bits(43)) multiplexer_31 (.sel(CLR), .in_0(or_63_out), .in_1({43{1'b0}}), .out(multiplexer_31_out));
  Multiplexer #(.Bits(43)) multiplexer_32 (.sel(CLR), .in_0(or_65_out), .in_1({43{1'b0}}), .out(multiplexer_32_out));
  Register #(.Bits(43)) ROB_0 (.D(multiplexer_1_out), .C(CLK), .en(or_4_out), .Q(ROB_0_q));
  Register #(.Bits(43)) ROB_1 (.D(multiplexer_2_out), .C(CLK), .en(or_6_out), .Q(ROB_1_q));
  Register #(.Bits(43)) ROB_2 (.D(multiplexer_3_out), .C(CLK), .en(or_8_out), .Q(ROB_2_q));
  Register #(.Bits(43)) ROB_3 (.D(multiplexer_4_out), .C(CLK), .en(or_10_out), .Q(ROB_3_q));
  Register #(.Bits(43)) ROB_4 (.D(multiplexer_5_out), .C(CLK), .en(or_12_out), .Q(ROB_4_q));
  Register #(.Bits(43)) ROB_5 (.D(multiplexer_6_out), .C(CLK), .en(or_14_out), .Q(ROB_5_q));
  Register #(.Bits(43)) ROB_6 (.D(multiplexer_7_out), .C(CLK), .en(or_16_out), .Q(ROB_6_q));
  Register #(.Bits(43)) ROB_7 (.D(multiplexer_8_out), .C(CLK), .en(or_18_out), .Q(ROB_7_q));
  Register #(.Bits(43)) ROB_8 (.D(multiplexer_9_out), .C(CLK), .en(or_20_out), .Q(ROB_8_q));
  Register #(.Bits(43)) ROB_9 (.D(multiplexer_10_out), .C(CLK), .en(or_22_out), .Q(ROB_9_q));
  Register #(.Bits(43)) ROB_10 (.D(multiplexer_11_out), .C(CLK), .en(or_24_out), .Q(ROB_10_q));
  Register #(.Bits(43)) ROB_11 (.D(multiplexer_12_out), .C(CLK), .en(or_26_out), .Q(ROB_11_q));
  Register #(.Bits(43)) ROB_12 (.D(multiplexer_13_out), .C(CLK), .en(or_28_out), .Q(ROB_12_q));
  Register #(.Bits(43)) ROB_13 (.D(multiplexer_14_out), .C(CLK), .en(or_30_out), .Q(ROB_13_q));
  Register #(.Bits(43)) ROB_14 (.D(multiplexer_15_out), .C(CLK), .en(or_32_out), .Q(ROB_14_q));
  Register #(.Bits(43)) ROB_15 (.D(multiplexer_16_out), .C(CLK), .en(or_34_out), .Q(ROB_15_q));
  Register #(.Bits(43)) ROB_16 (.D(multiplexer_17_out), .C(CLK), .en(or_36_out), .Q(ROB_16_q));
  Register #(.Bits(43)) ROB_17 (.D(multiplexer_18_out), .C(CLK), .en(or_38_out), .Q(ROB_17_q));
  Register #(.Bits(43)) ROB_18 (.D(multiplexer_19_out), .C(CLK), .en(or_40_out), .Q(ROB_18_q));
  Register #(.Bits(43)) ROB_19 (.D(multiplexer_20_out), .C(CLK), .en(or_42_out), .Q(ROB_19_q));
  Register #(.Bits(43)) ROB_20 (.D(multiplexer_21_out), .C(CLK), .en(or_44_out), .Q(ROB_20_q));
  Register #(.Bits(43)) ROB_21 (.D(multiplexer_22_out), .C(CLK), .en(or_46_out), .Q(ROB_21_q));
  Register #(.Bits(43)) ROB_22 (.D(multiplexer_23_out), .C(CLK), .en(or_48_out), .Q(ROB_22_q));
  Register #(.Bits(43)) ROB_23 (.D(multiplexer_24_out), .C(CLK), .en(or_50_out), .Q(ROB_23_q));
  Register #(.Bits(43)) ROB_24 (.D(multiplexer_25_out), .C(CLK), .en(or_52_out), .Q(ROB_24_q));
  Register #(.Bits(43)) ROB_25 (.D(multiplexer_26_out), .C(CLK), .en(or_54_out), .Q(ROB_25_q));
  Register #(.Bits(43)) ROB_26 (.D(multiplexer_27_out), .C(CLK), .en(or_56_out), .Q(ROB_26_q));
  Register #(.Bits(43)) ROB_27 (.D(multiplexer_28_out), .C(CLK), .en(or_58_out), .Q(ROB_27_q));
  Register #(.Bits(43)) ROB_28 (.D(multiplexer_29_out), .C(CLK), .en(or_60_out), .Q(ROB_28_q));
  Register #(.Bits(43)) ROB_29 (.D(multiplexer_30_out), .C(CLK), .en(or_62_out), .Q(ROB_29_q));
  Register #(.Bits(43)) ROB_30 (.D(multiplexer_31_out), .C(CLK), .en(or_64_out), .Q(ROB_30_q));
  Register #(.Bits(43)) ROB_31 (.D(multiplexer_32_out), .C(CLK), .en(or_66_out), .Q(ROB_31_q));
  Multiplexer #(.Selector_Bits(5), .Bits(43)) multiplexer_33 (
    .sel(UpdateA_IRALU), .in_0(ROB_0_q), .in_1(ROB_1_q), .in_2(ROB_2_q), .in_3(ROB_3_q), .in_4(ROB_4_q),
    .in_5(ROB_5_q), .in_6(ROB_6_q), .in_7(ROB_7_q), .in_8(ROB_8_q), .in_9(ROB_9_q), .in_10(ROB_10_q),
    .in_11(ROB_11_q), .in_12(ROB_12_q), .in_13(ROB_13_q), .in_14(ROB_14_q), .in_15(ROB_15_q),
    .in_16(ROB_16_q), .in_17(ROB_17_q), .in_18(ROB_18_q), .in_19(ROB_19_q), .in_20(ROB_20_q),
    .in_21(ROB_21_q), .in_22(ROB_22_q), .in_23(ROB_23_q), .in_24(ROB_24_q), .in_25(ROB_25_q),
    .in_26(ROB_26_q), .in_27(ROB_27_q), .in_28(ROB_28_q), .in_29(ROB_29_q), .in_30(ROB_30_q),
    .in_31(ROB_31_q), .out(multiplexer_33_out));
  Multiplexer #(.Selector_Bits(5), .Bits(43)) multiplexer_34 (
    .sel(UpdateA_RMEM), .in_0(ROB_0_q), .in_1(ROB_1_q), .in_2(ROB_2_q), .in_3(ROB_3_q), .in_4(ROB_4_q),
    .in_5(ROB_5_q), .in_6(ROB_6_q), .in_7(ROB_7_q), .in_8(ROB_8_q), .in_9(ROB_9_q), .in_10(ROB_10_q),
    .in_11(ROB_11_q), .in_12(ROB_12_q), .in_13(ROB_13_q), .in_14(ROB_14_q), .in_15(ROB_15_q),
    .in_16(ROB_16_q), .in_17(ROB_17_q), .in_18(ROB_18_q), .in_19(ROB_19_q), .in_20(ROB_20_q),
    .in_21(ROB_21_q), .in_22(ROB_22_q), .in_23(ROB_23_q), .in_24(ROB_24_q), .in_25(ROB_25_q),
    .in_26(ROB_26_q), .in_27(ROB_27_q), .in_28(ROB_28_q), .in_29(ROB_29_q), .in_30(ROB_30_q),
    .in_31(ROB_31_q), .out(multiplexer_34_out));
  Multiplexer #(.Selector_Bits(5), .Bits(43)) multiplexer_35 (
    .sel(HeadIdx), .in_0(ROB_0_q), .in_1(ROB_1_q), .in_2(ROB_2_q), .in_3(ROB_3_q), .in_4(ROB_4_q),
    .in_5(ROB_5_q), .in_6(ROB_6_q), .in_7(ROB_7_q), .in_8(ROB_8_q), .in_9(ROB_9_q), .in_10(ROB_10_q),
    .in_11(ROB_11_q), .in_12(ROB_12_q), .in_13(ROB_13_q), .in_14(ROB_14_q), .in_15(ROB_15_q),
    .in_16(ROB_16_q), .in_17(ROB_17_q), .in_18(ROB_18_q), .in_19(ROB_19_q), .in_20(ROB_20_q),
    .in_21(ROB_21_q), .in_22(ROB_22_q), .in_23(ROB_23_q), .in_24(ROB_24_q), .in_25(ROB_25_q),
    .in_26(ROB_26_q), .in_27(ROB_27_q), .in_28(ROB_28_q), .in_29(ROB_29_q), .in_30(ROB_30_q),
    .in_31(ROB_31_q), .out(HeadData));

  // Notes on the sheet:
  //   ROB Circular Buffer
  //   Update Enable (R-MEM)
  //   Update Data (R-MEM)
  //   Update Enable (I/R-ALU)
  //   Tail Enable
  //   Update Data (I/R-ALU)
  //   Tail Data
  //   Current Data (I/R-ALU)
  //   Current Data (R-MEM)
endmodule
