// Digital circuit condensed_drrd_forwarding.dig as structural Verilog
module condensed_drrd_forwarding (
  input  [15:0] UpdateData,
  input  V_IN,
  input  [4:0] ROBTag,
  input  [2:0] UpdateDst,
  input  [15:0] RegOut,
  input  [2:0] RegA,
  output [15:0] Reg_Tag,
  output V_OUT
);

  wire comparator_1_eq, not_1_out;
  wire [15:0] multiplexer_1_out;

  Comparator #(.Bits(3)) comparator_1 (.a(RegA), .b(UpdateDst), .eq(comparator_1_eq));  // open: gt, lt
  Multiplexer #(.Bits(16)) multiplexer_1 (
    .sel(comparator_1_eq), .in_0(RegOut), .in_1(UpdateData), .out(multiplexer_1_out));
  Multiplexer multiplexer_2 (.sel(comparator_1_eq), .in_0(not_1_out), .in_1(1'b1), .out(V_OUT));
  not not_1 (not_1_out, V_IN);
  Multiplexer #(.Bits(16)) multiplexer_3 (
    .sel(V_IN), .in_0(multiplexer_1_out), .in_1({{11{1'b0}}, ROBTag}), .out(Reg_Tag));

  // Notes on the sheet:
  //   Condensed DRRD Forwarding
endmodule
