// Digital circuit condition_unit.dig as structural Verilog
module condition_unit (
  input  FlagWriteE,
  input  CondE,
  input  [3:0] FlagsE,
  input  [3:0] ALUFlags,
  output CondExE,
  output [3:0] FlagsM
);

  wire not_1_out;

  Multiplexer #(.Bits(4)) multiplexer_1 (.sel(FlagWriteE), .in_0(FlagsE), .in_1(ALUFlags), .out(FlagsM));
  not not_1 (not_1_out, CondE);
  or or_1 (CondExE, FlagsE[0], not_1_out);

  // Notes on the sheet:
  //   Condition Unit
endmodule
