// Digital circuit control_unit.dig as structural Verilog
module control_unit (
  input  [15:0] INSN,
  output FlagWriteD,
  output ALUSrcD,
  output BranchD,
  output [1:0] ALUCtrlD,
  output MemWriteD,
  output MemToRegD,
  output RegWriteD,
  output PCSrcD,
  output SethD,
  output FlagEN,
  output NOP
);

  wire Is_Rd_PC_eq, or_1_out, or_2_out;
  wire [10:0] lookuptable_1_out;

  Comparator #(.Bits(16)) comparator_1 (.a({16{1'b0}}), .b(INSN), .eq(NOP));  // open: gt, lt
  LookUpTable #(.Bits(11)) lookuptable_1 (
    .in0(INSN[12]), .in1(INSN[13]), .in2(INSN[14]), .in3(INSN[15]), .out(lookuptable_1_out));
  Comparator #(.Bits(3)) Is_Rd_PC (.a(INSN[10:8]), .b(3'b111), .eq(Is_Rd_PC_eq));  // open: gt, lt
  or or_1 (or_1_out, Is_Rd_PC_eq, lookuptable_1_out[10]);
  or or_2 (or_2_out, Is_Rd_PC_eq, lookuptable_1_out[4]);
  Multiplexer multiplexer_1 (.sel(NOP), .in_0(or_1_out), .in_1(1'b0), .out(PCSrcD));
  Multiplexer multiplexer_2 (.sel(NOP), .in_0(lookuptable_1_out[9]), .in_1(1'b0), .out(RegWriteD));
  Multiplexer multiplexer_3 (.sel(NOP), .in_0(lookuptable_1_out[8]), .in_1(1'b0), .out(MemToRegD));
  Multiplexer multiplexer_4 (.sel(NOP), .in_0(lookuptable_1_out[7]), .in_1(1'b0), .out(MemWriteD));
  Multiplexer #(.Bits(2)) multiplexer_5 (.sel(NOP), .in_0(lookuptable_1_out[6:5]), .in_1(2'b00), .out(ALUCtrlD));
  Multiplexer multiplexer_6 (.sel(NOP), .in_0(or_2_out), .in_1(1'b0), .out(BranchD));
  Multiplexer multiplexer_7 (.sel(NOP), .in_0(lookuptable_1_out[3]), .in_1(1'b0), .out(ALUSrcD));
  Multiplexer multiplexer_8 (.sel(NOP), .in_0(lookuptable_1_out[2]), .in_1(1'b0), .out(FlagWriteD));
  Multiplexer multiplexer_9 (.sel(NOP), .in_0(lookuptable_1_out[1]), .in_1(1'b0), .out(SethD));
  Multiplexer multiplexer_10 (.sel(NOP), .in_0(lookuptable_1_out[0]), .in_1(1'b0), .out(FlagEN));

  // Notes on the sheet:
  //   Rd
  //   contents of lookuptable_1 (hex, n*v repeats v):
  //   208,20a,0,0,80,300,0,0,205,225,245,265
endmodule
