// Digital circuit cpu.dig as structural Verilog
module cpu (
  input  CLK
);

  wire and_1_out, and_2_out, and_3_out, and_4_out, and_5_out, and_6_out, and_7_out, and_8_out,
       comparator_1_eq, comparator_2_eq, condensed_drrd_forwarding_1_v_out,
       condensed_drrd_forwarding_2_v_out, Condition_Unit_2_condexe, Condition_Unit_condexe,
       Control_Unit_2_branchd, Control_Unit_2_flagwrited, Control_Unit_2_memtoregd, Control_Unit_2_memwrited,
       Control_Unit_2_sethd, Control_Unit_2_updaterob, Control_Unit_branchd, Control_Unit_flagwrited,
       Control_Unit_memtoregd, Control_Unit_memwrited, Control_Unit_sethd, Control_Unit_updaterob,
       DP_I_PPR_2_branchi, DP_I_PPR_2_condi, DP_I_PPR_2_flagwritei, DP_I_PPR_2_hei, DP_I_PPR_2_memtoregi,
       DP_I_PPR_2_memwritei, DP_I_PPR_2_updaterobi, DP_I_PPR_branchi, DP_I_PPR_condi, DP_I_PPR_flagwritei,
       DP_I_PPR_hei, DP_I_PPR_memtoregi, DP_I_PPR_memwritei, DP_I_PPR_updaterobi, Hazard_Unit_clrd,
       Hazard_Unit_clrrrd, Hazard_Unit_stalld, Hazard_Unit_stallf, Hazard_Unit_stallrrd,
       I_WB_PPR_2_memtoregw, I_WB_PPR_2_memwritew, I_WB_PPR_2_updaterobw, I_WB_PPR_flagwritew,
       I_WB_PPR_updaterobw, Is_I_Format_lt, Is_NOP_eq, Issue_Queue_full, not_1_out, not_2_out, not_3_out,
       not_4_out, not_5_out, not_6_out, not_7_out, not_8_out, RMT_r1v_out, RMT_r2v_out, xnor_1_out;
  wire [1:0] Control_Unit_2_aluctrld, Control_Unit_aluctrld, DP_I_PPR_2_aluopi, DP_I_PPR_aluopi;
  wire [2:0] IF_ID_RR_RD_PPR_insn_out, IF_ID_RR_RD_PPR_insn_out_3, IF_ID_RR_RD_PPR_insn_out_4;
  wire [3:0] ALU_2_flag, ALU_flag, Condition_Unit_2_flagsm, Condition_Unit_flagsm, driver_8_out,
       I_WB_PPR_2_flagsw, I_WB_PPR_flagsw;
  wire [4:0] DP_I_PPR_2_dsttagi, DP_I_PPR_dsttagi, driver_2_out, driver_4_out, I_WB_PPR_2_dsttagw,
       I_WB_PPR_dsttagw, RMT_r1robtag_out, RMT_r2robtag_out, ROB_headidx, ROB_tailidx, RRD_DP_PPR_tagdstdp;
  wire [15:0] ALU_2_result, ALU_result, ARF_out1, ARF_out2, bitextender_1_out, bitextender_2_out,
       condensed_drrd_forwarding_1_reg_tag, condensed_drrd_forwarding_2_reg_tag, DP_I_PPR_2_rai,
       DP_I_PPR_2_rbi, DP_I_PPR_rai, DP_I_PPR_rbi, driver_3_out, driver_5_out, driver_6_out, driver_7_out,
       I_WB_PPR_2_aluresultw, I_WB_PPR_2_writedataw, I_WB_PPR_aluresultw, multiplexer_1_out,
       multiplexer_2_out, multiplexer_3_out, multiplexer_5_out, PC_q, plus_1_s, RAM_d1, RAM_d2, ROB_headdata,
       RRD_DP_PPR_insndp, RRD_DP_PPR_ra_tag1dp, RRD_DP_PPR_rb_tag2dp;
  wire [15:3] IF_ID_RR_RD_PPR_insn_out_2;
  wire [23:6] RRD_DP_PPR_r2vdp;
  wire [37:22] IF_ID_RR_RD_PPR_pc_out;
  wire [42:16] ROB_headdata_2;
  wire [42:21] I_WB_PPR_2_hew, I_WB_PPR_hew;
  wire [48:0] driver_1_out, Issue_Queue_nextdata_iralu, Issue_Queue_nextdata_rmem, multiplexer_4_out;

  Seven_Seg_Hex seven_seg_hex_1 (.d(PC_q[11:8]), .dp(1'b0));
  Seven_Seg_Hex seven_seg_hex_2 (.d(PC_q[15:12]), .dp(1'b0));
  Seven_Seg_Hex seven_seg_hex_3 (.d(PC_q[3:0]), .dp(1'b0));
  Seven_Seg_Hex seven_seg_hex_4 (.d(PC_q[7:4]), .dp(1'b0));
  not not_1 (not_1_out, Hazard_Unit_stallf);
  Multiplexer #(.Bits(16)) multiplexer_1 (
    .sel(and_1_out), .in_0(plus_1_s), .in_1(ROB_headdata), .out(multiplexer_1_out));
  Register #(.Bits(16), .isProgramCounter("true")) PC (.D(multiplexer_1_out), .C(CLK), .en(not_1_out), .Q(PC_q));
  Add #(.Bits(16)) plus_1 (.a(16'h1), .b(PC_q), .c_i(1'b0), .s(plus_1_s));  // open: c_o
  RAMDualAccess #(.AddrBits(16), .isProgramMemory("true"), .Bits(16)) RAM (
    .str(I_WB_PPR_2_memwritew), .C(CLK), .ld(I_WB_PPR_2_memtoregw), .A1(I_WB_PPR_2_aluresultw),
    .Din1(I_WB_PPR_2_writedataw), .A2(PC_q), .D1(RAM_d1), .D2(RAM_d2));
  ifd_rrd_ppr IF_ID_RR_RD_PPR (
    .CLK(CLK), .INSN_IN(RAM_d2), .PC_IN(PC_q),
    .INSN_OUT({IF_ID_RR_RD_PPR_insn_out_2[15:11], IF_ID_RR_RD_PPR_insn_out_4, IF_ID_RR_RD_PPR_insn_out_2[7], IF_ID_RR_RD_PPR_insn_out_3, IF_ID_RR_RD_PPR_insn_out_2[3], IF_ID_RR_RD_PPR_insn_out}),
    .PC_OUT(IF_ID_RR_RD_PPR_pc_out), .CLR(Hazard_Unit_clrd), .EN(not_2_out));
  not not_2 (not_2_out, Hazard_Unit_stalld);
  Comparator #(.Bits(16)) comparator_1 (
    .a({IF_ID_RR_RD_PPR_insn_out_2[15:11], IF_ID_RR_RD_PPR_insn_out_4, IF_ID_RR_RD_PPR_insn_out_2[7], IF_ID_RR_RD_PPR_insn_out_3, IF_ID_RR_RD_PPR_insn_out_2[3], IF_ID_RR_RD_PPR_insn_out}),
    .b({16{1'b0}}), .eq(comparator_1_eq));  // open: gt, lt
  not not_3 (not_3_out, comparator_1_eq);
  and and_1 (and_1_out, xnor_1_out, comparator_2_eq);
  Multiplexer #(.Bits(16)) multiplexer_2 (
    .sel(I_WB_PPR_hew[21]), .in_0({16{1'b0}}), .in_1(I_WB_PPR_aluresultw), .out(multiplexer_2_out));
  not not_4 (not_4_out, comparator_2_eq);
  and and_2 (and_2_out, xnor_1_out, not_4_out);
  BitExtender #(.inputBits(4)) bitextender_1 (.in(ROB_headdata_2[41:38]), .out(bitextender_1_out));
  Multiplexer #(.Bits(16)) multiplexer_3 (
    .sel(comparator_2_eq), .in_0(ROB_headdata_2[37:22]), .in_1(ROB_headdata), .out(multiplexer_3_out));
  Comparator #(.Bits(3)) comparator_2 (.a(3'b111), .b(ROB_headdata_2[18:16]), .eq(comparator_2_eq));  // open: gt, lt
  rename_map_table RMT (
    .CLK(CLK), .RS1(IF_ID_RR_RD_PPR_insn_out_3), .RS2(IF_ID_RR_RD_PPR_insn_out),
    .WS(IF_ID_RR_RD_PPR_insn_out_4), .V_IN(not_3_out), .ROBTag_IN(ROB_tailidx),
    .UpdateDst(ROB_headdata_2[18:16]), .UpdateTag(ROB_headidx), .Update_EN(xnor_1_out),
    .R1V_OUT(RMT_r1v_out), .R1ROBTag_OUT(RMT_r1robtag_out), .R2V_OUT(RMT_r2v_out),
    .R2ROBTag_OUT(RMT_r2robtag_out), .CLR(ROB_headdata_2[21]));
  reg_file ARF (
    .RS1(IF_ID_RR_RD_PPR_insn_out_3), .RS2(IF_ID_RR_RD_PPR_insn_out), .WS(ROB_headdata_2[18:16]),
    .WE(and_2_out), .IN(ROB_headdata), .CLK(CLK), .FL_IN(bitextender_1_out),
    .FL_EN(IF_ID_RR_RD_PPR_insn_out_2[15]), .PC_IN(multiplexer_3_out), .HE(ROB_headdata_2[42]),
    .OUT1(ARF_out1), .OUT2(ARF_out2));
  circular_buffer ROB (
    .TailWE(not_3_out),
    .TailData({{5{1'b0}}, IF_ID_RR_RD_PPR_pc_out, 3'b000, IF_ID_RR_RD_PPR_insn_out_4, {16{1'b0}}}),
    .HeadRE(xnor_1_out), .UpdateWE_IRALU(I_WB_PPR_updaterobw),
    .UpdateData_IRALU({I_WB_PPR_hew[42], driver_8_out, multiplexer_2_out, I_WB_PPR_hew[21], 5'b01000, I_WB_PPR_aluresultw}),
    .UpdateA_IRALU(I_WB_PPR_dsttagw), .CLK(CLK), .CLR(ROB_headdata_2[21]),
    .UpdateData_RMEM({I_WB_PPR_2_hew[42], I_WB_PPR_2_flagsw, {16{1'b0}}, I_WB_PPR_2_hew[21], 5'b01000, multiplexer_5_out}),
    .UpdateWE_RMEM(I_WB_PPR_2_updaterobw), .UpdateA_RMEM(I_WB_PPR_2_dsttagw),
    .HeadData({ROB_headdata_2, ROB_headdata}), .TailIdx(ROB_tailidx), .HeadIdx(ROB_headidx));
  xnor xnor_1 (xnor_1_out, ROB_headdata_2[19], 1'b1);
  condensed_drrd_forwarding condensed_drrd_forwarding_1 (
    .V_IN(RMT_r1v_out), .ROBTag(RMT_r1robtag_out), .RegOut(ARF_out1), .RegA(IF_ID_RR_RD_PPR_insn_out_3),
    .UpdateDst(ROB_headdata_2[18:16]), .UpdateData(ROB_headdata), .V_OUT(condensed_drrd_forwarding_1_v_out),
    .Reg_Tag(condensed_drrd_forwarding_1_reg_tag));
  condensed_drrd_forwarding condensed_drrd_forwarding_2 (
    .V_IN(RMT_r2v_out), .ROBTag(RMT_r2robtag_out), .RegOut(ARF_out2), .RegA(IF_ID_RR_RD_PPR_insn_out),
    .UpdateDst(ROB_headdata_2[18:16]), .UpdateData(ROB_headdata), .V_OUT(condensed_drrd_forwarding_2_v_out),
    .Reg_Tag(condensed_drrd_forwarding_2_reg_tag));
  rrd_dp_ppr RRD_DP_PPR (
    .CLK(CLK), .R1VRRD(condensed_drrd_forwarding_1_v_out), .R2VRRD(condensed_drrd_forwarding_2_v_out),
    .Ra_Tag1RRD(condensed_drrd_forwarding_1_reg_tag), .Rb_Tag2RRD(condensed_drrd_forwarding_2_reg_tag),
    .TagDstRRD(ROB_tailidx),
    .INSNRRD({IF_ID_RR_RD_PPR_insn_out_2[15:11], IF_ID_RR_RD_PPR_insn_out_4, IF_ID_RR_RD_PPR_insn_out_2[7], IF_ID_RR_RD_PPR_insn_out_3, IF_ID_RR_RD_PPR_insn_out_2[3], IF_ID_RR_RD_PPR_insn_out}),
    .R1VDP(RRD_DP_PPR_r2vdp[6]), .R2VDP(RRD_DP_PPR_r2vdp[23]), .Ra_Tag1DP(RRD_DP_PPR_ra_tag1dp),
    .Rb_Tag2DP(RRD_DP_PPR_rb_tag2dp), .TagDstDP(RRD_DP_PPR_tagdstdp), .INSNDP(RRD_DP_PPR_insndp),
    .CLR(Hazard_Unit_clrrrd), .EN(not_5_out));
  not not_5 (not_5_out, Hazard_Unit_stallrrd);
  BitExtender bitextender_2 (.in(RRD_DP_PPR_insndp[7:0]), .out(bitextender_2_out));
  hazard_unit_ooo Hazard_Unit (
    .IQFull(Issue_Queue_full), .BranchW(I_WB_PPR_hew[21]), .StallF(Hazard_Unit_stallf),
    .StallD(Hazard_Unit_stalld), .StallRRD(Hazard_Unit_stallrrd), .CLRD(Hazard_Unit_clrd),
    .CLRRRD(Hazard_Unit_clrrrd));
  Comparator #(.Bits(16)) Is_NOP (.a(RRD_DP_PPR_insndp), .b({16{1'b0}}), .eq(Is_NOP_eq));  // open: gt, lt
  Comparator #(.Bits(4)) Is_I_Format (.a(RRD_DP_PPR_insndp[15:12]), .b(4'b0010), .lt(Is_I_Format_lt));  // open: gt, eq
  not not_6 (not_6_out, Is_I_Format_lt);
  Multiplexer #(.Bits(49)) multiplexer_4 (
    .sel(not_6_out),
    .in_0({1'b1, RRD_DP_PPR_insndp[10:8], RRD_DP_PPR_insndp[11], RRD_DP_PPR_insndp[15:12], bitextender_2_out, 18'h20001, RRD_DP_PPR_tagdstdp, 1'b1}),
    .in_1({RRD_DP_PPR_insndp[15], RRD_DP_PPR_insndp[10:8], RRD_DP_PPR_insndp[11], RRD_DP_PPR_insndp[15:12], RRD_DP_PPR_rb_tag2dp, RRD_DP_PPR_r2vdp[23], RRD_DP_PPR_ra_tag1dp, RRD_DP_PPR_r2vdp[6], RRD_DP_PPR_tagdstdp, 1'b1}),
    .out(multiplexer_4_out));
  not not_7 (not_7_out, Is_NOP_eq);
  assign driver_1_out = not_7_out ? multiplexer_4_out : 49'bz;  // Driver driver_1
  PullDown #(.Bits(49)) pulldown_1 (.out(driver_1_out));
  issue_queue Issue_Queue (
    .CLK(CLK), .CLRNext(1'b1), .BC_Tag_IRALU(I_WB_PPR_dsttagw), .BC_Result_IRALU(I_WB_PPR_aluresultw),
    .BC_WE_IRALU(I_WB_PPR_updaterobw), .BC_Tag_RMEM(I_WB_PPR_2_dsttagw), .BC_Result_RMEM(multiplexer_5_out),
    .BC_WE_RMEM(I_WB_PPR_2_updaterobw), .TailData(driver_1_out), .Tail_WE(not_8_out),
    .NextData_IRALU(Issue_Queue_nextdata_iralu), .NextData_RMEM(Issue_Queue_nextdata_rmem),
    .Full(Issue_Queue_full), .CLR(ROB_headdata_2[21]));  // open: Empty
  not not_8 (not_8_out, Issue_Queue_full);
  control_unit_ooo Control_Unit (
    .MemToRegD(Control_Unit_memtoregd), .MemWriteD(Control_Unit_memwrited), .ALUCtrlD(Control_Unit_aluctrld),
    .BranchD(Control_Unit_branchd), .FlagWriteD(Control_Unit_flagwrited), .SethD(Control_Unit_sethd),
    .UpdateROB(Control_Unit_updaterob), .OPCode(Issue_Queue_nextdata_iralu[43:40]),
    .Rd(Issue_Queue_nextdata_iralu[47:45]));
  control_unit_ooo Control_Unit_2 (
    .MemToRegD(Control_Unit_2_memtoregd), .MemWriteD(Control_Unit_2_memwrited),
    .ALUCtrlD(Control_Unit_2_aluctrld), .BranchD(Control_Unit_2_branchd),
    .FlagWriteD(Control_Unit_2_flagwrited), .SethD(Control_Unit_2_sethd),
    .UpdateROB(Control_Unit_2_updaterob), .OPCode(Issue_Queue_nextdata_rmem[43:40]),
    .Rd(Issue_Queue_nextdata_rmem[47:45]));
  assign driver_2_out = Control_Unit_updaterob ? Issue_Queue_nextdata_iralu[5:1] : 5'bz;  // Driver driver_2
  assign driver_3_out = Control_Unit_updaterob ? Issue_Queue_nextdata_iralu[22:7] : 16'bz;  // Driver driver_3
  assign driver_4_out = Control_Unit_2_updaterob ? Issue_Queue_nextdata_rmem[5:1] : 5'bz;  // Driver driver_4
  assign driver_5_out = Control_Unit_2_updaterob ? Issue_Queue_nextdata_rmem[22:7] : 16'bz;  // Driver driver_5
  assign driver_6_out = Control_Unit_updaterob ? Issue_Queue_nextdata_iralu[39:24] : 16'bz;  // Driver driver_6
  PullDown #(.Bits(5)) pulldown_2 (.out(driver_2_out));
  assign driver_7_out = Control_Unit_2_updaterob ? Issue_Queue_nextdata_rmem[39:24] : 16'bz;  // Driver driver_7
  PullDown #(.Bits(5)) pulldown_3 (.out(driver_4_out));
  PullDown #(.Bits(16)) pulldown_4 (.out(driver_3_out));
  PullDown #(.Bits(16)) pulldown_5 (.out(driver_6_out));
  PullDown #(.Bits(16)) pulldown_6 (.out(driver_5_out));
  PullDown #(.Bits(16)) pulldown_7 (.out(driver_7_out));
  dp_i_ppr DP_I_PPR (
    .CLK(CLK), .DstTagDP(driver_2_out), .RaDP(driver_3_out), .RbDP(driver_6_out),
    .ALUOPDP(Control_Unit_aluctrld), .BranchDP(Control_Unit_branchd), .FlagWriteDP(Control_Unit_flagwrited),
    .HEDP(Control_Unit_sethd), .CondDP(Issue_Queue_nextdata_iralu[44]), .MemToRegDP(Control_Unit_memtoregd),
    .MemWriteDP(Control_Unit_memwrited), .UpdateROBDP(Control_Unit_updaterob), .DstTagI(DP_I_PPR_dsttagi),
    .RaI(DP_I_PPR_rai), .RbI(DP_I_PPR_rbi), .ALUOPI(DP_I_PPR_aluopi), .BranchI(DP_I_PPR_branchi),
    .FlagWriteI(DP_I_PPR_flagwritei), .HEI(DP_I_PPR_hei), .CondI(DP_I_PPR_condi),
    .MemToRegI(DP_I_PPR_memtoregi), .MemWriteI(DP_I_PPR_memwritei), .UpdateROBI(DP_I_PPR_updaterobi));
  dp_i_ppr DP_I_PPR_2 (
    .CLK(CLK), .DstTagDP(driver_4_out), .RaDP(driver_5_out), .RbDP(driver_7_out),
    .ALUOPDP(Control_Unit_2_aluctrld), .BranchDP(Control_Unit_2_branchd),
    .FlagWriteDP(Control_Unit_2_flagwrited), .HEDP(Control_Unit_2_sethd),
    .CondDP(Issue_Queue_nextdata_rmem[44]), .MemToRegDP(Control_Unit_2_memtoregd),
    .MemWriteDP(Control_Unit_2_memwrited), .UpdateROBDP(Control_Unit_2_updaterob),
    .DstTagI(DP_I_PPR_2_dsttagi), .RaI(DP_I_PPR_2_rai), .RbI(DP_I_PPR_2_rbi), .ALUOPI(DP_I_PPR_2_aluopi),
    .BranchI(DP_I_PPR_2_branchi), .FlagWriteI(DP_I_PPR_2_flagwritei), .HEI(DP_I_PPR_2_hei),
    .CondI(DP_I_PPR_2_condi), .MemToRegI(DP_I_PPR_2_memtoregi), .MemWriteI(DP_I_PPR_2_memwritei),
    .UpdateROBI(DP_I_PPR_2_updaterobi));
  alu ALU (.A(DP_I_PPR_rai), .B(DP_I_PPR_rbi), .ALUOP(DP_I_PPR_aluopi), .RESULT(ALU_result), .FLAG(ALU_flag));
  alu ALU_2 (
    .A(DP_I_PPR_2_rai), .B(DP_I_PPR_2_rbi), .ALUOP(DP_I_PPR_2_aluopi), .RESULT(ALU_2_result),
    .FLAG(ALU_2_flag));
  condition_unit Condition_Unit (
    .FlagWriteE(DP_I_PPR_flagwritei), .CondE(DP_I_PPR_condi), .FlagsE(driver_8_out), .ALUFlags(ALU_flag),
    .FlagsM(Condition_Unit_flagsm), .CondExE(Condition_Unit_condexe));
  condition_unit Condition_Unit_2 (
    .FlagWriteE(DP_I_PPR_2_flagwritei), .CondE(DP_I_PPR_2_condi), .FlagsE(I_WB_PPR_2_flagsw),
    .ALUFlags(ALU_2_flag), .FlagsM(Condition_Unit_2_flagsm), .CondExE(Condition_Unit_2_condexe));
  and and_3 (and_3_out, DP_I_PPR_memtoregi, Condition_Unit_condexe);
  and and_4 (and_4_out, DP_I_PPR_memwritei, Condition_Unit_condexe);
  and and_5 (and_5_out, DP_I_PPR_branchi, Condition_Unit_condexe);
  and and_6 (and_6_out, DP_I_PPR_2_memtoregi, Condition_Unit_2_condexe);
  and and_7 (and_7_out, DP_I_PPR_2_memwritei, Condition_Unit_2_condexe);
  and and_8 (and_8_out, DP_I_PPR_2_branchi, Condition_Unit_2_condexe);
  i_wb_ppr I_WB_PPR (
    .CLK(CLK), .DstTagI(DP_I_PPR_dsttagi), .HEI(DP_I_PPR_hei), .BCWriteI(Condition_Unit_condexe),
    .MemToRegI(and_3_out), .MemWriteI(and_4_out), .WriteDataI(DP_I_PPR_rbi), .ALUResultI(ALU_result),
    .FlagsI(Condition_Unit_flagsm), .FlagWriteI(DP_I_PPR_flagwritei), .BranchI(and_5_out),
    .UpdateROBI(DP_I_PPR_updaterobi), .DstTagW(I_WB_PPR_dsttagw), .HEW(I_WB_PPR_hew[42]),
    .ALUResultW(I_WB_PPR_aluresultw), .FlagsW(I_WB_PPR_flagsw), .FlagWriteW(I_WB_PPR_flagwritew),
    .BranchW(I_WB_PPR_hew[21]), .UpdateROBW(I_WB_PPR_updaterobw));  // open: BCWriteW, MemToRegW, MemWriteW, WriteDataW
  i_wb_ppr I_WB_PPR_2 (
    .CLK(CLK), .DstTagI(DP_I_PPR_2_dsttagi), .HEI(DP_I_PPR_2_hei), .BCWriteI(Condition_Unit_2_condexe),
    .MemToRegI(and_6_out), .MemWriteI(and_7_out), .WriteDataI(DP_I_PPR_2_rbi), .ALUResultI(ALU_2_result),
    .FlagsI(Condition_Unit_2_flagsm), .FlagWriteI(DP_I_PPR_2_flagwritei), .BranchI(and_8_out),
    .UpdateROBI(DP_I_PPR_2_updaterobi), .DstTagW(I_WB_PPR_2_dsttagw), .HEW(I_WB_PPR_2_hew[42]),
    .MemToRegW(I_WB_PPR_2_memtoregw), .MemWriteW(I_WB_PPR_2_memwritew), .WriteDataW(I_WB_PPR_2_writedataw),
    .ALUResultW(I_WB_PPR_2_aluresultw), .FlagsW(I_WB_PPR_2_flagsw), .BranchW(I_WB_PPR_2_hew[21]),
    .UpdateROBW(I_WB_PPR_2_updaterobw));  // open: BCWriteW, FlagWriteW
  Multiplexer #(.Bits(16)) multiplexer_5 (
    .sel(I_WB_PPR_2_memtoregw), .in_0(I_WB_PPR_2_aluresultw), .in_1(RAM_d1), .out(multiplexer_5_out));
  assign driver_8_out = I_WB_PPR_flagwritew ? I_WB_PPR_flagsw : 4'bz;  // Driver driver_8
  PullDown #(.Bits(4)) pulldown_8 (.out(driver_8_out));
  // Probe DstTag on I_WB_PPR_dsttagw
  // Probe CDB on I_WB_PPR_aluresultw

  // Notes on the sheet:
  //   Update is masked into ROB with
  //   an OR with the existing value
  //   0-15: Value
  //   16-18: Dst
  //   19: Rdy
  //   20: Exc
  //   21: Misp
  //   22-37: PC
  //   38-41: Flags
  //   42: HE
  //   For I-Format insns, we can just 
  //   put the Imm8 as R2 and mark it,
  //   also using 0 for R1 with it marked
  //   0: Valid
  //   1-5: Dst tag
  //   6: Rs1 rdy
  //   7-22: Rs1 tag/value
  //   23: Rs2 rdy
  //   24-39: Rs2 tag/value
  //   40-43: OPCode
  //   44: Cond
  //   45-57: Rd
  //   48: Exec type (1: I/R-ALU, 0: R-MEM)
  //   TODO: Dual issue for ALU R-Format and I-Format
  //   with LD/ST R-Format in parallel will need
  //   two data entries read at a time. Check if
  //   both are parallelisable via the opcode. Alternative
  //   is to have two issue queues, one for LD/ST and the
  //   other for regular. Potential solution is to copy
  //   warp scheduler from GPU implementation and
  //   cut down threads in SM to 2. Need CNVG/DIVG
  //   handler at the end as well.
endmodule
