// Digital circuit entry_formatter.dig as structural Verilog
module entry_formatter (
  input  [15:0] INSN,
  input  [15:0] TagDst,
  output [39:0] TailData
);

  wire Is_I_Format_eq, not_1_out;
  wire [15:0] bitextender_1_out;
  wire [39:0] undriven;

  Comparator Is_I_Format (.a(INSN[12]), .b(1'b0), .eq(Is_I_Format_eq));  // open: gt, lt
  BitExtender bitextender_1 (.in(INSN[7:0]), .out(bitextender_1_out));
  not not_1 (not_1_out, Is_I_Format_eq);
  Multiplexer #(.Bits(40)) multiplexer_1 (
    .sel(not_1_out), .in_0({bitextender_1_out, 18'h20001, TagDst[4:0], 1'b1}), .in_1(undriven), .out(TailData));
  // Pins of 1 and 4 bits meet at INSN[15:12]
  // Pins of 1 and 4 bits meet at 4'b0000
  // Pins of 5 and 16 bits meet at TagDst
endmodule
