// Digital circuit i_wb_ppr.dig as structural Verilog
module i_wb_ppr (
  input  CLK,
  input  MemToRegI,
  input  MemWriteI,
  input  [15:0] WriteDataI,
  input  [15:0] ALUResultI,
  input  [4:0] DstTagI,
  input  HEI,
  input  BCWriteI,
  input  [3:0] FlagsI,
  input  FlagWriteI,
  input  BranchI,
  input  UpdateROBI,
  output MemToRegW,
  output MemWriteW,
  output [15:0] WriteDataW,
  output [15:0] ALUResultW,
  output [4:0] DstTagW,
  output HEW,
  output BCWriteW,
  output [3:0] FlagsW,
  output FlagWriteW,
  output BranchW,
  output UpdateROBW
);

  Register #(.Bits(5)) DstTag (.D(DstTagI), .C(CLK), .en(1'b1), .Q(DstTagW));
  Register HE (.D(HEI), .C(CLK), .en(1'b1), .Q(HEW));
  Register BCWrite (.D(BCWriteI), .C(CLK), .en(1'b1), .Q(BCWriteW));
  Register MemToReg (.D(MemToRegI), .C(CLK), .en(1'b1), .Q(MemToRegW));
  Register MemWrite (.D(MemWriteI), .C(CLK), .en(1'b1), .Q(MemWriteW));
  Register #(.Bits(16)) WriteData (.D(WriteDataI), .C(CLK), .en(1'b1), .Q(WriteDataW));
  Register #(.Bits(16)) ALUResult (.D(ALUResultI), .C(CLK), .en(1'b1), .Q(ALUResultW));
  Register #(.Bits(4)) Flags (.D(FlagsI), .C(CLK), .en(1'b1), .Q(FlagsW));
  Register FlagWrite (.D(FlagWriteI), .C(CLK), .en(1'b1), .Q(FlagWriteW));
  Register Branch (.D(BranchI), .C(CLK), .en(1'b1), .Q(BranchW));
  Register UpdateROB (.D(UpdateROBI), .C(CLK), .en(1'b1), .Q(UpdateROBW));

  // Notes on the sheet:
  //   I/WB PPR
endmodule
