// Digital circuit if_id_ppr.dig as structural Verilog
module if_id_ppr (
  input  [15:0] INSN_IN,
  input  CLK,
  input  EN,
  input  CLR,
  output [15:0] INSN_OUT
);

  wire [15:0] multiplexer_1_out;

  Multiplexer #(.Bits(16)) multiplexer_1 (.sel(CLR), .in_0(INSN_IN), .in_1({16{1'b0}}), .out(multiplexer_1_out));
  Register #(.Bits(16)) INSN (.D(multiplexer_1_out), .C(CLK), .en(EN), .Q(INSN_OUT));

  // Notes on the sheet:
  //   IF/ID PRR
endmodule
