// Digital circuit iq_update_checker.dig as structural Verilog
module iq_update_checker (
  input  [4:0] BC_Tag_IRALU,
  input  [15:0] BC_Result_IRALU,
  input  [48:0] EntryValue_IN,
  input  BC_EN_IRALU,
  input  [4:0] BC_Tag_RMEM,
  input  [15:0] BC_Result_RMEM,
  input  BC_EN_RMEM,
  output [48:0] EntryValue_OUT
);

  wire and_1_out, and_2_out, and_3_out, and_4_out, and_5_out, comparator_1_eq, comparator_2_eq,
       comparator_3_eq, comparator_4_eq, multiplexer_1_out, multiplexer_3_out, multiplexer_5_out,
       multiplexer_7_out, nand_1_out, not_1_out, not_2_out, not_3_out, not_4_out, or_1_out;
  wire [15:0] multiplexer_2_out, multiplexer_4_out, multiplexer_6_out, multiplexer_8_out, multiplexer_10_out,
       multiplexer_12_out;
  wire [23:0] multiplexer_9_out;

  not not_1 (not_1_out, EntryValue_IN[6]);
  not not_2 (not_2_out, EntryValue_IN[6]);
  not not_3 (not_3_out, EntryValue_IN[23]);
  not not_4 (not_4_out, EntryValue_IN[23]);
  Comparator #(.Bits(5)) comparator_1 (.a(BC_Tag_RMEM), .b(EntryValue_IN[11:7]), .eq(comparator_1_eq));  // open: gt, lt
  Comparator #(.Bits(5)) comparator_2 (
    .a(BC_Tag_IRALU), .b(EntryValue_IN[11:7]), .eq(comparator_2_eq));  // open: gt, lt
  Comparator #(.Bits(5)) comparator_3 (
    .a(BC_Tag_RMEM), .b(EntryValue_IN[28:24]), .eq(comparator_3_eq));  // open: gt, lt
  Comparator #(.Bits(5)) comparator_4 (
    .a(BC_Tag_IRALU), .b(EntryValue_IN[28:24]), .eq(comparator_4_eq));  // open: gt, lt
  and and_1 (and_1_out, not_1_out, comparator_1_eq);
  and and_2 (and_2_out, not_2_out, comparator_2_eq);
  and and_3 (and_3_out, not_3_out, comparator_3_eq);
  and and_4 (and_4_out, not_4_out, comparator_4_eq);
  Multiplexer multiplexer_1 (.sel(and_1_out), .in_0(EntryValue_IN[6]), .in_1(not_1_out), .out(multiplexer_1_out));
  Multiplexer #(.Bits(16)) multiplexer_2 (
    .sel(and_1_out), .in_0(EntryValue_IN[22:7]), .in_1(BC_Result_RMEM), .out(multiplexer_2_out));
  Multiplexer multiplexer_3 (.sel(and_2_out), .in_0(EntryValue_IN[6]), .in_1(not_2_out), .out(multiplexer_3_out));
  Multiplexer #(.Bits(16)) multiplexer_4 (
    .sel(and_2_out), .in_0(EntryValue_IN[22:7]), .in_1(BC_Result_IRALU), .out(multiplexer_4_out));
  Multiplexer multiplexer_5 (.sel(and_3_out), .in_0(EntryValue_IN[23]), .in_1(not_3_out), .out(multiplexer_5_out));
  Multiplexer #(.Bits(16)) multiplexer_6 (
    .sel(and_3_out), .in_0(EntryValue_IN[39:24]), .in_1(BC_Result_RMEM), .out(multiplexer_6_out));
  Multiplexer multiplexer_7 (.sel(and_4_out), .in_0(EntryValue_IN[23]), .in_1(not_4_out), .out(multiplexer_7_out));
  Multiplexer #(.Bits(16)) multiplexer_8 (
    .sel(and_4_out), .in_0(EntryValue_IN[39:24]), .in_1(BC_Result_IRALU), .out(multiplexer_8_out));
  Multiplexer multiplexer_9 (
    .sel(BC_EN_IRALU), .in_0(multiplexer_1_out), .in_1(multiplexer_3_out), .out(multiplexer_9_out[6]));
  Multiplexer #(.Bits(16)) multiplexer_10 (
    .sel(BC_EN_RMEM), .in_0(multiplexer_2_out), .in_1(multiplexer_4_out), .out(multiplexer_10_out));
  Multiplexer multiplexer_11 (
    .sel(BC_EN_IRALU), .in_0(multiplexer_5_out), .in_1(multiplexer_7_out), .out(multiplexer_9_out[23]));
  Multiplexer #(.Bits(16)) multiplexer_12 (
    .sel(BC_EN_RMEM), .in_0(multiplexer_6_out), .in_1(multiplexer_8_out), .out(multiplexer_12_out));
  or or_1 (or_1_out, BC_EN_IRALU, BC_EN_RMEM);
  nand nand_1 (nand_1_out, multiplexer_9_out[6], multiplexer_9_out[23]);
  and and_5 (and_5_out, or_1_out, EntryValue_IN[0]);
  Multiplexer multiplexer_13 (.sel(and_5_out), .in_0(EntryValue_IN[0]), .in_1(nand_1_out), .out(multiplexer_9_out[0]));
  Multiplexer #(.Bits(49)) multiplexer_14 (
    .sel(and_5_out), .in_0(EntryValue_IN),
    .in_1({EntryValue_IN[48:40], multiplexer_12_out, multiplexer_9_out[23], multiplexer_10_out, multiplexer_9_out[6], EntryValue_IN[5:1], multiplexer_9_out[0]}),
    .out(EntryValue_OUT));

  // Notes on the sheet:
  //   Instruction Queue Update Checker
endmodule
