// Digital circuit issue_queue.dig as structural Verilog
module issue_queue (
  input  CLK,
  input  CLRNext,
  input  Tail_WE,
  input  [48:0] TailData,
  input  [4:0] BC_Tag_IRALU,
  input  [15:0] BC_Result_IRALU,
  input  BC_WE_IRALU,
  input  CLR,
  input  [4:0] BC_Tag_RMEM,
  input  [15:0] BC_Result_RMEM,
  input  BC_WE_RMEM,
  output [48:0] NextData_IRALU,
  output Full,
  output Empty,
  output [48:0] NextData_RMEM
);

  wire and_1_out, and_2_out, and_3_out, and_4_out, comparator_1_eq, comparator_2_eq, demultiplexer_1_out_0,
       demultiplexer_1_out_1, demultiplexer_1_out_2, demultiplexer_3_out_0, demultiplexer_3_out_1,
       demultiplexer_3_out_2, demultiplexer_4_out_0, demultiplexer_4_out_1, demultiplexer_4_out_2,
       demultiplexer_5_out_0, demultiplexer_5_out_1, demultiplexer_6_out_0, demultiplexer_6_out_1,
       demultiplexer_7_out_0, demultiplexer_7_out_1, I_R_ALU_Priority_any, multiplexer_1_out,
       multiplexer_3_out, multiplexer_5_out, not_1_out, or_1_out, or_2_out, or_3_out, or_4_out, or_5_out,
       or_6_out, R_MEM_Priority_any;
  wire [1:0] I_R_ALU_Priority_num, multiplexer_7_out, multiplexer_8_out, R_MEM_Priority_num, Tail_out;
  wire [2:0] IQEntry0_rd_out, IQEntry1_rd_out, IQEntry2_rd_out;
  wire [3:0] IQEntry0_opcode_out, IQEntry1_opcode_out, IQEntry2_opcode_out;
  wire [4:0] IQEntry0_tagdst_out, IQEntry1_tagdst_out, IQEntry2_tagdst_out;
  wire [15:0] IQEntry0_r1tagval_out, IQEntry0_r2tagval_out, IQEntry1_r1tagval_out, IQEntry1_r2tagval_out,
       IQEntry2_r1tagval_out, IQEntry2_r2tagval_out;
  wire [48:0] demultiplexer_2_out_0, demultiplexer_2_out_1, demultiplexer_2_out_2,
       iq_update_checker_1_entryvalue_out, iq_update_checker_2_entryvalue_out,
       iq_update_checker_3_entryvalue_out, iq_update_checker_4_entryvalue_out,
       iq_update_checker_5_entryvalue_out, iq_update_checker_6_entryvalue_out, IQEntry0_r1rdy_out,
       IQEntry1_r1rdy_out, IQEntry2_r1rdy_out, multiplexer_2_out, multiplexer_4_out, multiplexer_6_out;

  Comparator #(.Bits(49)) comparator_1 (.a({49{1'b0}}), .b(TailData), .eq(comparator_1_eq));  // open: gt, lt
  not not_1 (not_1_out, comparator_1_eq);
  and and_1 (and_1_out, not_1_out, Tail_WE);
  Demultiplexer #(.Selector_Bits(2)) demultiplexer_1 (
    .sel(Tail_out), .in(and_1_out), .out_0(demultiplexer_1_out_0), .out_1(demultiplexer_1_out_1),
    .out_2(demultiplexer_1_out_2));  // open: out_3
  Comparator #(.Bits(2)) comparator_2 (.a(Tail_out), .b(2'b10), .eq(comparator_2_eq));  // open: gt, lt
  Counter #(.Bits(2)) Tail (.en(and_1_out), .C(CLK), .clr(comparator_2_eq), .out(Tail_out));  // open: ovf
  Demultiplexer #(.Selector_Bits(2), .Bits(49)) demultiplexer_2 (
    .sel(Tail_out), .in(TailData), .out_0(demultiplexer_2_out_0), .out_1(demultiplexer_2_out_1),
    .out_2(demultiplexer_2_out_2));  // open: out_3
  // Probe IQTail on Tail_out
  Demultiplexer #(.Selector_Bits(2)) demultiplexer_3 (
    .sel(multiplexer_8_out), .in(CLRNext), .out_0(demultiplexer_3_out_0), .out_1(demultiplexer_3_out_1),
    .out_2(demultiplexer_3_out_2));  // open: out_3
  Demultiplexer #(.Selector_Bits(2)) demultiplexer_4 (
    .sel(multiplexer_7_out), .in(CLRNext), .out_0(demultiplexer_4_out_0), .out_1(demultiplexer_4_out_1),
    .out_2(demultiplexer_4_out_2));  // open: out_3
  or or_1 (or_1_out, demultiplexer_3_out_2, demultiplexer_4_out_2);
  or or_2 (or_2_out, demultiplexer_3_out_1, demultiplexer_4_out_1);
  or or_3 (or_3_out, demultiplexer_3_out_0, demultiplexer_4_out_0);
  iq_update_checker iq_update_checker_1 (
    .BC_Result_IRALU(BC_Result_IRALU), .BC_Tag_IRALU(BC_Tag_IRALU), .BC_EN_IRALU(BC_WE_IRALU),
    .BC_Result_RMEM(BC_Result_RMEM), .BC_Tag_RMEM(BC_Tag_RMEM), .BC_EN_RMEM(BC_WE_RMEM),
    .EntryValue_IN({IQEntry0_r1rdy_out[48], IQEntry0_rd_out, IQEntry0_r1rdy_out[44], IQEntry0_opcode_out, IQEntry0_r2tagval_out, IQEntry0_r1rdy_out[23], IQEntry0_r1tagval_out, IQEntry0_r1rdy_out[6], IQEntry0_tagdst_out, IQEntry0_r1rdy_out[0]}),
    .EntryValue_OUT(iq_update_checker_1_entryvalue_out));
  iq_update_checker iq_update_checker_2 (
    .BC_Result_IRALU(BC_Result_IRALU), .BC_Tag_IRALU(BC_Tag_IRALU), .BC_EN_IRALU(BC_WE_IRALU),
    .BC_Result_RMEM(BC_Result_RMEM), .BC_Tag_RMEM(BC_Tag_RMEM), .BC_EN_RMEM(BC_WE_RMEM),
    .EntryValue_IN(demultiplexer_2_out_0), .EntryValue_OUT(iq_update_checker_2_entryvalue_out));
  iq_update_checker iq_update_checker_3 (
    .BC_Result_IRALU(BC_Result_IRALU), .BC_Tag_IRALU(BC_Tag_IRALU), .BC_EN_IRALU(BC_WE_IRALU),
    .BC_Result_RMEM(BC_Result_RMEM), .BC_Tag_RMEM(BC_Tag_RMEM), .BC_EN_RMEM(BC_WE_RMEM),
    .EntryValue_IN({IQEntry1_r1rdy_out[48], IQEntry1_rd_out, IQEntry1_r1rdy_out[44], IQEntry1_opcode_out, IQEntry1_r2tagval_out, IQEntry1_r1rdy_out[23], IQEntry1_r1tagval_out, IQEntry1_r1rdy_out[6], IQEntry1_tagdst_out, IQEntry1_r1rdy_out[0]}),
    .EntryValue_OUT(iq_update_checker_3_entryvalue_out));
  iq_update_checker iq_update_checker_4 (
    .BC_Result_IRALU(BC_Result_IRALU), .BC_Tag_IRALU(BC_Tag_IRALU), .BC_EN_IRALU(BC_WE_IRALU),
    .BC_Result_RMEM(BC_Result_RMEM), .BC_Tag_RMEM(BC_Tag_RMEM), .BC_EN_RMEM(BC_WE_RMEM),
    .EntryValue_IN(demultiplexer_2_out_1), .EntryValue_OUT(iq_update_checker_4_entryvalue_out));
  iq_update_checker iq_update_checker_5 (
    .BC_Result_IRALU(BC_Result_IRALU), .BC_Tag_IRALU(BC_Tag_IRALU), .BC_EN_IRALU(BC_WE_IRALU),
    .BC_Result_RMEM(BC_Result_RMEM), .BC_Tag_RMEM(BC_Tag_RMEM), .BC_EN_RMEM(BC_WE_RMEM),
    .EntryValue_IN({IQEntry2_r1rdy_out[48], IQEntry2_rd_out, IQEntry2_r1rdy_out[44], IQEntry2_opcode_out, IQEntry2_r2tagval_out, IQEntry2_r1rdy_out[23], IQEntry2_r1tagval_out, IQEntry2_r1rdy_out[6], IQEntry2_tagdst_out, IQEntry2_r1rdy_out[0]}),
    .EntryValue_OUT(iq_update_checker_5_entryvalue_out));
  iq_update_checker iq_update_checker_6 (
    .BC_Result_IRALU(BC_Result_IRALU), .BC_Tag_IRALU(BC_Tag_IRALU), .BC_EN_IRALU(BC_WE_IRALU),
    .BC_Result_RMEM(BC_Result_RMEM), .BC_Tag_RMEM(BC_Tag_RMEM), .BC_EN_RMEM(BC_WE_RMEM),
    .EntryValue_IN(demultiplexer_2_out_2), .EntryValue_OUT(iq_update_checker_6_entryvalue_out));
  // Probe IQE0_CLR-SWITCH on demultiplexer_1_out_0
  Multiplexer multiplexer_1 (.sel(demultiplexer_1_out_0), .in_0(or_1_out), .in_1(1'b0), .out(multiplexer_1_out));
  Multiplexer #(.Bits(49)) multiplexer_2 (
    .sel(demultiplexer_1_out_0), .in_0(iq_update_checker_1_entryvalue_out),
    .in_1(iq_update_checker_2_entryvalue_out), .out(multiplexer_2_out));
  // Probe IQE1_CLR-SWITCH on demultiplexer_1_out_1
  Multiplexer multiplexer_3 (.sel(demultiplexer_1_out_1), .in_0(or_2_out), .in_1(1'b0), .out(multiplexer_3_out));
  Multiplexer #(.Bits(49)) multiplexer_4 (
    .sel(demultiplexer_1_out_1), .in_0(iq_update_checker_3_entryvalue_out),
    .in_1(iq_update_checker_4_entryvalue_out), .out(multiplexer_4_out));
  // Probe IQE2_CLR-SWITCH on demultiplexer_1_out_2
  Multiplexer multiplexer_5 (.sel(demultiplexer_1_out_2), .in_0(or_3_out), .in_1(1'b0), .out(multiplexer_5_out));
  Multiplexer #(.Bits(49)) multiplexer_6 (
    .sel(demultiplexer_1_out_2), .in_0(iq_update_checker_5_entryvalue_out),
    .in_1(iq_update_checker_6_entryvalue_out), .out(multiplexer_6_out));
  or or_4 (or_4_out, multiplexer_1_out, CLR);
  or or_5 (or_5_out, multiplexer_3_out, CLR);
  or or_6 (or_6_out, multiplexer_5_out, CLR);
  // Probe IQE0_CLR on or_4_out
  // Probe IQE0_PRE on multiplexer_2_out
  // Probe IQE1_CLR on or_5_out
  // Probe IQE1_PRE on multiplexer_4_out
  // Probe IQE2_CLR on or_6_out
  // Probe IQE2_PRE on multiplexer_6_out
  issue_queue_entry IQEntry0 (
    .V_OUT(IQEntry0_r1rdy_out[0]), .TagDst_OUT(IQEntry0_tagdst_out), .R1Rdy_OUT(IQEntry0_r1rdy_out[6]),
    .R1TagVal_OUT(IQEntry0_r1tagval_out), .R2Rdy_OUT(IQEntry0_r1rdy_out[23]),
    .R2TagVal_OUT(IQEntry0_r2tagval_out), .OPCode_OUT(IQEntry0_opcode_out),
    .Cond_OUT(IQEntry0_r1rdy_out[44]), .Rd_OUT(IQEntry0_rd_out), .ExecType_OUT(IQEntry0_r1rdy_out[48]),
    .CLK(CLK), .CLR(or_4_out), .V_IN(multiplexer_2_out[0]), .TagDst_IN(multiplexer_2_out[5:1]),
    .R1Rdy_IN(multiplexer_2_out[6]), .R1TagVal_IN(multiplexer_2_out[22:7]), .R2Rdy_IN(multiplexer_2_out[23]),
    .R2TagVal_IN(multiplexer_2_out[39:24]), .OPCode_IN(multiplexer_2_out[43:40]),
    .Cond_IN(multiplexer_2_out[44]), .Rd_IN(multiplexer_2_out[47:45]), .ExecType_IN(multiplexer_2_out[48]));
  issue_queue_entry IQEntry1 (
    .V_OUT(IQEntry1_r1rdy_out[0]), .TagDst_OUT(IQEntry1_tagdst_out), .R1Rdy_OUT(IQEntry1_r1rdy_out[6]),
    .R1TagVal_OUT(IQEntry1_r1tagval_out), .R2Rdy_OUT(IQEntry1_r1rdy_out[23]),
    .R2TagVal_OUT(IQEntry1_r2tagval_out), .OPCode_OUT(IQEntry1_opcode_out),
    .Cond_OUT(IQEntry1_r1rdy_out[44]), .Rd_OUT(IQEntry1_rd_out), .ExecType_OUT(IQEntry1_r1rdy_out[48]),
    .CLK(CLK), .CLR(or_5_out), .V_IN(multiplexer_4_out[0]), .TagDst_IN(multiplexer_4_out[5:1]),
    .R1Rdy_IN(multiplexer_4_out[6]), .R1TagVal_IN(multiplexer_4_out[22:7]), .R2Rdy_IN(multiplexer_4_out[23]),
    .R2TagVal_IN(multiplexer_4_out[39:24]), .OPCode_IN(multiplexer_4_out[43:40]),
    .Cond_IN(multiplexer_4_out[44]), .Rd_IN(multiplexer_4_out[47:45]), .ExecType_IN(multiplexer_4_out[48]));
  issue_queue_entry IQEntry2 (
    .V_OUT(IQEntry2_r1rdy_out[0]), .TagDst_OUT(IQEntry2_tagdst_out), .R1Rdy_OUT(IQEntry2_r1rdy_out[6]),
    .R1TagVal_OUT(IQEntry2_r1tagval_out), .R2Rdy_OUT(IQEntry2_r1rdy_out[23]),
    .R2TagVal_OUT(IQEntry2_r2tagval_out), .OPCode_OUT(IQEntry2_opcode_out),
    .Cond_OUT(IQEntry2_r1rdy_out[44]), .Rd_OUT(IQEntry2_rd_out), .ExecType_OUT(IQEntry2_r1rdy_out[48]),
    .CLK(CLK), .CLR(or_6_out), .V_IN(multiplexer_6_out[0]), .TagDst_IN(multiplexer_6_out[5:1]),
    .R1Rdy_IN(multiplexer_6_out[6]), .R1TagVal_IN(multiplexer_6_out[22:7]), .R2Rdy_IN(multiplexer_6_out[23]),
    .R2TagVal_IN(multiplexer_6_out[39:24]), .OPCode_IN(multiplexer_6_out[43:40]),
    .Cond_IN(multiplexer_6_out[44]), .Rd_IN(multiplexer_6_out[47:45]), .ExecType_IN(multiplexer_6_out[48]));
  // Probe IQ I/R-ALU Priority on multiplexer_7_out
  // Probe IQ R-MEM Priority on multiplexer_8_out
  and and_2 (and_2_out, IQEntry0_r1rdy_out[6], IQEntry0_r1rdy_out[23]);
  and and_3 (and_3_out, IQEntry1_r1rdy_out[6], IQEntry1_r1rdy_out[23]);
  and and_4 (and_4_out, IQEntry2_r1rdy_out[6], IQEntry2_r1rdy_out[23]);
  Demultiplexer demultiplexer_5 (
    .sel(IQEntry2_r1rdy_out[48]), .in(and_4_out), .out_0(demultiplexer_5_out_0), .out_1(demultiplexer_5_out_1));
  Demultiplexer demultiplexer_6 (
    .sel(IQEntry1_r1rdy_out[48]), .in(and_3_out), .out_0(demultiplexer_6_out_0), .out_1(demultiplexer_6_out_1));
  Demultiplexer demultiplexer_7 (
    .sel(IQEntry0_r1rdy_out[48]), .in(and_2_out), .out_0(demultiplexer_7_out_0), .out_1(demultiplexer_7_out_1));
  PriorityEncoder #(.Selector_Bits(2)) I_R_ALU_Priority (
    .in0(demultiplexer_5_out_0), .in1(demultiplexer_6_out_0), .in2(demultiplexer_7_out_0), .in3(1'b0),
    .num(I_R_ALU_Priority_num), .any(I_R_ALU_Priority_any));
  PriorityEncoder #(.Selector_Bits(2)) R_MEM_Priority (
    .in0(demultiplexer_5_out_1), .in1(demultiplexer_6_out_1), .in2(demultiplexer_7_out_1), .in3(1'b0),
    .num(R_MEM_Priority_num), .any(R_MEM_Priority_any));
  Multiplexer #(.Bits(2)) multiplexer_7 (
    .sel(I_R_ALU_Priority_any), .in_0(2'b11), .in_1(I_R_ALU_Priority_num), .out(multiplexer_7_out));
  Multiplexer #(.Bits(2)) multiplexer_8 (
    .sel(R_MEM_Priority_any), .in_0(2'b11), .in_1(R_MEM_Priority_num), .out(multiplexer_8_out));
  // Probe IQEntry0 on {IQEntry0_r1rdy_out[48], IQEntry0_rd_out, IQEntry0_r1rdy_out[44], IQEntry0_opcode_out, IQEntry0_r2tagval_out, IQEntry0_r1rdy_out[23], IQEntry0_r1tagval_out, IQEntry0_r1rdy_out[6], IQEntry0_tagdst_out, IQEntry0_r1rdy_out[0]}
  // Probe IQEntry1 on {IQEntry1_r1rdy_out[48], IQEntry1_rd_out, IQEntry1_r1rdy_out[44], IQEntry1_opcode_out, IQEntry1_r2tagval_out, IQEntry1_r1rdy_out[23], IQEntry1_r1tagval_out, IQEntry1_r1rdy_out[6], IQEntry1_tagdst_out, IQEntry1_r1rdy_out[0]}
  // Probe IQEntry2 on {IQEntry2_r1rdy_out[48], IQEntry2_rd_out, IQEntry2_r1rdy_out[44], IQEntry2_opcode_out, IQEntry2_r2tagval_out, IQEntry2_r1rdy_out[23], IQEntry2_r1tagval_out, IQEntry2_r1rdy_out[6], IQEntry2_tagdst_out, IQEntry2_r1rdy_out[0]}
  Multiplexer #(.Selector_Bits(2), .Bits(49)) multiplexer_9 (
    .sel(multiplexer_7_out),
    .in_0({IQEntry2_r1rdy_out[48], IQEntry2_rd_out, IQEntry2_r1rdy_out[44], IQEntry2_opcode_out, IQEntry2_r2tagval_out, IQEntry2_r1rdy_out[23], IQEntry2_r1tagval_out, IQEntry2_r1rdy_out[6], IQEntry2_tagdst_out, IQEntry2_r1rdy_out[0]}),
    .in_1({IQEntry1_r1rdy_out[48], IQEntry1_rd_out, IQEntry1_r1rdy_out[44], IQEntry1_opcode_out, IQEntry1_r2tagval_out, IQEntry1_r1rdy_out[23], IQEntry1_r1tagval_out, IQEntry1_r1rdy_out[6], IQEntry1_tagdst_out, IQEntry1_r1rdy_out[0]}),
    .in_2({IQEntry0_r1rdy_out[48], IQEntry0_rd_out, IQEntry0_r1rdy_out[44], IQEntry0_opcode_out, IQEntry0_r2tagval_out, IQEntry0_r1rdy_out[23], IQEntry0_r1tagval_out, IQEntry0_r1rdy_out[6], IQEntry0_tagdst_out, IQEntry0_r1rdy_out[0]}),
    .in_3({49{1'b0}}), .out(NextData_IRALU));
  Multiplexer #(.Selector_Bits(2), .Bits(49)) multiplexer_10 (
    .sel(multiplexer_8_out),
    .in_0({IQEntry2_r1rdy_out[48], IQEntry2_rd_out, IQEntry2_r1rdy_out[44], IQEntry2_opcode_out, IQEntry2_r2tagval_out, IQEntry2_r1rdy_out[23], IQEntry2_r1tagval_out, IQEntry2_r1rdy_out[6], IQEntry2_tagdst_out, IQEntry2_r1rdy_out[0]}),
    .in_1({IQEntry1_r1rdy_out[48], IQEntry1_rd_out, IQEntry1_r1rdy_out[44], IQEntry1_opcode_out, IQEntry1_r2tagval_out, IQEntry1_r1rdy_out[23], IQEntry1_r1tagval_out, IQEntry1_r1rdy_out[6], IQEntry1_tagdst_out, IQEntry1_r1rdy_out[0]}),
    .in_2({IQEntry0_r1rdy_out[48], IQEntry0_rd_out, IQEntry0_r1rdy_out[44], IQEntry0_opcode_out, IQEntry0_r2tagval_out, IQEntry0_r1rdy_out[23], IQEntry0_r1tagval_out, IQEntry0_r1rdy_out[6], IQEntry0_tagdst_out, IQEntry0_r1rdy_out[0]}),
    .in_3({49{1'b0}}), .out(NextData_RMEM));
  and and_5 (Full, IQEntry0_r1rdy_out[0], IQEntry1_r1rdy_out[0], IQEntry2_r1rdy_out[0]);
  nor nor_1 (Empty, IQEntry0_r1rdy_out[0], IQEntry1_r1rdy_out[0], IQEntry2_r1rdy_out[0]);

  // Notes on the sheet:
  //   Issue Queue (IQ)
endmodule
