// Digital circuit issue_queue_entry.dig as structural Verilog
module issue_queue_entry (
  input  CLK,
  input  V_IN,
  input  [4:0] TagDst_IN,
  input  R1Rdy_IN,
  input  [15:0] R1TagVal_IN,
  input  R2Rdy_IN,
  input  [15:0] R2TagVal_IN,
  input  CLR,
  input  [3:0] OPCode_IN,
  input  Cond_IN,
  input  [2:0] Rd_IN,
  input  ExecType_IN,
  output V_OUT,
  output [4:0] TagDst_OUT,
  output R1Rdy_OUT,
  output [15:0] R1TagVal_OUT,
  output R2Rdy_OUT,
  output [15:0] R2TagVal_OUT,
  output [3:0] OPCode_OUT,
  output Cond_OUT,
  output [2:0] Rd_OUT,
  output ExecType_OUT
);

  wire multiplexer_1_out, multiplexer_3_out, multiplexer_5_out, multiplexer_8_out, multiplexer_10_out;
  wire [2:0] multiplexer_9_out;
  wire [3:0] multiplexer_7_out;
  wire [4:0] multiplexer_2_out;
  wire [15:0] multiplexer_4_out, multiplexer_6_out;

  Multiplexer multiplexer_1 (.sel(CLR), .in_0(V_IN), .in_1(1'b0), .out(multiplexer_1_out));
  Multiplexer #(.Bits(5)) multiplexer_2 (.sel(CLR), .in_0(TagDst_IN), .in_1({5{1'b0}}), .out(multiplexer_2_out));
  Multiplexer multiplexer_3 (.sel(CLR), .in_0(R1Rdy_IN), .in_1(1'b0), .out(multiplexer_3_out));
  Multiplexer #(.Bits(16)) multiplexer_4 (.sel(CLR), .in_0(R1TagVal_IN), .in_1({16{1'b0}}), .out(multiplexer_4_out));
  Multiplexer multiplexer_5 (.sel(CLR), .in_0(R2Rdy_IN), .in_1(1'b0), .out(multiplexer_5_out));
  Multiplexer #(.Bits(16)) multiplexer_6 (.sel(CLR), .in_0(R2TagVal_IN), .in_1({16{1'b0}}), .out(multiplexer_6_out));
  Multiplexer #(.Bits(4)) multiplexer_7 (.sel(CLR), .in_0(OPCode_IN), .in_1(4'b0000), .out(multiplexer_7_out));
  Multiplexer multiplexer_8 (.sel(CLR), .in_0(Cond_IN), .in_1(1'b0), .out(multiplexer_8_out));
  Multiplexer #(.Bits(3)) multiplexer_9 (.sel(CLR), .in_0(Rd_IN), .in_1(3'b000), .out(multiplexer_9_out));
  Multiplexer multiplexer_10 (.sel(CLR), .in_0(ExecType_IN), .in_1(1'b0), .out(multiplexer_10_out));
  Register V (.D(multiplexer_1_out), .C(CLK), .en(1'b1), .Q(V_OUT));
  Register #(.Bits(5)) TagDst (.D(multiplexer_2_out), .C(CLK), .en(1'b1), .Q(TagDst_OUT));
  Register R1Rdy (.D(multiplexer_3_out), .C(CLK), .en(1'b1), .Q(R1Rdy_OUT));
  Register #(.Bits(16)) R1TagVal (.D(multiplexer_4_out), .C(CLK), .en(1'b1), .Q(R1TagVal_OUT));
  Register R2Rdy (.D(multiplexer_5_out), .C(CLK), .en(1'b1), .Q(R2Rdy_OUT));
  Register #(.Bits(16)) R2TagVal (.D(multiplexer_6_out), .C(CLK), .en(1'b1), .Q(R2TagVal_OUT));
  Register #(.Bits(4)) OPCode (.D(multiplexer_7_out), .C(CLK), .en(1'b1), .Q(OPCode_OUT));
  Register Cond (.D(multiplexer_8_out), .C(CLK), .en(1'b1), .Q(Cond_OUT));
  Register #(.Bits(3)) Rd (.D(multiplexer_9_out), .C(CLK), .en(1'b1), .Q(Rd_OUT));
  Register ExecType (.D(multiplexer_10_out), .C(CLK), .en(1'b1), .Q(ExecType_OUT));
endmodule
