// Digital circuit rrd_dp_ppr.dig as structural Verilog
module rrd_dp_ppr (
  input  CLK,
  input  R1VRRD,
  input  R2VRRD,
  input  [15:0] Ra_Tag1RRD,
  input  [15:0] Rb_Tag2RRD,
  input  [4:0] TagDstRRD,
  input  [15:0] INSNRRD,
  input  EN,
  input  CLR,
  output R1VDP,
  output R2VDP,
  output [15:0] Ra_Tag1DP,
  output [15:0] Rb_Tag2DP,
  output [4:0] TagDstDP,
  output [15:0] INSNDP
);

  wire multiplexer_1_out, multiplexer_2_out;
  wire [4:0] multiplexer_5_out;
  wire [15:0] multiplexer_3_out, multiplexer_4_out, multiplexer_6_out;

  Multiplexer multiplexer_1 (.sel(CLR), .in_0(R1VRRD), .in_1(1'b0), .out(multiplexer_1_out));
  Multiplexer multiplexer_2 (.sel(CLR), .in_0(R2VRRD), .in_1(1'b0), .out(multiplexer_2_out));
  Multiplexer #(.Bits(16)) multiplexer_3 (.sel(CLR), .in_0(Ra_Tag1RRD), .in_1({16{1'b0}}), .out(multiplexer_3_out));
  Multiplexer #(.Bits(16)) multiplexer_4 (.sel(CLR), .in_0(Rb_Tag2RRD), .in_1({16{1'b0}}), .out(multiplexer_4_out));
  Multiplexer #(.Bits(5)) multiplexer_5 (.sel(CLR), .in_0(TagDstRRD), .in_1({5{1'b0}}), .out(multiplexer_5_out));
  Multiplexer #(.Bits(16)) multiplexer_6 (.sel(CLR), .in_0(INSNRRD), .in_1({16{1'b0}}), .out(multiplexer_6_out));
  Register R1V (.D(multiplexer_1_out), .C(CLK), .en(EN), .Q(R1VDP));
  Register R2V (.D(multiplexer_2_out), .C(CLK), .en(EN), .Q(R2VDP));
  Register #(.Bits(16)) Ra_Tag1 (.D(multiplexer_3_out), .C(CLK), .en(EN), .Q(Ra_Tag1DP));
  Register #(.Bits(16)) Rb_Tag2 (.D(multiplexer_4_out), .C(CLK), .en(EN), .Q(Rb_Tag2DP));
  Register #(.Bits(5)) TagDst (.D(multiplexer_5_out), .C(CLK), .en(EN), .Q(TagDstDP));
  Register #(.Bits(16)) INSN (.D(multiplexer_6_out), .C(CLK), .en(EN), .Q(INSNDP));

  // Notes on the sheet:
  //   RRD/DP PPR
endmodule
