// Digital circuit wb_r_ppr.dig as structural Verilog
module wb_r_ppr (
  input  DstTagW,
  input  CLK,
  input  [15:0] ALUResultW,
  input  BCWriteW,
  input  HEW,
  input  PCSrcW,
  input  [3:0] FlagsW,
  input  FlagWriteW,
  input  [15:0] ReadDataW,
  output DstTagR,
  output [15:0] ALUResultR,
  output BCWriteR,
  output HER,
  output PCSrcR,
  output [3:0] FlagsR,
  output FlagWriteR,
  output [15:0] ReadDataR
);

  Register DstTag (.D(DstTagW), .C(CLK), .en(1'b1), .Q(DstTagR));
  Register HE (.D(HEW), .C(CLK), .en(1'b1), .Q(HER));
  Register BCWrite (.D(BCWriteW), .C(CLK), .en(1'b1), .Q(BCWriteR));
  Register PCSrc (.D(PCSrcW), .C(CLK), .en(1'b1), .Q(PCSrcR));
  Register #(.Bits(16)) ALUResult (.D(ALUResultW), .C(CLK), .en(1'b1), .Q(ALUResultR));
  Register #(.Bits(4)) Flags (.D(FlagsW), .C(CLK), .en(1'b1), .Q(FlagsR));
  Register FlagWrite (.D(FlagWriteW), .C(CLK), .en(1'b1), .Q(FlagWriteR));
  Register #(.Bits(16)) ReadData (.D(ReadDataW), .C(CLK), .en(1'b1), .Q(ReadDataR));

  // Notes on the sheet:
  //   WB/R PPR
endmodule
