// Digital circuit control_unit_ooo.dig as structural Verilog
module control_unit_ooo (
  input  [3:0] OPCode,
  input  [2:0] Rd,
  output FlagWriteD,
  output BranchD,
  output [1:0] ALUCtrlD,
  output MemWriteD,
  output MemToRegD,
  output SethD,
  output UpdateROB
);

  wire comparator_1_eq, Is_Rd_PC_eq, or_1_out, or_2_out;
  wire [10:0] lookuptable_1_out;

  Comparator #(.Bits(7)) comparator_1 (.a({7{1'b0}}), .b({Rd, OPCode}), .eq(comparator_1_eq));  // open: gt, lt
  LookUpTable #(.Bits(11)) lookuptable_1 (
    .in0(OPCode[0]), .in1(OPCode[1]), .in2(OPCode[2]), .in3(OPCode[3]), .out(lookuptable_1_out));
  Comparator #(.Bits(3)) Is_Rd_PC (.a(Rd), .b(3'b111), .eq(Is_Rd_PC_eq));  // open: gt, lt
  or or_1 (or_1_out, Is_Rd_PC_eq, lookuptable_1_out[10]);
  or or_2 (or_2_out, Is_Rd_PC_eq, lookuptable_1_out[4]);
  Multiplexer multiplexer_1 (.sel(comparator_1_eq), .in_0(or_1_out), .in_1(1'b0));  // open: out
  Multiplexer multiplexer_2 (.sel(comparator_1_eq), .in_0(lookuptable_1_out[9]), .in_1(1'b0));  // open: out
  Multiplexer multiplexer_3 (.sel(comparator_1_eq), .in_0(lookuptable_1_out[8]), .in_1(1'b0), .out(MemToRegD));
  Multiplexer multiplexer_4 (.sel(comparator_1_eq), .in_0(lookuptable_1_out[7]), .in_1(1'b0), .out(MemWriteD));
  Multiplexer #(.Bits(2)) multiplexer_5 (
    .sel(comparator_1_eq), .in_0(lookuptable_1_out[6:5]), .in_1(2'b00), .out(ALUCtrlD));
  Multiplexer multiplexer_6 (.sel(comparator_1_eq), .in_0(or_2_out), .in_1(1'b0), .out(BranchD));
  Multiplexer multiplexer_7 (.sel(comparator_1_eq), .in_0(lookuptable_1_out[3]), .in_1(1'b0));  // open: out
  Multiplexer multiplexer_8 (.sel(comparator_1_eq), .in_0(lookuptable_1_out[2]), .in_1(1'b0), .out(FlagWriteD));
  Multiplexer multiplexer_9 (.sel(comparator_1_eq), .in_0(lookuptable_1_out[1]), .in_1(1'b0), .out(SethD));
  Multiplexer multiplexer_10 (.sel(comparator_1_eq), .in_0(lookuptable_1_out[0]), .in_1(1'b0));  // open: out
  not not_1 (UpdateROB, comparator_1_eq);

  // Notes on the sheet:
  //   Rd
  //   contents of lookuptable_1 (hex, n*v repeats v):
  //   208,20a,0,0,80,300,0,0,205,225,245,265
endmodule
