// Digital circuit iq_update_checker.dig as structural Verilog
module iq_update_checker (
  input  [4:0] BC_Tag,
  input  [15:0] BC_Result,
  input  [47:0] EntryValue_IN,
  input  BC_EN,
  output [47:0] EntryValue_OUT
);

  wire and_1_out, and_2_out, and_3_out, comparator_1_eq, comparator_2_eq, nand_1_out, not_1_out, not_2_out;
  wire [15:0] multiplexer_2_out, multiplexer_4_out;
  wire [23:0] multiplexer_1_out;

  not not_1 (not_1_out, EntryValue_IN[6]);
  not not_2 (not_2_out, EntryValue_IN[23]);
  Comparator #(.Bits(5)) comparator_1 (.a(BC_Tag), .b(EntryValue_IN[11:7]), .eq(comparator_1_eq));  // open: gt, lt
  Comparator #(.Bits(5)) comparator_2 (.a(BC_Tag), .b(EntryValue_IN[28:24]), .eq(comparator_2_eq));  // open: gt, lt
  and and_1 (and_1_out, not_1_out, comparator_1_eq);
  and and_2 (and_2_out, not_2_out, comparator_2_eq);
  Multiplexer multiplexer_1 (.sel(and_1_out), .in_0(EntryValue_IN[6]), .in_1(not_1_out), .out(multiplexer_1_out[6]));
  Multiplexer #(.Bits(16)) multiplexer_2 (
    .sel(and_1_out), .in_0(EntryValue_IN[22:7]), .in_1(BC_Result), .out(multiplexer_2_out));
  Multiplexer multiplexer_3 (.sel(and_2_out), .in_0(EntryValue_IN[23]), .in_1(not_2_out), .out(multiplexer_1_out[23]));
  Multiplexer #(.Bits(16)) multiplexer_4 (
    .sel(and_2_out), .in_0(EntryValue_IN[39:24]), .in_1(BC_Result), .out(multiplexer_4_out));
  nand nand_1 (nand_1_out, multiplexer_1_out[6], multiplexer_1_out[23]);
  and and_3 (and_3_out, BC_EN, EntryValue_IN[0]);
  Multiplexer multiplexer_5 (.sel(and_3_out), .in_0(EntryValue_IN[0]), .in_1(nand_1_out), .out(multiplexer_1_out[0]));
  Multiplexer #(.Bits(48)) multiplexer_6 (
    .sel(and_3_out), .in_0(EntryValue_IN),
    .in_1({EntryValue_IN[47:40], multiplexer_4_out, multiplexer_1_out[23], multiplexer_2_out, multiplexer_1_out[6], EntryValue_IN[5:1], multiplexer_1_out[0]}),
    .out(EntryValue_OUT));

  // Notes on the sheet:
  //   Instruction Queue Update Checker
endmodule
