// Digital circuit issue_queue.dig as structural Verilog
module issue_queue (
  input  CLK,
  input  CLRNext,
  input  Tail_WE,
  input  [47:0] TailData,
  input  [4:0] BC_Tag,
  input  [15:0] BC_Result,
  input  BC_WE,
  input  CLR,
  output [47:0] NextData,
  output Full,
  output Empty
);

  wire and_1_out, and_2_out, and_3_out, and_4_out, comparator_1_eq, comparator_2_eq, demultiplexer_1_out_0,
       demultiplexer_1_out_1, demultiplexer_1_out_2, demultiplexer_3_out_0, demultiplexer_3_out_1,
       demultiplexer_3_out_2, multiplexer_2_out, multiplexer_4_out, multiplexer_6_out, not_1_out, or_1_out,
       or_2_out, or_3_out, priorityencoder_1_any;
  wire [1:0] multiplexer_7_out, priorityencoder_1_num, Tail_out;
  wire [47:0] demultiplexer_2_out_0, demultiplexer_2_out_1, demultiplexer_2_out_2,
       iq_update_checker_1_entryvalue_out, iq_update_checker_2_entryvalue_out,
       iq_update_checker_3_entryvalue_out, iq_update_checker_4_entryvalue_out,
       iq_update_checker_5_entryvalue_out, iq_update_checker_6_entryvalue_out, IQEntry0_tagdst_out,
       IQEntry1_tagdst_out, IQEntry2_tagdst_out, multiplexer_1_out, multiplexer_3_out, multiplexer_5_out;

  Comparator #(.Bits(48)) comparator_1 (.a({48{1'b0}}), .b(TailData), .eq(comparator_1_eq));  // open: gt, lt
  not not_1 (not_1_out, comparator_1_eq);
  and and_1 (and_1_out, not_1_out, Tail_WE);
  Demultiplexer #(.Selector_Bits(2)) demultiplexer_1 (
    .sel(Tail_out), .in(and_1_out), .out_0(demultiplexer_1_out_0), .out_1(demultiplexer_1_out_1),
    .out_2(demultiplexer_1_out_2));  // open: out_3
  Comparator #(.Bits(2)) comparator_2 (.a(Tail_out), .b(2'b10), .eq(comparator_2_eq));  // open: gt, lt
  Counter #(.Bits(2)) Tail (.en(and_1_out), .C(CLK), .clr(comparator_2_eq), .out(Tail_out));  // open: ovf
  Demultiplexer #(.Selector_Bits(2), .Bits(48)) demultiplexer_2 (
    .sel(Tail_out), .in(TailData), .out_0(demultiplexer_2_out_0), .out_1(demultiplexer_2_out_1),
    .out_2(demultiplexer_2_out_2));  // open: out_3
  // Probe IQTail on Tail_out
  Demultiplexer #(.Selector_Bits(2)) demultiplexer_3 (
    .sel(multiplexer_7_out), .in(CLRNext), .out_0(demultiplexer_3_out_0), .out_1(demultiplexer_3_out_1),
    .out_2(demultiplexer_3_out_2));  // open: out_3
  iq_update_checker iq_update_checker_1 (
    .BC_Result(BC_Result), .BC_Tag(BC_Tag), .BC_EN(BC_WE), .EntryValue_IN(IQEntry0_tagdst_out),
    .EntryValue_OUT(iq_update_checker_1_entryvalue_out));
  iq_update_checker iq_update_checker_2 (
    .BC_Result(BC_Result), .BC_Tag(BC_Tag), .BC_EN(BC_WE), .EntryValue_IN(demultiplexer_2_out_0),
    .EntryValue_OUT(iq_update_checker_2_entryvalue_out));
  iq_update_checker iq_update_checker_3 (
    .BC_Result(BC_Result), .BC_Tag(BC_Tag), .BC_EN(BC_WE), .EntryValue_IN(IQEntry1_tagdst_out),
    .EntryValue_OUT(iq_update_checker_3_entryvalue_out));
  iq_update_checker iq_update_checker_4 (
    .BC_Result(BC_Result), .BC_Tag(BC_Tag), .BC_EN(BC_WE), .EntryValue_IN(demultiplexer_2_out_1),
    .EntryValue_OUT(iq_update_checker_4_entryvalue_out));
  iq_update_checker iq_update_checker_5 (
    .BC_Result(BC_Result), .BC_Tag(BC_Tag), .BC_EN(BC_WE), .EntryValue_IN(IQEntry2_tagdst_out),
    .EntryValue_OUT(iq_update_checker_5_entryvalue_out));
  iq_update_checker iq_update_checker_6 (
    .BC_Result(BC_Result), .BC_Tag(BC_Tag), .BC_EN(BC_WE), .EntryValue_IN(demultiplexer_2_out_2),
    .EntryValue_OUT(iq_update_checker_6_entryvalue_out));
  Multiplexer #(.Bits(48)) multiplexer_1 (
    .sel(demultiplexer_1_out_0), .in_0(iq_update_checker_1_entryvalue_out),
    .in_1(iq_update_checker_2_entryvalue_out), .out(multiplexer_1_out));
  Multiplexer multiplexer_2 (
    .sel(demultiplexer_1_out_1), .in_0(demultiplexer_3_out_1), .in_1(1'b0), .out(multiplexer_2_out));
  Multiplexer #(.Bits(48)) multiplexer_3 (
    .sel(demultiplexer_1_out_1), .in_0(iq_update_checker_3_entryvalue_out),
    .in_1(iq_update_checker_4_entryvalue_out), .out(multiplexer_3_out));
  Multiplexer multiplexer_4 (
    .sel(demultiplexer_1_out_2), .in_0(demultiplexer_3_out_0), .in_1(1'b0), .out(multiplexer_4_out));
  Multiplexer #(.Bits(48)) multiplexer_5 (
    .sel(demultiplexer_1_out_2), .in_0(iq_update_checker_5_entryvalue_out),
    .in_1(iq_update_checker_6_entryvalue_out), .out(multiplexer_5_out));
  // Probe IQE0_CLR-SWITCH on demultiplexer_1_out_0
  Multiplexer multiplexer_6 (
    .sel(demultiplexer_1_out_0), .in_0(demultiplexer_3_out_2), .in_1(1'b0), .out(multiplexer_6_out));
  or or_1 (or_1_out, multiplexer_6_out, CLR);
  // Probe IQE1_CLR-SWITCH on demultiplexer_1_out_1
  or or_2 (or_2_out, multiplexer_2_out, CLR);
  // Probe IQE2_CLR-SWITCH on demultiplexer_1_out_2
  or or_3 (or_3_out, multiplexer_4_out, CLR);
  // Probe IQE0_PRE on multiplexer_1_out
  // Probe IQE1_PRE on multiplexer_3_out
  // Probe IQE2_PRE on multiplexer_5_out
  issue_queue_entry IQEntry0 (
    .V_OUT(IQEntry0_tagdst_out[0]), .TagDst_OUT(IQEntry0_tagdst_out[5:1]),
    .R1Rdy_OUT(IQEntry0_tagdst_out[6]), .R1TagVal_OUT(IQEntry0_tagdst_out[22:7]),
    .R2Rdy_OUT(IQEntry0_tagdst_out[23]), .R2TagVal_OUT(IQEntry0_tagdst_out[39:24]),
    .OPCode_OUT(IQEntry0_tagdst_out[43:40]), .Cond_OUT(IQEntry0_tagdst_out[44]),
    .Rd_OUT(IQEntry0_tagdst_out[47:45]), .CLK(CLK), .CLR(or_1_out), .V_IN(multiplexer_1_out[0]),
    .TagDst_IN(multiplexer_1_out[5:1]), .R1Rdy_IN(multiplexer_1_out[6]),
    .R1TagVal_IN(multiplexer_1_out[22:7]), .R2Rdy_IN(multiplexer_1_out[23]),
    .R2TagVal_IN(multiplexer_1_out[39:24]), .OPCode_IN(multiplexer_1_out[43:40]),
    .Cond_IN(multiplexer_1_out[44]), .Rd_IN(multiplexer_1_out[47:45]));
  // Probe IQE0_CLR on or_1_out
  issue_queue_entry IQEntry1 (
    .V_OUT(IQEntry1_tagdst_out[0]), .TagDst_OUT(IQEntry1_tagdst_out[5:1]),
    .R1Rdy_OUT(IQEntry1_tagdst_out[6]), .R1TagVal_OUT(IQEntry1_tagdst_out[22:7]),
    .R2Rdy_OUT(IQEntry1_tagdst_out[23]), .R2TagVal_OUT(IQEntry1_tagdst_out[39:24]),
    .OPCode_OUT(IQEntry1_tagdst_out[43:40]), .Cond_OUT(IQEntry1_tagdst_out[44]),
    .Rd_OUT(IQEntry1_tagdst_out[47:45]), .CLK(CLK), .CLR(or_2_out), .V_IN(multiplexer_3_out[0]),
    .TagDst_IN(multiplexer_3_out[5:1]), .R1Rdy_IN(multiplexer_3_out[6]),
    .R1TagVal_IN(multiplexer_3_out[22:7]), .R2Rdy_IN(multiplexer_3_out[23]),
    .R2TagVal_IN(multiplexer_3_out[39:24]), .OPCode_IN(multiplexer_3_out[43:40]),
    .Cond_IN(multiplexer_3_out[44]), .Rd_IN(multiplexer_3_out[47:45]));
  // Probe IQE1_CLR on or_2_out
  issue_queue_entry IQEntry2 (
    .V_OUT(IQEntry2_tagdst_out[0]), .TagDst_OUT(IQEntry2_tagdst_out[5:1]),
    .R1Rdy_OUT(IQEntry2_tagdst_out[6]), .R1TagVal_OUT(IQEntry2_tagdst_out[22:7]),
    .R2Rdy_OUT(IQEntry2_tagdst_out[23]), .R2TagVal_OUT(IQEntry2_tagdst_out[39:24]),
    .OPCode_OUT(IQEntry2_tagdst_out[43:40]), .Cond_OUT(IQEntry2_tagdst_out[44]),
    .Rd_OUT(IQEntry2_tagdst_out[47:45]), .CLK(CLK), .CLR(or_3_out), .V_IN(multiplexer_5_out[0]),
    .TagDst_IN(multiplexer_5_out[5:1]), .R1Rdy_IN(multiplexer_5_out[6]),
    .R1TagVal_IN(multiplexer_5_out[22:7]), .R2Rdy_IN(multiplexer_5_out[23]),
    .R2TagVal_IN(multiplexer_5_out[39:24]), .OPCode_IN(multiplexer_5_out[43:40]),
    .Cond_IN(multiplexer_5_out[44]), .Rd_IN(multiplexer_5_out[47:45]));
  // Probe IQE2_CLR on or_3_out
  and and_2 (and_2_out, IQEntry0_tagdst_out[6], IQEntry0_tagdst_out[23]);
  and and_3 (and_3_out, IQEntry1_tagdst_out[6], IQEntry1_tagdst_out[23]);
  and and_4 (and_4_out, IQEntry2_tagdst_out[6], IQEntry2_tagdst_out[23]);
  PriorityEncoder #(.Selector_Bits(2)) priorityencoder_1 (
    .in0(and_4_out), .in1(and_3_out), .in2(and_2_out), .in3(1'b0), .num(priorityencoder_1_num),
    .any(priorityencoder_1_any));
  Multiplexer #(.Bits(2)) multiplexer_7 (
    .sel(priorityencoder_1_any), .in_0(2'b11), .in_1(priorityencoder_1_num), .out(multiplexer_7_out));
  // Probe EQPriority on multiplexer_7_out
  // Probe IQEntry0 on IQEntry0_tagdst_out
  // Probe IQEntry1 on IQEntry1_tagdst_out
  // Probe IQEntry2 on IQEntry2_tagdst_out
  Multiplexer #(.Selector_Bits(2), .Bits(48)) multiplexer_8 (
    .sel(multiplexer_7_out), .in_0(IQEntry2_tagdst_out), .in_1(IQEntry1_tagdst_out),
    .in_2(IQEntry0_tagdst_out), .in_3({48{1'b0}}), .out(NextData));
  and and_5 (Full, IQEntry0_tagdst_out[0], IQEntry1_tagdst_out[0], IQEntry2_tagdst_out[0]);
  nor nor_1 (Empty, IQEntry0_tagdst_out[0], IQEntry1_tagdst_out[0], IQEntry2_tagdst_out[0]);

  // Notes on the sheet:
  //   Issue Queue (IQ)
endmodule
