// Digital circuit rename_map_table.dig as structural Verilog
module rename_map_table (
  input  [2:0] WS,
  input  CLK,
  input  V_IN,
  input  [4:0] ROBTag_IN,
  input  [2:0] RS1,
  input  [2:0] RS2,
  input  [2:0] UpdateDst,
  input  [4:0] UpdateTag,
  input  CLR,
  input  Update_EN,
  output R1V_OUT,
  output [4:0] R1ROBTag_OUT,
  output R2V_OUT,
  output [4:0] R2ROBTag_OUT
);

  wire decoder_1_out_0, decoder_1_out_1, decoder_1_out_2, decoder_1_out_3, decoder_1_out_4, decoder_1_out_5,
       decoder_1_out_7, demultiplexer_1_out_0, demultiplexer_1_out_1, demultiplexer_1_out_2,
       demultiplexer_1_out_3, demultiplexer_1_out_4, demultiplexer_1_out_5, demultiplexer_1_out_7,
       demultiplexer_5_out_0, demultiplexer_5_out_1, demultiplexer_5_out_2, demultiplexer_5_out_3,
       demultiplexer_5_out_4, demultiplexer_5_out_5, demultiplexer_5_out_7, demultiplexer_6_out_0,
       demultiplexer_6_out_1, demultiplexer_6_out_2, demultiplexer_6_out_3, demultiplexer_6_out_4,
       demultiplexer_6_out_5, demultiplexer_6_out_7, demultiplexer_7_out_0, demultiplexer_7_out_1,
       demultiplexer_7_out_2, demultiplexer_7_out_3, demultiplexer_7_out_4, demultiplexer_7_out_5,
       demultiplexer_7_out_7, multiplexer_1_out, multiplexer_3_out, multiplexer_5_out, multiplexer_7_out,
       multiplexer_9_out, multiplexer_11_out, multiplexer_13_out, multiplexer_15_out, or_1_out, or_2_out,
       or_3_out, or_4_out, or_5_out, or_6_out, or_7_out, or_8_out, or_9_out, or_10_out, or_11_out, or_12_out,
       or_13_out, or_14_out, R0_V_q, R1_V_q, R2_V_q, R3_V_q, R4_V_q, R5_V_q, R7_V_q,
       rmt_condition_write_1_v_out, rmt_condition_write_2_v_out, rmt_condition_write_3_v_out,
       rmt_condition_write_4_v_out, rmt_condition_write_5_v_out, rmt_condition_write_6_v_out,
       rmt_condition_write_7_v_out;
  wire [4:0] demultiplexer_2_out_0, demultiplexer_2_out_1, demultiplexer_2_out_2, demultiplexer_2_out_3,
       demultiplexer_2_out_4, demultiplexer_2_out_5, demultiplexer_2_out_7, demultiplexer_3_out_0,
       demultiplexer_3_out_1, demultiplexer_3_out_2, demultiplexer_3_out_3, demultiplexer_3_out_4,
       demultiplexer_3_out_5, demultiplexer_3_out_7, demultiplexer_4_out_0, demultiplexer_4_out_1,
       demultiplexer_4_out_2, demultiplexer_4_out_3, demultiplexer_4_out_4, demultiplexer_4_out_5,
       demultiplexer_4_out_7, multiplexer_2_out, multiplexer_4_out, multiplexer_6_out, multiplexer_8_out,
       multiplexer_10_out, multiplexer_12_out, multiplexer_14_out, multiplexer_16_out, R0_Tag_q, R1_Tag_q,
       R2_Tag_q, R3_Tag_q, R4_Tag_q, R5_Tag_q, R7_Tag_q, rmt_condition_write_1_data,
       rmt_condition_write_2_data, rmt_condition_write_3_data, rmt_condition_write_4_data,
       rmt_condition_write_5_data, rmt_condition_write_6_data, rmt_condition_write_7_data;

  Demultiplexer #(.Selector_Bits(3)) demultiplexer_1 (
    .sel(UpdateDst), .in(multiplexer_15_out), .out_0(demultiplexer_1_out_0), .out_1(demultiplexer_1_out_1),
    .out_2(demultiplexer_1_out_2), .out_3(demultiplexer_1_out_3), .out_4(demultiplexer_1_out_4),
    .out_5(demultiplexer_1_out_5), .out_7(demultiplexer_1_out_7));  // open: out_6
  Demultiplexer #(.Selector_Bits(3), .Bits(5)) demultiplexer_2 (
    .sel(UpdateDst), .in(multiplexer_16_out), .out_0(demultiplexer_2_out_0), .out_1(demultiplexer_2_out_1),
    .out_2(demultiplexer_2_out_2), .out_3(demultiplexer_2_out_3), .out_4(demultiplexer_2_out_4),
    .out_5(demultiplexer_2_out_5), .out_7(demultiplexer_2_out_7));  // open: out_6
  Demultiplexer #(.Selector_Bits(3), .Bits(5)) demultiplexer_3 (
    .sel(UpdateDst), .in(UpdateTag), .out_0(demultiplexer_3_out_0), .out_1(demultiplexer_3_out_1),
    .out_2(demultiplexer_3_out_2), .out_3(demultiplexer_3_out_3), .out_4(demultiplexer_3_out_4),
    .out_5(demultiplexer_3_out_5), .out_7(demultiplexer_3_out_7));  // open: out_6
  Demultiplexer #(.Selector_Bits(3), .Bits(5)) demultiplexer_4 (
    .sel(WS), .in(ROBTag_IN), .out_0(demultiplexer_4_out_0), .out_1(demultiplexer_4_out_1),
    .out_2(demultiplexer_4_out_2), .out_3(demultiplexer_4_out_3), .out_4(demultiplexer_4_out_4),
    .out_5(demultiplexer_4_out_5), .out_7(demultiplexer_4_out_7));  // open: out_6
  Demultiplexer #(.Selector_Bits(3)) demultiplexer_5 (
    .sel(WS), .in(V_IN), .out_0(demultiplexer_5_out_0), .out_1(demultiplexer_5_out_1),
    .out_2(demultiplexer_5_out_2), .out_3(demultiplexer_5_out_3), .out_4(demultiplexer_5_out_4),
    .out_5(demultiplexer_5_out_5), .out_7(demultiplexer_5_out_7));  // open: out_6
  Decoder #(.Selector_Bits(3)) decoder_1 (
    .sel(WS), .out_0(decoder_1_out_0), .out_1(decoder_1_out_1), .out_2(decoder_1_out_2),
    .out_3(decoder_1_out_3), .out_4(decoder_1_out_4), .out_5(decoder_1_out_5), .out_7(decoder_1_out_7));  // open: out_6
  rmt_condition_write rmt_condition_write_1 (
    .WS(decoder_1_out_0), .ROBTag_IN(demultiplexer_4_out_0), .V_IN(demultiplexer_5_out_0),
    .UpdateTag(demultiplexer_3_out_0), .CurrentTag(demultiplexer_2_out_0), .Update(demultiplexer_1_out_0),
    .EN(Update_EN), .V_OUT(rmt_condition_write_1_v_out), .Data(rmt_condition_write_1_data));
  rmt_condition_write rmt_condition_write_2 (
    .WS(decoder_1_out_1), .ROBTag_IN(demultiplexer_4_out_1), .V_IN(demultiplexer_5_out_1),
    .UpdateTag(demultiplexer_3_out_1), .CurrentTag(demultiplexer_2_out_1), .Update(demultiplexer_1_out_1),
    .EN(Update_EN), .V_OUT(rmt_condition_write_2_v_out), .Data(rmt_condition_write_2_data));
  rmt_condition_write rmt_condition_write_3 (
    .WS(decoder_1_out_2), .ROBTag_IN(demultiplexer_4_out_2), .V_IN(demultiplexer_5_out_2),
    .UpdateTag(demultiplexer_3_out_2), .CurrentTag(demultiplexer_2_out_2), .Update(demultiplexer_1_out_2),
    .EN(Update_EN), .V_OUT(rmt_condition_write_3_v_out), .Data(rmt_condition_write_3_data));
  rmt_condition_write rmt_condition_write_4 (
    .WS(decoder_1_out_3), .ROBTag_IN(demultiplexer_4_out_3), .V_IN(demultiplexer_5_out_3),
    .UpdateTag(demultiplexer_3_out_3), .CurrentTag(demultiplexer_2_out_3), .Update(demultiplexer_1_out_3),
    .EN(Update_EN), .V_OUT(rmt_condition_write_4_v_out), .Data(rmt_condition_write_4_data));
  rmt_condition_write rmt_condition_write_5 (
    .WS(decoder_1_out_4), .ROBTag_IN(demultiplexer_4_out_4), .V_IN(demultiplexer_5_out_4),
    .UpdateTag(demultiplexer_3_out_4), .CurrentTag(demultiplexer_2_out_4), .Update(demultiplexer_1_out_4),
    .EN(Update_EN), .V_OUT(rmt_condition_write_5_v_out), .Data(rmt_condition_write_5_data));
  rmt_condition_write rmt_condition_write_6 (
    .WS(decoder_1_out_5), .ROBTag_IN(demultiplexer_4_out_5), .V_IN(demultiplexer_5_out_5),
    .UpdateTag(demultiplexer_3_out_5), .CurrentTag(demultiplexer_2_out_5), .Update(demultiplexer_1_out_5),
    .EN(Update_EN), .V_OUT(rmt_condition_write_6_v_out), .Data(rmt_condition_write_6_data));
  rmt_condition_write rmt_condition_write_7 (
    .WS(decoder_1_out_7), .ROBTag_IN(demultiplexer_4_out_7), .V_IN(demultiplexer_5_out_7),
    .UpdateTag(demultiplexer_3_out_7), .CurrentTag(demultiplexer_2_out_7), .Update(demultiplexer_1_out_7),
    .EN(Update_EN), .V_OUT(rmt_condition_write_7_v_out), .Data(rmt_condition_write_7_data));
  Demultiplexer #(.Selector_Bits(3)) demultiplexer_6 (
    .sel(WS), .in(CLK), .out_0(demultiplexer_6_out_0), .out_1(demultiplexer_6_out_1),
    .out_2(demultiplexer_6_out_2), .out_3(demultiplexer_6_out_3), .out_4(demultiplexer_6_out_4),
    .out_5(demultiplexer_6_out_5), .out_7(demultiplexer_6_out_7));  // open: out_6
  Demultiplexer #(.Selector_Bits(3)) demultiplexer_7 (
    .sel(WS), .in(CLK), .out_0(demultiplexer_7_out_0), .out_1(demultiplexer_7_out_1),
    .out_2(demultiplexer_7_out_2), .out_3(demultiplexer_7_out_3), .out_4(demultiplexer_7_out_4),
    .out_5(demultiplexer_7_out_5), .out_7(demultiplexer_7_out_7));  // open: out_6
  Multiplexer multiplexer_1 (.sel(CLR), .in_0(rmt_condition_write_1_v_out), .in_1(1'b0), .out(multiplexer_1_out));
  Multiplexer #(.Bits(5)) multiplexer_2 (
    .sel(CLR), .in_0(rmt_condition_write_1_data), .in_1({5{1'b0}}), .out(multiplexer_2_out));
  Multiplexer multiplexer_3 (.sel(CLR), .in_0(rmt_condition_write_2_v_out), .in_1(1'b0), .out(multiplexer_3_out));
  Multiplexer #(.Bits(5)) multiplexer_4 (
    .sel(CLR), .in_0(rmt_condition_write_2_data), .in_1({5{1'b0}}), .out(multiplexer_4_out));
  Multiplexer multiplexer_5 (.sel(CLR), .in_0(rmt_condition_write_3_v_out), .in_1(1'b0), .out(multiplexer_5_out));
  Multiplexer #(.Bits(5)) multiplexer_6 (
    .sel(CLR), .in_0(rmt_condition_write_3_data), .in_1({5{1'b0}}), .out(multiplexer_6_out));
  Multiplexer multiplexer_7 (.sel(CLR), .in_0(rmt_condition_write_4_v_out), .in_1(1'b0), .out(multiplexer_7_out));
  Multiplexer #(.Bits(5)) multiplexer_8 (
    .sel(CLR), .in_0(rmt_condition_write_4_data), .in_1({5{1'b0}}), .out(multiplexer_8_out));
  Multiplexer multiplexer_9 (.sel(CLR), .in_0(rmt_condition_write_5_v_out), .in_1(1'b0), .out(multiplexer_9_out));
  Multiplexer #(.Bits(5)) multiplexer_10 (
    .sel(CLR), .in_0(rmt_condition_write_5_data), .in_1({5{1'b0}}), .out(multiplexer_10_out));
  Multiplexer multiplexer_11 (.sel(CLR), .in_0(rmt_condition_write_6_v_out), .in_1(1'b0), .out(multiplexer_11_out));
  Multiplexer #(.Bits(5)) multiplexer_12 (
    .sel(CLR), .in_0(rmt_condition_write_6_data), .in_1({5{1'b0}}), .out(multiplexer_12_out));
  Multiplexer multiplexer_13 (.sel(CLR), .in_0(rmt_condition_write_7_v_out), .in_1(1'b0), .out(multiplexer_13_out));
  Multiplexer #(.Bits(5)) multiplexer_14 (
    .sel(CLR), .in_0(rmt_condition_write_7_data), .in_1({5{1'b0}}), .out(multiplexer_14_out));
  or or_1 (or_1_out, demultiplexer_7_out_0, CLR);
  or or_2 (or_2_out, demultiplexer_6_out_0, CLR);
  or or_3 (or_3_out, demultiplexer_7_out_1, CLR);
  or or_4 (or_4_out, demultiplexer_6_out_1, CLR);
  or or_5 (or_5_out, demultiplexer_7_out_2, CLR);
  or or_6 (or_6_out, demultiplexer_6_out_2, CLR);
  or or_7 (or_7_out, demultiplexer_7_out_3, CLR);
  or or_8 (or_8_out, demultiplexer_6_out_3, CLR);
  or or_9 (or_9_out, demultiplexer_7_out_4, CLR);
  or or_10 (or_10_out, demultiplexer_6_out_4, CLR);
  or or_11 (or_11_out, demultiplexer_7_out_5, CLR);
  or or_12 (or_12_out, demultiplexer_6_out_5, CLR);
  or or_13 (or_13_out, demultiplexer_7_out_7, CLR);
  or or_14 (or_14_out, demultiplexer_6_out_7, CLR);
  Register R0_V (.D(multiplexer_1_out), .C(or_1_out), .en(1'b1), .Q(R0_V_q));
  Register #(.Bits(5)) R0_Tag (.D(multiplexer_2_out), .C(or_2_out), .en(1'b1), .Q(R0_Tag_q));
  Register R1_V (.D(multiplexer_3_out), .C(or_3_out), .en(1'b1), .Q(R1_V_q));
  Register #(.Bits(5)) R1_Tag (.D(multiplexer_4_out), .C(or_4_out), .en(1'b1), .Q(R1_Tag_q));
  Register R2_V (.D(multiplexer_5_out), .C(or_5_out), .en(1'b1), .Q(R2_V_q));
  Register #(.Bits(5)) R2_Tag (.D(multiplexer_6_out), .C(or_6_out), .en(1'b1), .Q(R2_Tag_q));
  Register R3_V (.D(multiplexer_7_out), .C(or_7_out), .en(1'b1), .Q(R3_V_q));
  Register #(.Bits(5)) R3_Tag (.D(multiplexer_8_out), .C(or_8_out), .en(1'b1), .Q(R3_Tag_q));
  Register R4_V (.D(multiplexer_9_out), .C(or_9_out), .en(1'b1), .Q(R4_V_q));
  Register #(.Bits(5)) R4_Tag (.D(multiplexer_10_out), .C(or_10_out), .en(1'b1), .Q(R4_Tag_q));
  Register R5_V (.D(multiplexer_11_out), .C(or_11_out), .en(1'b1), .Q(R5_V_q));
  Register #(.Bits(5)) R5_Tag (.D(multiplexer_12_out), .C(or_12_out), .en(1'b1), .Q(R5_Tag_q));
  Register R7_V (.D(multiplexer_13_out), .C(or_13_out), .en(1'b1), .Q(R7_V_q));
  Register #(.Bits(5)) R7_Tag (.D(multiplexer_14_out), .C(or_14_out), .en(1'b1), .Q(R7_Tag_q));
  Multiplexer #(.Selector_Bits(3)) multiplexer_15 (
    .sel(UpdateDst), .in_0(R0_V_q), .in_1(R1_V_q), .in_2(R2_V_q), .in_3(R3_V_q), .in_4(R4_V_q),
    .in_5(R5_V_q), .in_6(1'b0), .in_7(R7_V_q), .out(multiplexer_15_out));
  Multiplexer #(.Selector_Bits(3), .Bits(5)) multiplexer_16 (
    .sel(UpdateDst), .in_0(R0_Tag_q), .in_1(R1_Tag_q), .in_2(R2_Tag_q), .in_3(R3_Tag_q), .in_4(R4_Tag_q),
    .in_5(R5_Tag_q), .in_6({5{1'b0}}), .in_7(R7_Tag_q), .out(multiplexer_16_out));
  Multiplexer #(.Selector_Bits(3)) multiplexer_17 (
    .sel(RS1), .in_0(R0_V_q), .in_1(R1_V_q), .in_2(R2_V_q), .in_3(R3_V_q), .in_4(R4_V_q), .in_5(R5_V_q),
    .in_6(1'b0), .in_7(R7_V_q), .out(R1V_OUT));
  Multiplexer #(.Selector_Bits(3), .Bits(5)) multiplexer_18 (
    .sel(RS1), .in_0(R0_Tag_q), .in_1(R1_Tag_q), .in_2(R2_Tag_q), .in_3(R3_Tag_q), .in_4(R4_Tag_q),
    .in_5(R5_Tag_q), .in_6({5{1'b0}}), .in_7(R7_Tag_q), .out(R1ROBTag_OUT));
  Multiplexer #(.Selector_Bits(3)) multiplexer_19 (
    .sel(RS2), .in_0(R0_V_q), .in_1(R1_V_q), .in_2(R2_V_q), .in_3(R3_V_q), .in_4(R4_V_q), .in_5(R5_V_q),
    .in_6(1'b0), .in_7(R7_V_q), .out(R2V_OUT));
  Multiplexer #(.Selector_Bits(3), .Bits(5)) multiplexer_20 (
    .sel(RS2), .in_0(R0_Tag_q), .in_1(R1_Tag_q), .in_2(R2_Tag_q), .in_3(R3_Tag_q), .in_4(R4_Tag_q),
    .in_5(R5_Tag_q), .in_6({5{1'b0}}), .in_7(R7_Tag_q), .out(R2ROBTag_OUT));

  // Notes on the sheet:
  //   Rename Map Table (RMT)
  //   Rework this to multiplex the CLK
  //   line on each register based on OR
  //   between WS and all indexes of
  //   registers that have matching tag 
  //   values to RESET_TAG input
endmodule
