// Digital circuit rmt_condition_write.dig as structural Verilog
module rmt_condition_write (
  input  WS,
  input  Update,
  input  [4:0] UpdateTag,
  input  [4:0] CurrentTag,
  input  [4:0] ROBTag_IN,
  input  V_IN,
  input  EN,
  output [4:0] Data,
  output V_OUT
);

  wire and_1_out, and_2_out, comparator_1_eq;
  wire [5:0] multiplexer_1_out;

  and and_1 (and_1_out, Update, EN);
  Comparator #(.Bits(5)) comparator_1 (.a(UpdateTag), .b(CurrentTag), .eq(comparator_1_eq));  // open: gt, lt
  and and_2 (and_2_out, comparator_1_eq, and_1_out);
  Multiplexer #(.Bits(6)) multiplexer_1 (
    .sel(and_2_out), .in_0({6{1'b0}}), .in_1({1'b0, UpdateTag}), .out(multiplexer_1_out));
  Multiplexer #(.Bits(6)) multiplexer_2 (
    .sel(WS), .in_0(multiplexer_1_out), .in_1({V_IN, ROBTag_IN}), .out({V_OUT, Data}));
endmodule
