// Digital circuit rob_update_mask.dig as structural Verilog
module rob_update_mask (
  input  [42:0] Current,
  input  [42:0] Update,
  output [42:0] Entry
);

  wire comparator_1_eq, comparator_2_eq, comparator_3_eq, comparator_4_eq, xnor_1_out, xnor_2_out,
       xnor_3_out, xnor_4_out;

  Comparator #(.Bits(16)) comparator_1 (.a(Update[15:0]), .b({16{1'b0}}), .eq(comparator_1_eq));  // open: gt, lt
  Comparator #(.Bits(3)) comparator_2 (.a(Update[18:16]), .b(3'b000), .eq(comparator_2_eq));  // open: gt, lt
  xnor xnor_1 (xnor_1_out, Update[19], 1'b0);
  xnor xnor_2 (xnor_2_out, Update[20], 1'b0);
  xnor xnor_3 (xnor_3_out, Update[21], 1'b0);
  Comparator #(.Bits(16)) comparator_3 (.a(Update[37:22]), .b({16{1'b0}}), .eq(comparator_3_eq));  // open: gt, lt
  Comparator #(.Bits(4)) comparator_4 (.a(Update[41:38]), .b(4'b0000), .eq(comparator_4_eq));  // open: gt, lt
  xnor xnor_4 (xnor_4_out, Update[42], 1'b0);
  Multiplexer #(.Bits(16)) multiplexer_1 (
    .sel(comparator_1_eq), .in_0(Update[15:0]), .in_1(Current[15:0]), .out(Entry[15:0]));
  Multiplexer #(.Bits(3)) multiplexer_2 (
    .sel(comparator_2_eq), .in_0(Update[18:16]), .in_1(Current[18:16]), .out(Entry[18:16]));
  Multiplexer multiplexer_3 (.sel(xnor_1_out), .in_0(Update[19]), .in_1(Current[19]), .out(Entry[19]));
  Multiplexer multiplexer_4 (.sel(xnor_2_out), .in_0(Update[20]), .in_1(Current[20]), .out(Entry[20]));
  Multiplexer multiplexer_5 (.sel(xnor_3_out), .in_0(Update[21]), .in_1(Current[21]), .out(Entry[21]));
  Multiplexer #(.Bits(16)) multiplexer_6 (
    .sel(comparator_3_eq), .in_0(Update[37:22]), .in_1(Current[37:22]), .out(Entry[37:22]));
  Multiplexer #(.Bits(4)) multiplexer_7 (
    .sel(comparator_4_eq), .in_0(Update[41:38]), .in_1(Current[41:38]), .out(Entry[41:38]));
  Multiplexer multiplexer_8 (.sel(xnor_4_out), .in_0(Update[42]), .in_1(Current[42]), .out(Entry[42]));

  // Notes on the sheet:
  //   0-15: Value
  //   16-18: Dst
  //   19: Rdy
  //   20: Exc
  //   21: Misp
  //   22-37: PC
  //   38-41: Flags
  //   ROB Update Mask
endmodule
