// Digital circuit data_hazard_forwarding.dig as structural Verilog
module data_hazard_forwarding (
  input  I_3,
  input  I_2,
  input  I_1,
  input  I_0,
  output [1:0] ForwardE
);

  wire and_2_out, and_3_out, not_1_out, not_2_out;

  or or_1 (ForwardE[0], and_3_out, and_2_out);
  and and_1 (ForwardE[1], I_2, I_1);
  and and_2 (and_2_out, I_3, not_1_out, I_0);
  and and_3 (and_3_out, I_3, not_2_out, I_0);
  not not_1 (not_1_out, I_2);
  not not_2 (not_2_out, I_1);
  // Pins of 1 and 2 bits meet at ForwardE
endmodule
