// Digital circuit ex_mem_ppr.dig as structural Verilog
module ex_mem_ppr (
  input  CLK,
  input  PCSrcE,
  input  RegWriteE,
  input  MemToRegE,
  input  MemWriteE,
  input  [15:0] ALUResultE,
  input  [15:0] WriteDataE,
  input  [2:0] WAE,
  input  LDRE,
  input  sethE,
  output PCSrcM,
  output RegWriteM,
  output MemToReg,
  output MemWriteM,
  output [15:0] ALUResultM,
  output [15:0] WriteDataM,
  output [2:0] WA3M,
  output LDRM,
  output sethM
);

  Register PCSrc (.D(PCSrcE), .C(CLK), .en(1'b1), .Q(PCSrcM));
  Register RegWrite (.D(RegWriteE), .C(CLK), .en(1'b1), .Q(RegWriteM));
  Register u_MemToReg (.D(MemToRegE), .C(CLK), .en(1'b1), .Q(MemToReg));
  Register MemWrite (.D(MemWriteE), .C(CLK), .en(1'b1), .Q(MemWriteM));
  Register u_setHE (.D(sethE), .C(CLK), .en(1'b1), .Q(sethM));
  Register #(.Bits(16)) ALUResult (.D(ALUResultE), .C(CLK), .en(1'b1), .Q(ALUResultM));
  Register #(.Bits(16)) WriteData (.D(WriteDataE), .C(CLK), .en(1'b1), .Q(WriteDataM));
  Register #(.Bits(3)) WA (.D(WAE), .C(CLK), .en(1'b1), .Q(WA3M));
  Register LDR (.D(LDRE), .C(CLK), .en(1'b1), .Q(LDRM));

  // Notes on the sheet:
  //   EX/MEM PPR
endmodule
