// Digital circuit id_ex_ppr.dig as structural Verilog
module id_ex_ppr (
  input  CondD,
  input  [15:0] Ra1D,
  input  [15:0] Ra2D,
  input  [15:0] SEI16D,
  input  CLK,
  input  [2:0] WAD,
  input  [3:0] FlagsD,
  input  PCSrcD,
  input  RegWriteD,
  input  MemToRegD,
  input  [1:0] ALUCtrlD,
  input  BranchD,
  input  ALUSrcD,
  input  FlagWriteD,
  input  MemWriteD,
  input  LDRD,
  input  SethD,
  input  [15:0] Rd1D,
  input  [15:0] Rd2D,
  input  CLR,
  output CondE,
  output [15:0] Ra1E,
  output [15:0] Ra2E,
  output [15:0] SEI16E,
  output [2:0] WAE,
  output [3:0] FlagsE,
  output PCSrcE,
  output RegWriteE,
  output MemToRegE,
  output [1:0] ALUCtrlE,
  output BranchE,
  output ALUSrcE,
  output FlagWriteE,
  output MemWriteE,
  output LDRE,
  output SethE,
  output [15:0] Rd1E,
  output [15:0] Rd2E
);

  wire [2:0] multiplexer_1_out;
  wire [15:0] multiplexer_2_out, multiplexer_3_out, multiplexer_4_out, multiplexer_5_out, multiplexer_6_out;

  Multiplexer #(.Bits(3)) multiplexer_1 (.sel(CLR), .in_0(WAD), .in_1(3'b000), .out(multiplexer_1_out));
  Multiplexer #(.Bits(16)) multiplexer_2 (.sel(CLR), .in_0(SEI16D), .in_1({16{1'b0}}), .out(multiplexer_2_out));
  Multiplexer #(.Bits(16)) multiplexer_3 (.sel(CLR), .in_0(Ra1D), .in_1({16{1'b0}}), .out(multiplexer_3_out));
  Multiplexer #(.Bits(16)) multiplexer_4 (.sel(CLR), .in_0(Ra2D), .in_1({16{1'b0}}), .out(multiplexer_4_out));
  Multiplexer #(.Bits(16)) multiplexer_5 (.sel(CLR), .in_0(Rd1D), .in_1({16{1'b0}}), .out(multiplexer_5_out));
  Multiplexer #(.Bits(16)) multiplexer_6 (.sel(CLR), .in_0(Rd2D), .in_1({16{1'b0}}), .out(multiplexer_6_out));
  Register PCSrc (.D(PCSrcD), .C(CLK), .en(1'b1), .Q(PCSrcE));
  Register RegWrite (.D(RegWriteD), .C(CLK), .en(1'b1), .Q(RegWriteE));
  Register MemToReg (.D(MemToRegD), .C(CLK), .en(1'b1), .Q(MemToRegE));
  Register MemWrite (.D(MemWriteD), .C(CLK), .en(1'b1), .Q(MemWriteE));
  Register #(.Bits(2)) ALUCtrl (.D(ALUCtrlD), .C(CLK), .en(1'b1), .Q(ALUCtrlE));
  Register u_BranchD (.D(BranchD), .C(CLK), .en(1'b1), .Q(BranchE));
  Register ALUSrc (.D(ALUSrcD), .C(CLK), .en(1'b1), .Q(ALUSrcE));
  Register FlagWrite (.D(FlagWriteD), .C(CLK), .en(1'b1), .Q(FlagWriteE));
  Register u_SethD (.D(SethD), .C(CLK), .en(1'b1), .Q(SethE));
  Register LDR (.D(LDRD), .C(CLK), .en(1'b1), .Q(LDRE));
  Register Cond (.D(CondD), .C(CLK), .en(1'b1), .Q(CondE));
  Register #(.Bits(4)) Flags (.D(FlagsD), .C(CLK), .en(1'b1), .Q(FlagsE));
  Register #(.Bits(3)) WA (.D(multiplexer_1_out), .C(CLK), .en(1'b1), .Q(WAE));
  Register #(.Bits(16)) SEI16 (.D(multiplexer_2_out), .C(CLK), .en(1'b1), .Q(SEI16E));
  Register #(.Bits(16)) Ra1 (.D(multiplexer_3_out), .C(CLK), .en(1'b1), .Q(Ra1E));
  Register #(.Bits(16)) Ra2 (.D(multiplexer_4_out), .C(CLK), .en(1'b1), .Q(Ra2E));
  Register #(.Bits(16)) Rd1 (.D(multiplexer_5_out), .C(CLK), .en(1'b1), .Q(Rd1E));
  Register #(.Bits(16)) Rd2 (.D(multiplexer_6_out), .C(CLK), .en(1'b1), .Q(Rd2E));

  // Notes on the sheet:
  //   ID/EX PPR
endmodule
