// Digital circuit control_unit.dig as structural Verilog
module control_unit (
  input  [15:0] INST,
  input  FL_Z,
  output [1:0] ALUOP,
  output [2:0] RS1,
  output [2:0] RS2,
  output [2:0] WS,
  output STR,
  output WE,
  output [1:0] DMUX,
  output LDR,
  output FL_EN,
  output HE
);

  wire not_1_out, or_1_out;
  wire [2:0] multiplexer_1_out, multiplexer_2_out;
  wire [12:0] lookuptable_1_out;

  not not_1 (not_1_out, INST[11]);
  LookUpTable #(.Bits(13)) lookuptable_1 (
    .in0(INST[12]), .in1(INST[13]), .in2(INST[14]), .in3(INST[15]), .out(lookuptable_1_out));
  or or_1 (or_1_out, not_1_out, FL_Z);
  LED EXEC (.in(or_1_out));
  Multiplexer #(.Selector_Bits(2), .Bits(3)) multiplexer_1 (
    .sel(lookuptable_1_out[10:9]), .in_0(3'b000), .in_1(INST[10:8]), .in_2(INST[6:4]), .in_3(INST[2:0]),
    .out(multiplexer_1_out));
  Multiplexer #(.Selector_Bits(2), .Bits(3)) multiplexer_2 (
    .sel(lookuptable_1_out[8:7]), .in_0(3'b000), .in_1(INST[10:8]), .in_2(INST[6:4]), .in_3(INST[2:0]),
    .out(multiplexer_2_out));
  Multiplexer #(.Bits(2)) multiplexer_3 (.sel(or_1_out), .in_0(2'b00), .in_1(lookuptable_1_out[1:0]), .out(ALUOP));
  Multiplexer #(.Bits(2)) multiplexer_4 (.sel(or_1_out), .in_0(2'b00), .in_1(lookuptable_1_out[3:2]), .out(DMUX));
  Multiplexer multiplexer_5 (.sel(or_1_out), .in_0(1'b0), .in_1(lookuptable_1_out[4]), .out(LDR));
  Multiplexer multiplexer_6 (.sel(or_1_out), .in_0(1'b0), .in_1(lookuptable_1_out[5]), .out(WE));
  Multiplexer multiplexer_7 (.sel(or_1_out), .in_0(1'b0), .in_1(lookuptable_1_out[6]), .out(STR));
  Multiplexer multiplexer_8 (.sel(or_1_out), .in_0(1'b0), .in_1(lookuptable_1_out[11]), .out(FL_EN));
  Multiplexer #(.Bits(3)) multiplexer_9 (.sel(or_1_out), .in_0(3'b000), .in_1(multiplexer_2_out), .out(RS2));
  Multiplexer #(.Bits(3)) multiplexer_10 (.sel(or_1_out), .in_0(3'b000), .in_1(multiplexer_1_out), .out(RS1));
  Multiplexer #(.Bits(3)) multiplexer_11 (.sel(or_1_out), .in_0(3'b000), .in_1(INST[10:8]), .out(WS));
  Multiplexer multiplexer_12 (.sel(or_1_out), .in_0(1'b0), .in_1(lookuptable_1_out[12]), .out(HE));

  // Notes on the sheet:
  //   Rd
  //   opcode
  //   cond
  //   Ra
  //   Rb
  //   contents of lookuptable_1 (hex, n*v repeats v):
  //   28,1028,0,0,4cc,534,0,0,da0,da1,da2,da3
endmodule

/* Test case All Tests:
	INST                                              FL_Z WE  ALUOP  RS1   RS2  WS  STR  LDR DMUX

let cond   = 0b1;
let aluop  = 0b1000;
let ldrop  = 0b0101;
let strop  = 0b0100;
let movlop = 0b0000;

loop(rd, 1<<3)
loop(ra, 1<<3)
loop(rb, 1<<3)

loop(i, 4)
	((aluop+i) <<12            | rd<<8 | ra<<4 | rb<<0) 0   1  (i)     (ra)  (rb) (rd)  0   X    0  #test add/sub/and/orr (no condition)
  	((aluop+i) <<12 | cond<<11 | rd<<8 | ra<<4 | rb<<0) 1   1  (i)     (ra)  (rb) (rd)  0   X    0  #test add/sub/and/orr (with condition and FL_Z)
   	((aluop+i) <<12 | cond<<11 | rd<<8 | ra<<4 | rb<<0) 0   0  0       0     0    0     0   0    0  #test add/sub/and/orr (with condition and no FL_Z)
end loop

	(ldrop     <<12                    | rd<<8 | ra<<4) 0   1  X       (ra)  x    (rd)  0   1    1  #test ldr (no condition)
    	(ldrop     <<12 | cond<<11         | rd<<8 | ra<<4) 1   1  X       (ra)  x    (rd)  0   1    1  #test ldr (with condition and FL_Z)
    	(ldrop     <<12 | cond<<11         | rd<<8 | ra<<4) 0   0  0       0     0    0     0   0    0  #test ldr (with condition and no FL_Z)
	(strop     <<12                    | rd<<8 | ra<<4) 0   0  X       (ra)  (rd)  X    1   X    X  #test str (no condition)
    	(strop     <<12 | cond<<11         | rd<<8 | ra<<4) 1   0  X       (ra)  (rd)  X    1   X    X  #test str (with condition and FL_Z)
    	(strop     <<12 | cond<<11         | rd<<8 | ra<<4) 0   0  0       0     0    0     0   0    0  #test str (with condition and no FL_Z)
	
	let imm = random(256);
	(movlop    <<12            | rd<<8          | imm ) 0   1  X       X      X   (rd)  0   X    2  #test movl (no condition)
    	(movlop    <<12 | cond<<11 | rd<<8          | imm ) 1   1  X       X      X   (rd)  0   X    2  #test movl (with condition and FL_Z)
    	(movlop    <<12 | cond<<11 | rd<<8          | imm ) 0   0  0       0     0    0     0   0    0  #test movl (with condition and no FL_Z)

end loop
end loop
end loop
*/

/* Test case WS:
	INST                                    WS 

let aluop  = 0b1000;
let ldrop  = 0b0101;
let strop  = 0b0100;
let movlop = 0b0000;

loop(rd, 1<<3)
loop(ra, 1<<3)
loop(rb, 1<<3)

loop(i, 4)
	((aluop+i)<<12 | rd<<8 | ra<<4 | rb<<0) (rd)  #test add/sub/and/orr
end loop

	(ldrop    <<12 | rd<<8 | ra<<4 )        (rd)   #test ldr
	(strop    <<12 | rd<<8 | ra<<4 )        X     #test str
	
	let imm = random(256);
	(movlop   <<12 | rd<<8 | imm )          (rd)  #test movl

end loop
end loop
end loop
*/

/* Test case RS1:
	INST                                    RS1  

let aluop  = 0b1000;
let ldrop  = 0b0101;
let strop  = 0b0100;
let movlop = 0b0000;

loop(rd, 1<<3)
loop(ra, 1<<3)
loop(rb, 1<<3)

loop(i, 4)
	((aluop+i)<<12 | rd<<8 | ra<<4 | rb<<0) (ra)  #test add/sub/and/orr
end loop

	(ldrop    <<12 | rd<<8 | ra<<4 )        (ra)  #test ldr
	(strop    <<12 | rd<<8 | ra<<4 )        (ra)  #test str

end loop
end loop
end loop
*/

/* Test case RS2:
	INST                                    RS2  

let aluop  = 0b1000;
let ldrop  = 0b0101;
let strop  = 0b0100;
let movlop = 0b0000;

loop(rd, 1<<3)
loop(ra, 1<<3)
loop(rb, 1<<3)

loop(i, 4)
	((aluop+i)<<12 | rd<<8 | ra<<4 | rb<<0) (rb) #test add/sub/and/orr
end loop
	(strop    <<12 | rd<<8 | ra<<4 )        (rd) #test str

end loop
end loop
end loop
*/

/* Test case STR:
	INST                                    STR 

let aluop  = 0b1000;
let ldrop  = 0b0101;
let strop  = 0b0100;
let movlop = 0b0000;

loop(rd, 1<<3)
loop(ra, 1<<3)
loop(rb, 1<<3)

loop(i, 4)
	((aluop+i)<<12 | rd<<8 | ra<<4 | rb<<0) 0  #test add/sub/and/orr
end loop

	(ldrop    <<12 | rd<<8 | ra<<4 )        0  #test ldr
	(strop    <<12 | rd<<8 | ra<<4 )        1  #test str
	
	let imm = random(256);
	(movlop   <<12 | rd<<8 | imm )          0  #test movl

end loop
end loop
end loop
*/

/* Test case WE:
	INST                                    WE  

let aluop  = 0b1000;
let ldrop  = 0b0101;
let strop  = 0b0100;
let movlop = 0b0000;

loop(rd, 1<<3)
loop(ra, 1<<3)
loop(rb, 1<<3)

loop(i, 4)
	((aluop+i)<<12 | rd<<8 | ra<<4 | rb<<0) 1  #test add/sub/and/orr
end loop

	(ldrop    <<12 | rd<<8 | ra<<4 )        1  #test ldr
	(strop    <<12 | rd<<8 | ra<<4 )        0  #test str
	
	let imm = random(256);
	(movlop   <<12 | rd<<8 | imm )          1  #test movl

end loop
end loop
end loop
*/

/* Test case LDR:
	INST                                    LDR 

let aluop  = 0b1000;
let ldrop  = 0b0101;
let strop  = 0b0100;
let movlop = 0b0000;

loop(rd, 1<<3)
loop(ra, 1<<3)
loop(rb, 1<<3)

loop(i, 4)
	((aluop+i)<<12 | rd<<8 | ra<<4 | rb<<0) X    #test add/sub/and/orr
end loop

	(ldrop    <<12 | rd<<8 | ra<<4 )        1    #test ldr
	(strop    <<12 | rd<<8 | ra<<4 )        X    #test str
	
	let imm = random(256);
	(movlop   <<12 | rd<<8 | imm )          X    #test movl

end loop
end loop
end loop
*/

/* Test case DMUX:
	INST                                    DMUX

let aluop  = 0b1000;
let ldrop  = 0b0101;
let strop  = 0b0100;
let movlop = 0b0000;

loop(rd, 1<<3)
loop(ra, 1<<3)
loop(rb, 1<<3)

loop(i, 4)
	((aluop+i)<<12 | rd<<8 | ra<<4 | rb<<0) 0  #test add/sub/and/orr
end loop

	(ldrop    <<12 | rd<<8 | ra<<4 )        1  #test ldr
	
	let imm = random(256);
	(movlop   <<12 | rd<<8 | imm )          2  #test movl

end loop
end loop
end loop
*/

/* Test case ALUOP:
	INST                                    ALUOP 

let aluop  = 0b1000;
let ldrop  = 0b0101;
let strop  = 0b0100;
let movlop = 0b0000;

loop(rd, 1<<3)
loop(ra, 1<<3)
loop(rb, 1<<3)

loop(i, 4)
	((aluop+i)<<12 | rd<<8 | ra<<4 | rb<<0) (i)    #test add/sub/and/orr
end loop

end loop
end loop
end loop
*/
