// Digital circuit cpu.dig as structural Verilog
module cpu (
  input  CLK
);

  wire FL_EN, HE, LDR, reg_file_1_pc_we, STR, WE;
  wire [1:0] ALUOP, DMUX;
  wire [2:0] RS1, RS2, WS;
  wire [3:0] alu_1_flag, PC_q, PC_q_2, PC_q_3, PC_q_4;
  wire [15:0] alu_1_result, multiplexer_1_out, multiplexer_2_out, plus_1_s, RAM_d1, RAM_d2,
       reg_file_1_fl_out, reg_file_1_out1, reg_file_1_out2, reg_file_1_pc_s;

  Seven_Seg_Hex seven_seg_hex_1 (.d(PC_q_4), .dp(1'b0));
  Seven_Seg_Hex seven_seg_hex_2 (.d(PC_q_2), .dp(1'b0));
  Seven_Seg_Hex seven_seg_hex_3 (.d(PC_q_3), .dp(1'b0));
  Seven_Seg_Hex seven_seg_hex_4 (.d(PC_q), .dp(1'b0));
  Multiplexer #(.Bits(16)) multiplexer_1 (
    .sel(reg_file_1_pc_we), .in_0(plus_1_s), .in_1(reg_file_1_pc_s), .out(multiplexer_1_out));
  Register #(.Bits(16), .isProgramCounter("true")) PC (
    .D(multiplexer_1_out), .C(CLK), .en(1'b1), .Q({PC_q_4, PC_q_3, PC_q_2, PC_q}));
  Add #(.Bits(16)) plus_1 (.a(16'h1), .b({PC_q_4, PC_q_3, PC_q_2, PC_q}), .c_i(1'b0), .s(plus_1_s));  // open: c_o
  RAMDualAccess #(.AddrBits(16), .isProgramMemory("true"), .Bits(16)) RAM (
    .str(STR), .C(CLK), .ld(LDR), .A1(reg_file_1_out1), .Din1(reg_file_1_out2),
    .A2({PC_q_4, PC_q_3, PC_q_2, PC_q}), .D1(RAM_d1), .D2(RAM_d2));
  Multiplexer #(.Selector_Bits(2), .Bits(16)) multiplexer_2 (
    .sel(DMUX), .in_0(alu_1_result), .in_1(RAM_d1), .in_2({{8{1'b0}}, RAM_d2[7:0]}), .in_3({16{1'b0}}),
    .out(multiplexer_2_out));
  control_unit control_unit_1 (
    .INST(RAM_d2), .FL_Z(reg_file_1_fl_out[0]), .ALUOP(ALUOP), .RS1(RS1), .RS2(RS2), .WS(WS), .STR(STR),
    .WE(WE), .DMUX(DMUX), .LDR(LDR), .FL_EN(FL_EN), .HE(HE));
  reg_file reg_file_1 (
    .RS1(RS1), .RS2(RS2), .WS(WS), .WE(WE), .IN(multiplexer_2_out), .clk(CLK),
    .FL_IN({{12{1'b0}}, alu_1_flag}), .FL_EN(FL_EN), .PC_IN({PC_q_4, PC_q_3, PC_q_2, PC_q}), .HE(HE),
    .OUT1(reg_file_1_out1), .OUT2(reg_file_1_out2), .PC_S(reg_file_1_pc_s), .PC_WE(reg_file_1_pc_we),
    .FL_OUT(reg_file_1_fl_out));
  alu alu_1 (.A(reg_file_1_out1), .B(reg_file_1_out2), .ALUOP(ALUOP), .RESULT(alu_1_result), .FLAG(alu_1_flag));
endmodule
